// Logisim project dunk.circ as structural Verilog: 74 circuits, main circuit main
module main (
);

  wire clk_out, controlled_buffer_1_out, controlled_buffer_2_out, controlled_buffer_3_out,
       controlled_buffer_4_out, double_click_1_out_2, io_pins_4_1_out_10, io_pins_4_1_out_11,
       io_pins_4_1_out_12, io_pins_4_1_out_13, io_pins_4_1_out_14, io_pins_4_1_out_15, io_pins_4_1_out_16,
       io_pins_4_1_out_17, memory_ctrl_1_mem_write, memory_ctrl_1_reg_write, reset_out;
  wire [1:0] memory_ctrl_1_reg_select;
  wire [15:0] addr_bus_controller_1_addr_bus_out, alu_1_out_6, control_bus_controller_1_control_bus_1,
       control_bus_controller_1_control_bus_2, control_unit_1_addr_bus_out, control_unit_1_control_bus_1_out,
       control_unit_1_control_bus_2_out, control_unit_1_data_bus_out, control_unit_1_to_pk,
       data_bus_controller_1_data_bus_out, io_pins_4_1_data_bus_out, memory_ctrl_1_data_bus_out,
       memory_ctrl_1_data_to_mem, memory_ctrl_1_mem_addr_out, mmio_registers_1_out_6, ram_1_dout,
       register_unit_1_addr_bus_out, register_unit_1_alu1_out, register_unit_1_alu2_out,
       register_unit_1_data_bus_out, special_registers_1_addr_bus_out, special_registers_1_data_bus_out,
       special_registers_1_offset_out, special_registers_1_program_kounter, special_registers_1_stack_pointer;

  Clock clk (.out(clk_out));
  Button reset (.out(reset_out));
  double_click double_click_1 (.in_1(reset_out), .out_2(double_click_1_out_2));
  control_bus_controller control_bus_controller_1 (
    .control_1(control_unit_1_control_bus_1_out), .control_2(control_unit_1_control_bus_2_out),
    .clock(clk_out), .reset(double_click_1_out_2), .control_bus_1(control_bus_controller_1_control_bus_1),
    .control_bus_2(control_bus_controller_1_control_bus_2));
  data_bus_controller data_bus_controller_1 (
    .control_bus_2(control_bus_controller_1_control_bus_2),
    .control_bus_1(control_bus_controller_1_control_bus_1), .clock(clk_out), .reset(double_click_1_out_2),
    .addr_bus_in(addr_bus_controller_1_addr_bus_out), .control_unit_in(control_unit_1_data_bus_out),
    .registers_in(register_unit_1_data_bus_out), .special_registers_in(alu_1_out_6),
    .ALU_in(special_registers_1_data_bus_out), .memory_in(memory_ctrl_1_data_bus_out),
    .io_in(io_pins_4_1_data_bus_out), .data_bus_out(data_bus_controller_1_data_bus_out));
  addr_bus_controller addr_bus_controller_1 (
    .control_bus_2(control_bus_controller_1_control_bus_2), .clock(clk_out), .reset(double_click_1_out_2),
    .control_bus_1(control_bus_controller_1_control_bus_1), .data_bus_in(data_bus_controller_1_data_bus_out),
    .control_unit_in(control_unit_1_addr_bus_out), .registers_in(register_unit_1_addr_bus_out),
    .special_registers_in(special_registers_1_addr_bus_out), .addr_bus_out(addr_bus_controller_1_addr_bus_out));
  control_unit control_unit_1 (
    .program_kounter(special_registers_1_program_kounter), .stack_pointer(special_registers_1_stack_pointer),
    .addr_bus(addr_bus_controller_1_addr_bus_out), .reset(double_click_1_out_2), .clock(clk_out),
    .control_bus_1(control_bus_controller_1_control_bus_1),
    .control_bus_2(control_bus_controller_1_control_bus_2), .data_bus_in(data_bus_controller_1_data_bus_out),
    .control_bus_2_out(control_unit_1_control_bus_2_out),
    .control_bus_1_out(control_unit_1_control_bus_1_out), .data_bus_out(control_unit_1_data_bus_out),
    .addr_bus_out(control_unit_1_addr_bus_out), .to_pk(control_unit_1_to_pk));
  register_unit register_unit_1 (
    .control_bus_1(control_bus_controller_1_control_bus_1),
    .control_bus_2(control_bus_controller_1_control_bus_2), .data_bus_in(data_bus_controller_1_data_bus_out),
    .clock(clk_out), .reset(double_click_1_out_2), .data_bus_out(register_unit_1_data_bus_out),
    .addr_bus_out(register_unit_1_addr_bus_out), .alu1_out(register_unit_1_alu1_out),
    .alu2_out(register_unit_1_alu2_out));
  assign controlled_buffer_1_out = io_pins_4_1_out_11 ? io_pins_4_1_out_10 : 1'bz;  // Controlled_Buffer controlled_buffer_1
  ALU alu_1 (
    .control_bus(control_bus_controller_1_control_bus_1), .argument1(register_unit_1_alu1_out),
    .argument2(register_unit_1_alu2_out), .clock(clk_out), .reset(double_click_1_out_2), .out_6(alu_1_out_6));  // open: out_7
  assign controlled_buffer_2_out = io_pins_4_1_out_13 ? io_pins_4_1_out_12 : 1'bz;  // Controlled_Buffer controlled_buffer_2
  // Probe on special_registers_1_program_kounter
  assign controlled_buffer_3_out = io_pins_4_1_out_15 ? io_pins_4_1_out_14 : 1'bz;  // Controlled_Buffer controlled_buffer_3
  // Probe on special_registers_1_stack_pointer
  special_registers special_registers_1 (
    .control_bus_1(control_bus_controller_1_control_bus_1),
    .control_bus_2(control_bus_controller_1_control_bus_2), .temp_register(control_unit_1_to_pk),
    .clock(clk_out), .reset(double_click_1_out_2), .data_bus_in(data_bus_controller_1_data_bus_out),
    .program_kounter(special_registers_1_program_kounter), .data_bus_out(special_registers_1_data_bus_out),
    .addr_bus_out(special_registers_1_addr_bus_out), .stack_pointer(special_registers_1_stack_pointer),
    .offset_out(special_registers_1_offset_out));  // open: sp_reset_value
  io_pins_4 io_pins_4_1 (
    .in_7(controlled_buffer_3_out), .clock(clk_out), .reset(double_click_1_out_2),
    .in_8(controlled_buffer_4_out), .control_bus(control_bus_controller_1_control_bus_1),
    .data_bus_in(data_bus_controller_1_data_bus_out), .in_5(controlled_buffer_1_out),
    .in_6(controlled_buffer_2_out), .out_14(io_pins_4_1_out_14), .out_15(io_pins_4_1_out_15),
    .out_16(io_pins_4_1_out_16), .out_17(io_pins_4_1_out_17), .data_bus_out(io_pins_4_1_data_bus_out),
    .out_10(io_pins_4_1_out_10), .out_11(io_pins_4_1_out_11), .out_12(io_pins_4_1_out_12),
    .out_13(io_pins_4_1_out_13));
  assign controlled_buffer_4_out = io_pins_4_1_out_17 ? io_pins_4_1_out_16 : 1'bz;  // Controlled_Buffer controlled_buffer_4
  mmio_registers mmio_registers_1 (
    .write(memory_ctrl_1_reg_write), .clock(clk_out), .reset(double_click_1_out_2),
    .data_in(memory_ctrl_1_data_to_mem), .reg_select(memory_ctrl_1_reg_select), .out_6(mmio_registers_1_out_6));  // open: out_7, out_8, out_9
  RAM #(.addrWidth(16), .dataWidth(16), .enables("line")) ram_1 (
    .addr(memory_ctrl_1_mem_addr_out), .we(memory_ctrl_1_mem_write), .clk(clk_out),
    .din(memory_ctrl_1_data_to_mem), .dout(ram_1_dout));
  memory_ctrl memory_ctrl_1 (
    .control_bus_2(control_bus_controller_1_control_bus_2), .pk_in(special_registers_1_program_kounter),
    .mem_in(ram_1_dout), .addr_in(addr_bus_controller_1_addr_bus_out), .clock(clk_out),
    .reset(double_click_1_out_2), .control_bus_1(control_bus_controller_1_control_bus_1),
    .data_bus_in(data_bus_controller_1_data_bus_out), .offset_in(special_registers_1_offset_out),
    .data_bus_out(memory_ctrl_1_data_bus_out), .mem_addr_out(memory_ctrl_1_mem_addr_out),
    .mem_write(memory_ctrl_1_mem_write), .reg_select(memory_ctrl_1_reg_select),
    .reg_write(memory_ctrl_1_reg_write), .data_to_mem(memory_ctrl_1_data_to_mem));
  // Probe on control_bus_controller_1_control_bus_1
  // Probe on control_bus_controller_1_control_bus_2
  // Probe on data_bus_controller_1_data_bus_out
  // Probe on addr_bus_controller_1_addr_bus_out
  TTY tty_1 (
    .data(mmio_registers_1_out_6[6:0]), .clk(controlled_buffer_4_out), .clr(double_click_1_out_2));  // open: we

  // Notes on the sheet:
  //   David's Universal Number Kounter
endmodule

module four_bit_incrementer (
  input  [3:0] in_1,
  output [3:0] out_2
);

  wire and_1_out, and_2_out, and_3_out, and_4_out, and_5_out, xor_2_out, xor_3_out, xor_4_out, xor_8_out,
       xor_9_out;

  xor xor_1 (out_2[0], in_1[0], 1'b1);
  and and_1 (and_1_out, in_1[0], 1'b1);
  xor xor_2 (xor_2_out, in_1[1], 1'b0);
  and and_2 (and_2_out, in_1[1], 1'b0);
  xor xor_3 (xor_3_out, in_1[2], 1'b0);
  and and_3 (and_3_out, in_1[2], 1'b0);
  xor xor_4 (xor_4_out, in_1[3], 1'b0);
  xor xor_5 (out_2[1], xor_2_out, and_1_out);
  and and_4 (and_4_out, xor_2_out, and_1_out);
  xor xor_6 (out_2[2], xor_3_out, xor_8_out);
  and and_5 (and_5_out, xor_3_out, xor_8_out);
  xor xor_7 (out_2[3], xor_4_out, xor_9_out);
  xor xor_8 (xor_8_out, and_2_out, and_4_out);
  xor xor_9 (xor_9_out, and_3_out, and_5_out);
endmodule

module sixt_bit_adder (
  input  [15:0] in_1,
  input  [15:0] in_2,
  output [15:0] out_3,
  output out_4
);

  wire and_1_out, and_2_out, and_3_out, and_4_out, and_5_out, and_6_out, and_7_out, and_8_out, and_9_out,
       and_10_out, and_11_out, and_12_out, and_13_out, and_14_out, and_15_out, and_16_out, and_17_out,
       and_18_out, and_19_out, and_20_out, and_21_out, and_22_out, and_23_out, and_24_out, and_25_out,
       and_26_out, and_27_out, and_28_out, and_29_out, and_30_out, and_31_out, xor_2_out, xor_3_out,
       xor_4_out, xor_5_out, xor_6_out, xor_7_out, xor_8_out, xor_9_out, xor_10_out, xor_11_out, xor_12_out,
       xor_13_out, xor_14_out, xor_15_out, xor_16_out, xor_32_out, xor_33_out, xor_34_out, xor_35_out,
       xor_36_out, xor_37_out, xor_38_out, xor_39_out, xor_40_out, xor_41_out, xor_42_out, xor_43_out,
       xor_44_out, xor_45_out;

  xor xor_1 (out_3[0], in_1[0], in_2[0]);
  and and_1 (and_1_out, in_1[0], in_2[0]);
  xor xor_2 (xor_2_out, in_1[1], in_2[1]);
  and and_2 (and_2_out, in_1[1], in_2[1]);
  xor xor_3 (xor_3_out, in_1[2], in_2[2]);
  and and_3 (and_3_out, in_1[2], in_2[2]);
  xor xor_4 (xor_4_out, in_1[3], in_2[3]);
  and and_4 (and_4_out, in_1[3], in_2[3]);
  xor xor_5 (xor_5_out, in_1[4], in_2[4]);
  and and_5 (and_5_out, in_1[4], in_2[4]);
  xor xor_6 (xor_6_out, in_1[5], in_2[5]);
  and and_6 (and_6_out, in_1[5], in_2[5]);
  xor xor_7 (xor_7_out, in_1[6], in_2[6]);
  and and_7 (and_7_out, in_1[6], in_2[6]);
  xor xor_8 (xor_8_out, in_1[7], in_2[7]);
  and and_8 (and_8_out, in_1[7], in_2[7]);
  xor xor_9 (xor_9_out, in_1[8], in_2[8]);
  and and_9 (and_9_out, in_1[8], in_2[8]);
  xor xor_10 (xor_10_out, in_1[9], in_2[9]);
  and and_10 (and_10_out, in_1[9], in_2[9]);
  xor xor_11 (xor_11_out, in_1[10], in_2[10]);
  and and_11 (and_11_out, in_1[10], in_2[10]);
  xor xor_12 (xor_12_out, in_1[11], in_2[11]);
  and and_12 (and_12_out, in_1[11], in_2[11]);
  xor xor_13 (xor_13_out, in_1[12], in_2[12]);
  and and_13 (and_13_out, in_1[12], in_2[12]);
  xor xor_14 (xor_14_out, in_1[13], in_2[13]);
  and and_14 (and_14_out, in_1[13], in_2[13]);
  xor xor_15 (xor_15_out, in_1[14], in_2[14]);
  and and_15 (and_15_out, in_1[14], in_2[14]);
  xor xor_16 (xor_16_out, in_1[15], in_2[15]);
  and and_16 (and_16_out, in_1[15], in_2[15]);
  xor xor_17 (out_3[1], xor_2_out, and_1_out);
  and and_17 (and_17_out, xor_2_out, and_1_out);
  xor xor_18 (out_3[2], xor_3_out, xor_32_out);
  and and_18 (and_18_out, xor_3_out, xor_32_out);
  xor xor_19 (out_3[3], xor_4_out, xor_33_out);
  and and_19 (and_19_out, xor_4_out, xor_33_out);
  xor xor_20 (out_3[4], xor_5_out, xor_34_out);
  and and_20 (and_20_out, xor_5_out, xor_34_out);
  xor xor_21 (out_3[5], xor_6_out, xor_35_out);
  and and_21 (and_21_out, xor_6_out, xor_35_out);
  xor xor_22 (out_3[6], xor_7_out, xor_36_out);
  and and_22 (and_22_out, xor_7_out, xor_36_out);
  xor xor_23 (out_3[7], xor_8_out, xor_37_out);
  and and_23 (and_23_out, xor_8_out, xor_37_out);
  xor xor_24 (out_3[8], xor_9_out, xor_38_out);
  and and_24 (and_24_out, xor_9_out, xor_38_out);
  xor xor_25 (out_3[9], xor_10_out, xor_39_out);
  and and_25 (and_25_out, xor_10_out, xor_39_out);
  xor xor_26 (out_3[10], xor_11_out, xor_40_out);
  and and_26 (and_26_out, xor_11_out, xor_40_out);
  xor xor_27 (out_3[11], xor_12_out, xor_41_out);
  and and_27 (and_27_out, xor_12_out, xor_41_out);
  xor xor_28 (out_3[12], xor_13_out, xor_42_out);
  and and_28 (and_28_out, xor_13_out, xor_42_out);
  xor xor_29 (out_3[13], xor_14_out, xor_43_out);
  and and_29 (and_29_out, xor_14_out, xor_43_out);
  xor xor_30 (out_3[14], xor_15_out, xor_44_out);
  and and_30 (and_30_out, xor_15_out, xor_44_out);
  xor xor_31 (out_3[15], xor_16_out, xor_45_out);
  and and_31 (and_31_out, xor_16_out, xor_45_out);
  xor xor_32 (xor_32_out, and_2_out, and_17_out);
  xor xor_33 (xor_33_out, and_3_out, and_18_out);
  xor xor_34 (xor_34_out, and_4_out, and_19_out);
  xor xor_35 (xor_35_out, and_5_out, and_20_out);
  xor xor_36 (xor_36_out, and_6_out, and_21_out);
  xor xor_37 (xor_37_out, and_7_out, and_22_out);
  xor xor_38 (xor_38_out, and_8_out, and_23_out);
  xor xor_39 (xor_39_out, and_9_out, and_24_out);
  xor xor_40 (xor_40_out, and_10_out, and_25_out);
  xor xor_41 (xor_41_out, and_11_out, and_26_out);
  xor xor_42 (xor_42_out, and_12_out, and_27_out);
  xor xor_43 (xor_43_out, and_13_out, and_28_out);
  xor xor_44 (xor_44_out, and_14_out, and_29_out);
  xor xor_45 (xor_45_out, and_15_out, and_30_out);
  xor xor_46 (out_4, and_16_out, and_31_out);
endmodule

module sixt_bit_adder_c (
  input  in_1,
  input  [15:0] in_2,
  input  [15:0] in_3,
  output [15:0] out_4,
  output out_5
);

  wire and_1_out, and_2_out, and_3_out, and_4_out, and_5_out, and_6_out, and_7_out, and_8_out, and_9_out,
       and_10_out, and_11_out, and_12_out, and_13_out, and_14_out, and_15_out, and_16_out, and_17_out,
       and_18_out, and_19_out, and_20_out, and_21_out, and_22_out, and_23_out, and_24_out, and_25_out,
       and_26_out, and_27_out, and_28_out, and_29_out, and_30_out, and_31_out, and_32_out, xor_1_out,
       xor_2_out, xor_3_out, xor_4_out, xor_5_out, xor_6_out, xor_7_out, xor_8_out, xor_9_out, xor_10_out,
       xor_11_out, xor_12_out, xor_13_out, xor_14_out, xor_15_out, xor_16_out, xor_33_out, xor_34_out,
       xor_35_out, xor_36_out, xor_37_out, xor_38_out, xor_39_out, xor_40_out, xor_41_out, xor_42_out,
       xor_43_out, xor_44_out, xor_45_out, xor_46_out, xor_47_out;

  xor xor_1 (xor_1_out, in_2[0], in_3[0]);
  and and_1 (and_1_out, in_2[0], in_3[0]);
  xor xor_2 (xor_2_out, in_2[1], in_3[1]);
  and and_2 (and_2_out, in_2[1], in_3[1]);
  xor xor_3 (xor_3_out, in_2[2], in_3[2]);
  and and_3 (and_3_out, in_2[2], in_3[2]);
  xor xor_4 (xor_4_out, in_2[3], in_3[3]);
  and and_4 (and_4_out, in_2[3], in_3[3]);
  xor xor_5 (xor_5_out, in_2[4], in_3[4]);
  and and_5 (and_5_out, in_2[4], in_3[4]);
  xor xor_6 (xor_6_out, in_2[5], in_3[5]);
  and and_6 (and_6_out, in_2[5], in_3[5]);
  xor xor_7 (xor_7_out, in_2[6], in_3[6]);
  and and_7 (and_7_out, in_2[6], in_3[6]);
  xor xor_8 (xor_8_out, in_2[7], in_3[7]);
  and and_8 (and_8_out, in_2[7], in_3[7]);
  xor xor_9 (xor_9_out, in_2[8], in_3[8]);
  and and_9 (and_9_out, in_2[8], in_3[8]);
  xor xor_10 (xor_10_out, in_2[9], in_3[9]);
  and and_10 (and_10_out, in_2[9], in_3[9]);
  xor xor_11 (xor_11_out, in_2[10], in_3[10]);
  and and_11 (and_11_out, in_2[10], in_3[10]);
  xor xor_12 (xor_12_out, in_2[11], in_3[11]);
  and and_12 (and_12_out, in_2[11], in_3[11]);
  xor xor_13 (xor_13_out, in_2[12], in_3[12]);
  and and_13 (and_13_out, in_2[12], in_3[12]);
  xor xor_14 (xor_14_out, in_2[13], in_3[13]);
  and and_14 (and_14_out, in_2[13], in_3[13]);
  xor xor_15 (xor_15_out, in_2[14], in_3[14]);
  and and_15 (and_15_out, in_2[14], in_3[14]);
  xor xor_16 (xor_16_out, in_2[15], in_3[15]);
  and and_16 (and_16_out, in_2[15], in_3[15]);
  xor xor_17 (out_4[0], xor_1_out, in_1);
  and and_17 (and_17_out, xor_1_out, in_1);
  xor xor_18 (out_4[1], xor_2_out, xor_33_out);
  and and_18 (and_18_out, xor_2_out, xor_33_out);
  xor xor_19 (out_4[2], xor_3_out, xor_34_out);
  and and_19 (and_19_out, xor_3_out, xor_34_out);
  xor xor_20 (out_4[3], xor_4_out, xor_35_out);
  and and_20 (and_20_out, xor_4_out, xor_35_out);
  xor xor_21 (out_4[4], xor_5_out, xor_36_out);
  and and_21 (and_21_out, xor_5_out, xor_36_out);
  xor xor_22 (out_4[5], xor_6_out, xor_37_out);
  and and_22 (and_22_out, xor_6_out, xor_37_out);
  xor xor_23 (out_4[6], xor_7_out, xor_38_out);
  and and_23 (and_23_out, xor_7_out, xor_38_out);
  xor xor_24 (out_4[7], xor_8_out, xor_39_out);
  and and_24 (and_24_out, xor_8_out, xor_39_out);
  xor xor_25 (out_4[8], xor_9_out, xor_40_out);
  and and_25 (and_25_out, xor_9_out, xor_40_out);
  xor xor_26 (out_4[9], xor_10_out, xor_41_out);
  and and_26 (and_26_out, xor_10_out, xor_41_out);
  xor xor_27 (out_4[10], xor_11_out, xor_42_out);
  and and_27 (and_27_out, xor_11_out, xor_42_out);
  xor xor_28 (out_4[11], xor_12_out, xor_43_out);
  and and_28 (and_28_out, xor_12_out, xor_43_out);
  xor xor_29 (out_4[12], xor_13_out, xor_44_out);
  and and_29 (and_29_out, xor_13_out, xor_44_out);
  xor xor_30 (out_4[13], xor_14_out, xor_45_out);
  and and_30 (and_30_out, xor_14_out, xor_45_out);
  xor xor_31 (out_4[14], xor_15_out, xor_46_out);
  and and_31 (and_31_out, xor_15_out, xor_46_out);
  xor xor_32 (out_4[15], xor_16_out, xor_47_out);
  and and_32 (and_32_out, xor_16_out, xor_47_out);
  xor xor_33 (xor_33_out, and_1_out, and_17_out);
  xor xor_34 (xor_34_out, and_2_out, and_18_out);
  xor xor_35 (xor_35_out, and_3_out, and_19_out);
  xor xor_36 (xor_36_out, and_4_out, and_20_out);
  xor xor_37 (xor_37_out, and_5_out, and_21_out);
  xor xor_38 (xor_38_out, and_6_out, and_22_out);
  xor xor_39 (xor_39_out, and_7_out, and_23_out);
  xor xor_40 (xor_40_out, and_8_out, and_24_out);
  xor xor_41 (xor_41_out, and_9_out, and_25_out);
  xor xor_42 (xor_42_out, and_10_out, and_26_out);
  xor xor_43 (xor_43_out, and_11_out, and_27_out);
  xor xor_44 (xor_44_out, and_12_out, and_28_out);
  xor xor_45 (xor_45_out, and_13_out, and_29_out);
  xor xor_46 (xor_46_out, and_14_out, and_30_out);
  xor xor_47 (xor_47_out, and_15_out, and_31_out);
  xor xor_48 (out_5, and_16_out, and_32_out);
endmodule

module sixt_bit_adder_subtractor (
  input  [15:0] in_1,
  input  [15:0] in_2,
  input  in_3,
  output [15:0] out_4,
  output out_5
);

  wire and_1_out, and_2_out, and_3_out, and_4_out, and_5_out, and_6_out, and_7_out, and_8_out, and_9_out,
       and_10_out, and_11_out, and_12_out, and_13_out, and_14_out, and_15_out, and_16_out, and_17_out,
       and_18_out, and_19_out, and_20_out, and_21_out, and_22_out, and_23_out, and_24_out, and_25_out,
       and_26_out, and_27_out, and_28_out, and_29_out, and_30_out, and_31_out, xor_2_out, xor_4_out,
       xor_6_out, xor_8_out, xor_10_out, xor_12_out, xor_14_out, xor_16_out, xor_18_out, xor_20_out,
       xor_22_out, xor_24_out, xor_26_out, xor_28_out, xor_30_out, xor_32_out, xor_33_out, xor_34_out,
       xor_35_out, xor_36_out, xor_37_out, xor_38_out, xor_39_out, xor_40_out, xor_41_out, xor_42_out,
       xor_43_out, xor_44_out, xor_45_out;
  wire [15:0] not_1_out, sixt_bit_incrementer_1_out_2, sixt_bit_selector_1_out_4;

  assign not_1_out = ~in_2;  // NOT_Gate not_1, 16 bits wide
  sixt_bit_selector sixt_bit_selector_1 (
    .in_3(sixt_bit_incrementer_1_out_2), .in_1(in_3), .in_2(in_2), .out_4(sixt_bit_selector_1_out_4));
  sixt_bit_incrementer sixt_bit_incrementer_1 (.in_1(not_1_out), .out_2(sixt_bit_incrementer_1_out_2));
  xor xor_1 (out_4[0], in_1[0], sixt_bit_selector_1_out_4[0]);
  and and_1 (and_1_out, in_1[0], sixt_bit_selector_1_out_4[0]);
  xor xor_2 (xor_2_out, in_1[1], sixt_bit_selector_1_out_4[1]);
  xor xor_3 (out_4[1], xor_2_out, and_1_out);
  and and_2 (and_2_out, in_1[1], sixt_bit_selector_1_out_4[1]);
  and and_3 (and_3_out, xor_2_out, and_1_out);
  xor xor_4 (xor_4_out, in_1[2], sixt_bit_selector_1_out_4[2]);
  xor xor_5 (out_4[2], xor_4_out, xor_32_out);
  and and_4 (and_4_out, in_1[2], sixt_bit_selector_1_out_4[2]);
  and and_5 (and_5_out, xor_4_out, xor_32_out);
  xor xor_6 (xor_6_out, in_1[3], sixt_bit_selector_1_out_4[3]);
  xor xor_7 (out_4[3], xor_6_out, xor_33_out);
  and and_6 (and_6_out, in_1[3], sixt_bit_selector_1_out_4[3]);
  and and_7 (and_7_out, xor_6_out, xor_33_out);
  xor xor_8 (xor_8_out, in_1[4], sixt_bit_selector_1_out_4[4]);
  xor xor_9 (out_4[4], xor_8_out, xor_34_out);
  and and_8 (and_8_out, in_1[4], sixt_bit_selector_1_out_4[4]);
  and and_9 (and_9_out, xor_8_out, xor_34_out);
  xor xor_10 (xor_10_out, in_1[5], sixt_bit_selector_1_out_4[5]);
  xor xor_11 (out_4[5], xor_10_out, xor_35_out);
  and and_10 (and_10_out, in_1[5], sixt_bit_selector_1_out_4[5]);
  and and_11 (and_11_out, xor_10_out, xor_35_out);
  xor xor_12 (xor_12_out, in_1[6], sixt_bit_selector_1_out_4[6]);
  xor xor_13 (out_4[6], xor_12_out, xor_36_out);
  and and_12 (and_12_out, in_1[6], sixt_bit_selector_1_out_4[6]);
  and and_13 (and_13_out, xor_12_out, xor_36_out);
  xor xor_14 (xor_14_out, in_1[7], sixt_bit_selector_1_out_4[7]);
  xor xor_15 (out_4[7], xor_14_out, xor_37_out);
  and and_14 (and_14_out, in_1[7], sixt_bit_selector_1_out_4[7]);
  and and_15 (and_15_out, xor_14_out, xor_37_out);
  xor xor_16 (xor_16_out, in_1[8], sixt_bit_selector_1_out_4[8]);
  xor xor_17 (out_4[8], xor_16_out, xor_38_out);
  and and_16 (and_16_out, in_1[8], sixt_bit_selector_1_out_4[8]);
  and and_17 (and_17_out, xor_16_out, xor_38_out);
  xor xor_18 (xor_18_out, in_1[9], sixt_bit_selector_1_out_4[9]);
  xor xor_19 (out_4[9], xor_18_out, xor_39_out);
  and and_18 (and_18_out, in_1[9], sixt_bit_selector_1_out_4[9]);
  and and_19 (and_19_out, xor_18_out, xor_39_out);
  xor xor_20 (xor_20_out, in_1[10], sixt_bit_selector_1_out_4[10]);
  xor xor_21 (out_4[10], xor_20_out, xor_40_out);
  and and_20 (and_20_out, in_1[10], sixt_bit_selector_1_out_4[10]);
  and and_21 (and_21_out, xor_20_out, xor_40_out);
  xor xor_22 (xor_22_out, in_1[11], sixt_bit_selector_1_out_4[11]);
  xor xor_23 (out_4[11], xor_22_out, xor_41_out);
  and and_22 (and_22_out, in_1[11], sixt_bit_selector_1_out_4[11]);
  and and_23 (and_23_out, xor_22_out, xor_41_out);
  xor xor_24 (xor_24_out, in_1[12], sixt_bit_selector_1_out_4[12]);
  xor xor_25 (out_4[12], xor_24_out, xor_42_out);
  and and_24 (and_24_out, in_1[12], sixt_bit_selector_1_out_4[12]);
  and and_25 (and_25_out, xor_24_out, xor_42_out);
  xor xor_26 (xor_26_out, in_1[13], sixt_bit_selector_1_out_4[13]);
  xor xor_27 (out_4[13], xor_26_out, xor_43_out);
  and and_26 (and_26_out, in_1[13], sixt_bit_selector_1_out_4[13]);
  and and_27 (and_27_out, xor_26_out, xor_43_out);
  xor xor_28 (xor_28_out, in_1[14], sixt_bit_selector_1_out_4[14]);
  xor xor_29 (out_4[14], xor_28_out, xor_44_out);
  and and_28 (and_28_out, in_1[14], sixt_bit_selector_1_out_4[14]);
  and and_29 (and_29_out, xor_28_out, xor_44_out);
  xor xor_30 (xor_30_out, in_1[15], sixt_bit_selector_1_out_4[15]);
  xor xor_31 (out_4[15], xor_30_out, xor_45_out);
  and and_30 (and_30_out, in_1[15], sixt_bit_selector_1_out_4[15]);
  and and_31 (and_31_out, xor_30_out, xor_45_out);
  xor xor_32 (xor_32_out, and_2_out, and_3_out);
  xor xor_33 (xor_33_out, and_4_out, and_5_out);
  xor xor_34 (xor_34_out, and_6_out, and_7_out);
  xor xor_35 (xor_35_out, and_8_out, and_9_out);
  xor xor_36 (xor_36_out, and_10_out, and_11_out);
  xor xor_37 (xor_37_out, and_12_out, and_13_out);
  xor xor_38 (xor_38_out, and_14_out, and_15_out);
  xor xor_39 (xor_39_out, and_16_out, and_17_out);
  xor xor_40 (xor_40_out, and_18_out, and_19_out);
  xor xor_41 (xor_41_out, and_20_out, and_21_out);
  xor xor_42 (xor_42_out, and_22_out, and_23_out);
  xor xor_43 (xor_43_out, and_24_out, and_25_out);
  xor xor_44 (xor_44_out, and_26_out, and_27_out);
  xor xor_45 (xor_45_out, and_28_out, and_29_out);
  xor xor_46 (out_5, and_30_out, and_31_out);
endmodule

module sixt_bit_incrementer (
  input  [15:0] in_1,
  output [15:0] out_2
);

  sixt_bit_adder sixt_bit_adder_1 (.in_1(16'h1), .in_2(in_1), .out_3(out_2));  // open: out_4
endmodule

module sixt_bit_decrementer (
  input  [15:0] in_1,
  output [15:0] out_2
);

  sixt_bit_adder sixt_bit_adder_1 (.in_1({16{1'b1}}), .in_2(in_1), .out_3(out_2));  // open: out_4
endmodule

module sixt_bit_selector (
  input  in_1,
  input  [15:0] in_2,
  input  [15:0] in_3,
  output [15:0] out_4
);

  wire [15:0] and_1_out, and_2_out;
  wire [15:15] not_1_out;

  not not_1 (not_1_out[15], in_1);
  assign and_1_out = {16{not_1_out[15]}} & in_2;  // AND_Gate and_1, 16 bits wide
  assign and_2_out = in_3 & {16{in_1}};  // AND_Gate and_2, 16 bits wide
  assign out_4 = and_1_out | and_2_out;  // OR_Gate or_1, 16 bits wide
endmodule

module sixt_bit_shift_by_one (
  input  [15:0] in_1,
  output [15:0] out_2
);


  assign out_2 = {in_1[14:0], 1'b0};
endmodule

module sixt_bit_gatekeeper (
  input  in_1,
  input  [15:0] in_2,
  output [15:0] out_3
);

  assign out_3 = {16{in_1}} & in_2;  // AND_Gate and_1, 16 bits wide
endmodule

module sixt_bit_gatekeeper_vert (
  input  in_1,
  input  [15:0] in_2,
  output [15:0] out_3
);

  assign out_3 = {16{in_1}} & in_2;  // AND_Gate and_1, 16 bits wide
endmodule

module sixt_bit_multuiplier (
  input  [15:0] in_1,
  input  [15:0] in_2,
  output [15:0] out_3
);

  wire [15:0] sixt_bit_adder_1_out_3, sixt_bit_adder_2_out_3, sixt_bit_adder_3_out_3, sixt_bit_adder_4_out_3,
       sixt_bit_adder_5_out_3, sixt_bit_adder_6_out_3, sixt_bit_adder_7_out_3, sixt_bit_adder_8_out_3,
       sixt_bit_adder_9_out_3, sixt_bit_adder_10_out_3, sixt_bit_adder_11_out_3, sixt_bit_adder_12_out_3,
       sixt_bit_adder_13_out_3, sixt_bit_adder_14_out_3, sixt_bit_gatekeeper_vert_1_out_3,
       sixt_bit_gatekeeper_vert_2_out_3, sixt_bit_gatekeeper_vert_3_out_3, sixt_bit_gatekeeper_vert_4_out_3,
       sixt_bit_gatekeeper_vert_5_out_3, sixt_bit_gatekeeper_vert_6_out_3, sixt_bit_gatekeeper_vert_7_out_3,
       sixt_bit_gatekeeper_vert_8_out_3, sixt_bit_gatekeeper_vert_9_out_3, sixt_bit_gatekeeper_vert_10_out_3,
       sixt_bit_gatekeeper_vert_11_out_3, sixt_bit_gatekeeper_vert_12_out_3,
       sixt_bit_gatekeeper_vert_13_out_3, sixt_bit_gatekeeper_vert_14_out_3,
       sixt_bit_gatekeeper_vert_15_out_3, sixt_bit_gatekeeper_vert_16_out_3, sixt_bit_shift_by_one_1_out_2,
       sixt_bit_shift_by_one_2_out_2, sixt_bit_shift_by_one_3_out_2, sixt_bit_shift_by_one_4_out_2,
       sixt_bit_shift_by_one_5_out_2, sixt_bit_shift_by_one_6_out_2, sixt_bit_shift_by_one_7_out_2,
       sixt_bit_shift_by_one_8_out_2, sixt_bit_shift_by_one_9_out_2, sixt_bit_shift_by_one_10_out_2,
       sixt_bit_shift_by_one_11_out_2, sixt_bit_shift_by_one_12_out_2, sixt_bit_shift_by_one_13_out_2,
       sixt_bit_shift_by_one_14_out_2, sixt_bit_shift_by_one_15_out_2;

  sixt_bit_gatekeeper_vert sixt_bit_gatekeeper_vert_1 (
    .in_1(in_1[0]), .in_2(in_2), .out_3(sixt_bit_gatekeeper_vert_1_out_3));
  sixt_bit_shift_by_one sixt_bit_shift_by_one_1 (.in_1(in_2), .out_2(sixt_bit_shift_by_one_1_out_2));
  sixt_bit_shift_by_one sixt_bit_shift_by_one_2 (
    .in_1(sixt_bit_shift_by_one_1_out_2), .out_2(sixt_bit_shift_by_one_2_out_2));
  sixt_bit_gatekeeper_vert sixt_bit_gatekeeper_vert_2 (
    .in_1(in_1[1]), .in_2(sixt_bit_shift_by_one_1_out_2), .out_3(sixt_bit_gatekeeper_vert_2_out_3));
  sixt_bit_gatekeeper_vert sixt_bit_gatekeeper_vert_3 (
    .in_1(in_1[2]), .in_2(sixt_bit_shift_by_one_2_out_2), .out_3(sixt_bit_gatekeeper_vert_3_out_3));
  sixt_bit_adder sixt_bit_adder_1 (
    .in_1(sixt_bit_gatekeeper_vert_2_out_3), .in_2(sixt_bit_gatekeeper_vert_1_out_3),
    .out_3(sixt_bit_adder_1_out_3));  // open: out_4
  sixt_bit_shift_by_one sixt_bit_shift_by_one_3 (
    .in_1(sixt_bit_shift_by_one_2_out_2), .out_2(sixt_bit_shift_by_one_3_out_2));
  sixt_bit_gatekeeper_vert sixt_bit_gatekeeper_vert_4 (
    .in_1(in_1[3]), .in_2(sixt_bit_shift_by_one_3_out_2), .out_3(sixt_bit_gatekeeper_vert_4_out_3));
  sixt_bit_adder sixt_bit_adder_2 (
    .in_1(sixt_bit_gatekeeper_vert_3_out_3), .in_2(sixt_bit_adder_1_out_3), .out_3(sixt_bit_adder_2_out_3));  // open: out_4
  sixt_bit_adder sixt_bit_adder_3 (
    .in_1(sixt_bit_gatekeeper_vert_4_out_3), .in_2(sixt_bit_adder_2_out_3), .out_3(sixt_bit_adder_3_out_3));  // open: out_4
  sixt_bit_shift_by_one sixt_bit_shift_by_one_4 (
    .in_1(sixt_bit_shift_by_one_3_out_2), .out_2(sixt_bit_shift_by_one_4_out_2));
  sixt_bit_shift_by_one sixt_bit_shift_by_one_5 (
    .in_1(sixt_bit_shift_by_one_4_out_2), .out_2(sixt_bit_shift_by_one_5_out_2));
  sixt_bit_gatekeeper_vert sixt_bit_gatekeeper_vert_5 (
    .in_1(in_1[4]), .in_2(sixt_bit_shift_by_one_4_out_2), .out_3(sixt_bit_gatekeeper_vert_5_out_3));
  sixt_bit_gatekeeper_vert sixt_bit_gatekeeper_vert_6 (
    .in_1(in_1[5]), .in_2(sixt_bit_shift_by_one_5_out_2), .out_3(sixt_bit_gatekeeper_vert_6_out_3));
  sixt_bit_adder sixt_bit_adder_4 (
    .in_1(sixt_bit_gatekeeper_vert_5_out_3), .in_2(sixt_bit_adder_3_out_3), .out_3(sixt_bit_adder_4_out_3));  // open: out_4
  sixt_bit_shift_by_one sixt_bit_shift_by_one_6 (
    .in_1(sixt_bit_shift_by_one_5_out_2), .out_2(sixt_bit_shift_by_one_6_out_2));
  sixt_bit_gatekeeper_vert sixt_bit_gatekeeper_vert_7 (
    .in_1(in_1[6]), .in_2(sixt_bit_shift_by_one_6_out_2), .out_3(sixt_bit_gatekeeper_vert_7_out_3));
  sixt_bit_gatekeeper_vert sixt_bit_gatekeeper_vert_8 (
    .in_1(in_1[7]), .in_2(sixt_bit_shift_by_one_7_out_2), .out_3(sixt_bit_gatekeeper_vert_8_out_3));
  sixt_bit_adder sixt_bit_adder_5 (
    .in_1(sixt_bit_gatekeeper_vert_6_out_3), .in_2(sixt_bit_adder_4_out_3), .out_3(sixt_bit_adder_5_out_3));  // open: out_4
  sixt_bit_adder sixt_bit_adder_6 (
    .in_1(sixt_bit_gatekeeper_vert_7_out_3), .in_2(sixt_bit_adder_5_out_3), .out_3(sixt_bit_adder_6_out_3));  // open: out_4
  sixt_bit_shift_by_one sixt_bit_shift_by_one_7 (
    .in_1(sixt_bit_shift_by_one_6_out_2), .out_2(sixt_bit_shift_by_one_7_out_2));
  sixt_bit_shift_by_one sixt_bit_shift_by_one_8 (
    .in_1(sixt_bit_shift_by_one_7_out_2), .out_2(sixt_bit_shift_by_one_8_out_2));
  sixt_bit_gatekeeper_vert sixt_bit_gatekeeper_vert_9 (
    .in_1(in_1[8]), .in_2(sixt_bit_shift_by_one_8_out_2), .out_3(sixt_bit_gatekeeper_vert_9_out_3));
  sixt_bit_adder sixt_bit_adder_7 (
    .in_1(sixt_bit_gatekeeper_vert_8_out_3), .in_2(sixt_bit_adder_6_out_3), .out_3(sixt_bit_adder_7_out_3));  // open: out_4
  sixt_bit_adder sixt_bit_adder_8 (
    .in_1(sixt_bit_gatekeeper_vert_9_out_3), .in_2(sixt_bit_adder_7_out_3), .out_3(sixt_bit_adder_8_out_3));  // open: out_4
  sixt_bit_shift_by_one sixt_bit_shift_by_one_9 (
    .in_1(sixt_bit_shift_by_one_8_out_2), .out_2(sixt_bit_shift_by_one_9_out_2));
  sixt_bit_shift_by_one sixt_bit_shift_by_one_10 (
    .in_1(sixt_bit_shift_by_one_9_out_2), .out_2(sixt_bit_shift_by_one_10_out_2));
  sixt_bit_gatekeeper_vert sixt_bit_gatekeeper_vert_10 (
    .in_1(in_1[9]), .in_2(sixt_bit_shift_by_one_9_out_2), .out_3(sixt_bit_gatekeeper_vert_10_out_3));
  sixt_bit_gatekeeper_vert sixt_bit_gatekeeper_vert_11 (
    .in_1(in_1[10]), .in_2(sixt_bit_shift_by_one_10_out_2), .out_3(sixt_bit_gatekeeper_vert_11_out_3));
  sixt_bit_adder sixt_bit_adder_9 (
    .in_1(sixt_bit_gatekeeper_vert_10_out_3), .in_2(sixt_bit_adder_8_out_3), .out_3(sixt_bit_adder_9_out_3));  // open: out_4
  sixt_bit_shift_by_one sixt_bit_shift_by_one_11 (
    .in_1(sixt_bit_shift_by_one_10_out_2), .out_2(sixt_bit_shift_by_one_11_out_2));
  sixt_bit_gatekeeper_vert sixt_bit_gatekeeper_vert_12 (
    .in_1(in_1[11]), .in_2(sixt_bit_shift_by_one_11_out_2), .out_3(sixt_bit_gatekeeper_vert_12_out_3));
  sixt_bit_adder sixt_bit_adder_10 (
    .in_1(sixt_bit_gatekeeper_vert_11_out_3), .in_2(sixt_bit_adder_9_out_3), .out_3(sixt_bit_adder_10_out_3));  // open: out_4
  sixt_bit_adder sixt_bit_adder_11 (
    .in_1(sixt_bit_gatekeeper_vert_12_out_3), .in_2(sixt_bit_adder_10_out_3), .out_3(sixt_bit_adder_11_out_3));  // open: out_4
  sixt_bit_shift_by_one sixt_bit_shift_by_one_12 (
    .in_1(sixt_bit_shift_by_one_11_out_2), .out_2(sixt_bit_shift_by_one_12_out_2));
  sixt_bit_shift_by_one sixt_bit_shift_by_one_13 (
    .in_1(sixt_bit_shift_by_one_12_out_2), .out_2(sixt_bit_shift_by_one_13_out_2));
  sixt_bit_gatekeeper_vert sixt_bit_gatekeeper_vert_13 (
    .in_1(in_1[12]), .in_2(sixt_bit_shift_by_one_12_out_2), .out_3(sixt_bit_gatekeeper_vert_13_out_3));
  sixt_bit_gatekeeper_vert sixt_bit_gatekeeper_vert_14 (
    .in_1(in_1[13]), .in_2(sixt_bit_shift_by_one_13_out_2), .out_3(sixt_bit_gatekeeper_vert_14_out_3));
  sixt_bit_adder sixt_bit_adder_12 (
    .in_1(sixt_bit_gatekeeper_vert_13_out_3), .in_2(sixt_bit_adder_11_out_3), .out_3(sixt_bit_adder_12_out_3));  // open: out_4
  sixt_bit_shift_by_one sixt_bit_shift_by_one_14 (
    .in_1(sixt_bit_shift_by_one_13_out_2), .out_2(sixt_bit_shift_by_one_14_out_2));
  sixt_bit_gatekeeper_vert sixt_bit_gatekeeper_vert_15 (
    .in_1(in_1[14]), .in_2(sixt_bit_shift_by_one_14_out_2), .out_3(sixt_bit_gatekeeper_vert_15_out_3));
  sixt_bit_gatekeeper_vert sixt_bit_gatekeeper_vert_16 (
    .in_1(in_1[15]), .in_2(sixt_bit_shift_by_one_15_out_2), .out_3(sixt_bit_gatekeeper_vert_16_out_3));
  sixt_bit_adder sixt_bit_adder_13 (
    .in_1(sixt_bit_gatekeeper_vert_14_out_3), .in_2(sixt_bit_adder_12_out_3), .out_3(sixt_bit_adder_13_out_3));  // open: out_4
  sixt_bit_adder sixt_bit_adder_14 (
    .in_1(sixt_bit_gatekeeper_vert_15_out_3), .in_2(sixt_bit_adder_13_out_3), .out_3(sixt_bit_adder_14_out_3));  // open: out_4
  sixt_bit_shift_by_one sixt_bit_shift_by_one_15 (
    .in_1(sixt_bit_shift_by_one_14_out_2), .out_2(sixt_bit_shift_by_one_15_out_2));
  sixt_bit_adder sixt_bit_adder_15 (
    .in_1(sixt_bit_gatekeeper_vert_16_out_3), .in_2(sixt_bit_adder_14_out_3), .out_3(out_3));  // open: out_4
endmodule

module sixt_bit_eq_cmp (
  input  [15:0] in_1,
  input  [15:0] in_2,
  output out_3
);

  wire or_1_out;
  wire [15:0] xor_1_out;

  xor xor_1 (xor_1_out[0], in_1[0], in_2[0]);
  xor xor_2 (xor_1_out[1], in_1[1], in_2[1]);
  xor xor_3 (xor_1_out[2], in_1[2], in_2[2]);
  xor xor_4 (xor_1_out[3], in_1[3], in_2[3]);
  xor xor_5 (xor_1_out[4], in_1[4], in_2[4]);
  xor xor_6 (xor_1_out[5], in_1[5], in_2[5]);
  xor xor_7 (xor_1_out[6], in_1[6], in_2[6]);
  xor xor_8 (xor_1_out[7], in_1[7], in_2[7]);
  xor xor_9 (xor_1_out[8], in_1[8], in_2[8]);
  xor xor_10 (xor_1_out[9], in_1[9], in_2[9]);
  xor xor_11 (xor_1_out[10], in_1[10], in_2[10]);
  xor xor_12 (xor_1_out[11], in_1[11], in_2[11]);
  xor xor_13 (xor_1_out[12], in_1[12], in_2[12]);
  xor xor_14 (xor_1_out[13], in_1[13], in_2[13]);
  xor xor_15 (xor_1_out[14], in_1[14], in_2[14]);
  xor xor_16 (xor_1_out[15], in_1[15], in_2[15]);
  or or_1 (or_1_out, xor_1_out[0], xor_1_out[1], xor_1_out[2], xor_1_out[3], xor_1_out[4], xor_1_out[5], xor_1_out[6], xor_1_out[7], xor_1_out[8], xor_1_out[9], xor_1_out[10], xor_1_out[11], xor_1_out[12], xor_1_out[13], xor_1_out[14], xor_1_out[15]);
  not not_1 (out_3, or_1_out);
endmodule

module eight_bit_eq_cmp (
  input  [7:0] in_1,
  input  [7:0] in_2,
  output out_3
);

  wire xor_1_out, xor_2_out, xor_3_out, xor_4_out, xor_5_out, xor_6_out, xor_7_out, xor_8_out;

  xor xor_1 (xor_1_out, in_1[0], in_2[0]);
  xor xor_2 (xor_2_out, in_1[1], in_2[1]);
  xor xor_3 (xor_3_out, in_1[2], in_2[2]);
  xor xor_4 (xor_4_out, in_1[3], in_2[3]);
  xor xor_5 (xor_5_out, in_1[4], in_2[4]);
  xor xor_6 (xor_6_out, in_1[5], in_2[5]);
  xor xor_7 (xor_7_out, in_1[6], in_2[6]);
  xor xor_8 (xor_8_out, in_1[7], in_2[7]);
  nor nor_1 (out_3, xor_1_out, xor_2_out, xor_3_out, xor_4_out, xor_5_out, xor_6_out, xor_7_out, xor_8_out);
endmodule

module four_bit_eq_cmp (
  input  [3:0] in_1,
  input  [3:0] in_2,
  output out_3
);

  wire xor_1_out, xor_2_out, xor_3_out, xor_4_out;

  xor xor_1 (xor_1_out, in_1[0], in_2[0]);
  xor xor_2 (xor_2_out, in_1[1], in_2[1]);
  xor xor_3 (xor_3_out, in_1[2], in_2[2]);
  xor xor_4 (xor_4_out, in_1[3], in_2[3]);
  nor nor_1 (out_3, xor_1_out, xor_2_out, xor_3_out, xor_4_out);
endmodule

module four_bit_x_or_y (
  input  [3:0] in_1,
  input  [3:0] in_2,
  input  [3:0] in_3,
  output out_4
);

  wire four_bit_eq_cmp_1_out_3, four_bit_eq_cmp_2_out_3;

  four_bit_eq_cmp four_bit_eq_cmp_1 (.in_1(in_1), .in_2(in_2), .out_3(four_bit_eq_cmp_1_out_3));
  or or_1 (out_4, four_bit_eq_cmp_1_out_3, four_bit_eq_cmp_2_out_3);
  four_bit_eq_cmp four_bit_eq_cmp_2 (.in_1(in_1), .in_2(in_3), .out_3(four_bit_eq_cmp_2_out_3));
endmodule

module sixt_bit_controlled_swapper (
  input  [15:0] in_1,
  input  [15:0] in_2,
  input  in_3,
  output [15:0] out_4,
  output [15:0] out_5
);

  sixt_bit_selector sixt_bit_selector_1 (.in_3(in_2), .in_1(in_3), .in_2(in_1), .out_4(out_4));
  sixt_bit_selector sixt_bit_selector_2 (.in_3(in_1), .in_1(in_3), .in_2(in_2), .out_4(out_5));
endmodule

module sixt_bit_comparator (
  input  [15:0] in_1,
  input  [15:0] in_2,
  output out_3,
  output out_4
);

  wire and_1_out, and_2_out, and_3_out, and_4_out, and_5_out, and_6_out, and_7_out, and_8_out, and_9_out,
       and_10_out, and_11_out, and_12_out, and_13_out, and_14_out, and_15_out, and_16_out, and_17_out,
       and_18_out, and_19_out, and_20_out, and_21_out, and_22_out, and_23_out, and_24_out, and_25_out,
       and_26_out, and_27_out, and_28_out, and_29_out, and_30_out, or_1_out, or_2_out, or_3_out, or_4_out,
       or_5_out, or_6_out, or_7_out, or_8_out, or_9_out, or_10_out, or_11_out, or_12_out, or_13_out,
       or_14_out, or_15_out, or_17_out, or_18_out, or_19_out, or_20_out, or_21_out, or_22_out, or_23_out,
       or_24_out, or_25_out, or_26_out, or_27_out, or_28_out, or_29_out, or_30_out, xor_1_out, xor_2_out,
       xor_3_out, xor_4_out, xor_5_out, xor_6_out, xor_7_out, xor_8_out, xor_9_out, xor_10_out, xor_11_out,
       xor_12_out, xor_13_out, xor_14_out, xor_15_out, xor_16_out;

  xor xor_1 (xor_1_out, in_1[0], in_2[0]);
  xor xor_2 (xor_2_out, in_1[1], in_2[1]);
  xor xor_3 (xor_3_out, in_1[2], in_2[2]);
  xor xor_4 (xor_4_out, in_1[3], in_2[3]);
  xor xor_5 (xor_5_out, in_1[4], in_2[4]);
  xor xor_6 (xor_6_out, in_1[5], in_2[5]);
  xor xor_7 (xor_7_out, in_1[6], in_2[6]);
  xor xor_8 (xor_8_out, in_1[7], in_2[7]);
  xor xor_9 (xor_9_out, in_1[8], in_2[8]);
  xor xor_10 (xor_10_out, in_1[9], in_2[9]);
  xor xor_11 (xor_11_out, in_1[10], in_2[10]);
  xor xor_12 (xor_12_out, in_1[11], in_2[11]);
  xor xor_13 (xor_13_out, in_1[12], in_2[12]);
  xor xor_14 (xor_14_out, in_1[13], in_2[13]);
  xor xor_15 (xor_15_out, in_1[14], in_2[14]);
  xor xor_16 (xor_16_out, in_1[15], in_2[15]);
  or or_1 (or_1_out, or_2_out, xor_1_out);
  and and_1 (and_1_out, xor_1_out, ~or_2_out);  // AND_Gate
  or or_2 (or_2_out, or_3_out, xor_2_out);
  and and_2 (and_2_out, xor_2_out, ~or_3_out);  // AND_Gate
  or or_3 (or_3_out, or_4_out, xor_3_out);
  and and_3 (and_3_out, xor_3_out, ~or_4_out);  // AND_Gate
  or or_4 (or_4_out, or_5_out, xor_4_out);
  and and_4 (and_4_out, xor_4_out, ~or_5_out);  // AND_Gate
  or or_5 (or_5_out, or_6_out, xor_5_out);
  and and_5 (and_5_out, xor_5_out, ~or_6_out);  // AND_Gate
  or or_6 (or_6_out, or_7_out, xor_6_out);
  and and_6 (and_6_out, xor_6_out, ~or_7_out);  // AND_Gate
  or or_7 (or_7_out, or_8_out, xor_7_out);
  and and_7 (and_7_out, xor_7_out, ~or_8_out);  // AND_Gate
  or or_8 (or_8_out, or_9_out, xor_8_out);
  and and_8 (and_8_out, xor_8_out, ~or_9_out);  // AND_Gate
  or or_9 (or_9_out, or_10_out, xor_9_out);
  and and_9 (and_9_out, xor_9_out, ~or_10_out);  // AND_Gate
  or or_10 (or_10_out, or_11_out, xor_10_out);
  and and_10 (and_10_out, xor_10_out, ~or_11_out);  // AND_Gate
  or or_11 (or_11_out, or_12_out, xor_11_out);
  and and_11 (and_11_out, xor_11_out, ~or_12_out);  // AND_Gate
  or or_12 (or_12_out, or_13_out, xor_12_out);
  and and_12 (and_12_out, xor_12_out, ~or_13_out);  // AND_Gate
  or or_13 (or_13_out, or_14_out, xor_13_out);
  and and_13 (and_13_out, xor_13_out, ~or_14_out);  // AND_Gate
  or or_14 (or_14_out, or_15_out, xor_14_out);
  and and_14 (and_14_out, xor_14_out, ~or_15_out);  // AND_Gate
  or or_15 (or_15_out, xor_16_out, xor_15_out);
  and and_15 (and_15_out, xor_15_out, ~xor_16_out);  // AND_Gate
  and and_16 (and_16_out, and_1_out, in_1[0]);
  or or_16 (out_3, and_16_out, or_17_out);
  and and_17 (and_17_out, and_2_out, in_1[1]);
  or or_17 (or_17_out, and_17_out, or_18_out);
  and and_18 (and_18_out, and_3_out, in_1[2]);
  or or_18 (or_18_out, and_18_out, or_19_out);
  and and_19 (and_19_out, and_4_out, in_1[3]);
  or or_19 (or_19_out, and_19_out, or_20_out);
  and and_20 (and_20_out, and_5_out, in_1[4]);
  or or_20 (or_20_out, and_20_out, or_21_out);
  and and_21 (and_21_out, and_6_out, in_1[5]);
  or or_21 (or_21_out, and_21_out, or_22_out);
  and and_22 (and_22_out, and_7_out, in_1[6]);
  or or_22 (or_22_out, and_22_out, or_23_out);
  and and_23 (and_23_out, and_8_out, in_1[7]);
  or or_23 (or_23_out, and_23_out, or_24_out);
  and and_24 (and_24_out, and_9_out, in_1[8]);
  or or_24 (or_24_out, and_24_out, or_25_out);
  and and_25 (and_25_out, and_10_out, in_1[9]);
  or or_25 (or_25_out, and_25_out, or_26_out);
  and and_26 (and_26_out, and_11_out, in_1[10]);
  or or_26 (or_26_out, and_26_out, or_27_out);
  and and_27 (and_27_out, and_12_out, in_1[11]);
  or or_27 (or_27_out, and_27_out, or_28_out);
  and and_28 (and_28_out, and_13_out, in_1[12]);
  or or_28 (or_28_out, and_28_out, or_29_out);
  and and_29 (and_29_out, and_14_out, in_1[13]);
  or or_29 (or_29_out, and_29_out, or_30_out);
  and and_30 (and_30_out, and_15_out, in_1[14]);
  or or_30 (or_30_out, and_30_out, xor_16_out);
  and and_31 (out_4, ~out_3, or_1_out);  // AND_Gate
endmodule

module sixt_bit_eq_zero (
  input  [15:0] in_1,
  output out_2
);

  wire [15:0] not_1_out;

  assign not_1_out = ~in_1;  // NOT_Gate not_1, 16 bits wide
  and and_1 (out_2, not_1_out[0], not_1_out[1], not_1_out[2], not_1_out[3], not_1_out[4], not_1_out[5], not_1_out[6], not_1_out[7], not_1_out[8], not_1_out[9], not_1_out[10], not_1_out[11], not_1_out[12], not_1_out[13], not_1_out[14], not_1_out[15]);
endmodule

module sixt_bit_looping_incrementer (
  input  [15:0] in_1,
  input  [15:0] in_2,
  output [15:0] out_3
);

  wire and_1_out, sixt_bit_comparator_1_out_3, sixt_bit_comparator_1_out_4;
  wire [15:0] sixt_bit_incrementer_1_out_2;

  sixt_bit_incrementer sixt_bit_incrementer_1 (.in_1(in_1), .out_2(sixt_bit_incrementer_1_out_2));
  sixt_bit_comparator sixt_bit_comparator_1 (
    .in_1(sixt_bit_incrementer_1_out_2), .in_2(in_2), .out_3(sixt_bit_comparator_1_out_3),
    .out_4(sixt_bit_comparator_1_out_4));
  sixt_bit_gatekeeper_vert sixt_bit_gatekeeper_vert_1 (
    .in_1(and_1_out), .in_2(sixt_bit_incrementer_1_out_2), .out_3(out_3));
  and and_1 (and_1_out, ~sixt_bit_comparator_1_out_3, sixt_bit_comparator_1_out_4);  // AND_Gate
endmodule

module sixt_bit_looping_counter (
  input  [15:0] in_1,
  input  in_2,
  input  in_3,
  output [15:0] out_4
);

  wire and_1_out, sixt_bit_comparator_1_out_3, sixt_bit_comparator_1_out_4;
  wire [15:0] sixt_bit_gatekeeper_1_out_3, sixt_bit_incrementer_1_out_2;

  Register #(.width(16)) register_1 (.D(sixt_bit_gatekeeper_1_out_3), .en(1'b1), .clk(in_2), .Q(out_4), .clr(in_3));
  sixt_bit_incrementer sixt_bit_incrementer_1 (.in_1(out_4), .out_2(sixt_bit_incrementer_1_out_2));
  sixt_bit_comparator sixt_bit_comparator_1 (
    .in_1(sixt_bit_incrementer_1_out_2), .in_2(in_1), .out_3(sixt_bit_comparator_1_out_3),
    .out_4(sixt_bit_comparator_1_out_4));
  and and_1 (and_1_out, sixt_bit_comparator_1_out_4, ~sixt_bit_comparator_1_out_3);  // AND_Gate
  sixt_bit_gatekeeper sixt_bit_gatekeeper_1 (
    .in_1(and_1_out), .in_2(sixt_bit_incrementer_1_out_2), .out_3(sixt_bit_gatekeeper_1_out_3));
endmodule

module sixt_bit_counter (
  input  in_1,
  input  in_2,
  output [15:0] out_3
);

  wire [15:0] sixt_bit_incrementer_1_out_2;

  Register #(.width(16)) register_1 (.D(sixt_bit_incrementer_1_out_2), .en(1'b1), .clk(in_1), .Q(out_3), .clr(in_2));
  sixt_bit_incrementer sixt_bit_incrementer_1 (.in_1(out_3), .out_2(sixt_bit_incrementer_1_out_2));
endmodule

module register_unit (
  input  [15:0] data_bus_in,
  input  [15:0] control_bus_1,
  input  [15:0] control_bus_2,
  input  clock,
  input  reset,
  output [15:0] data_bus_out,
  output [15:0] addr_bus_out,
  output [15:0] alu1_out,
  output [15:0] alu2_out
);

  wire and_1_out, and_2_out, and_3_out, and_4_out, and_5_out, and_6_out, and_7_out, and_8_out, and_9_out,
       and_10_out, and_11_out, and_12_out, and_13_out, and_14_out, and_15_out, and_16_out,
       eight_bit_eq_cmp_1_out_3, eight_bit_eq_cmp_2_out_3, eight_bit_eq_cmp_3_out_3,
       eight_bit_eq_cmp_4_out_3, eight_bit_eq_cmp_5_out_3, eight_bit_eq_cmp_6_out_3,
       eight_bit_eq_cmp_7_out_3, eight_bit_eq_cmp_8_out_3, eight_bit_eq_cmp_9_out_3,
       eight_bit_eq_cmp_10_out_3, four_bit_eq_cmp_1_out_3, four_bit_eq_cmp_2_out_3, four_bit_eq_cmp_3_out_3,
       four_bit_eq_cmp_4_out_3, four_bit_eq_cmp_5_out_3, four_bit_eq_cmp_6_out_3, four_bit_eq_cmp_7_out_3,
       four_bit_eq_cmp_8_out_3, four_bit_eq_cmp_9_out_3, four_bit_eq_cmp_10_out_3, four_bit_eq_cmp_11_out_3,
       four_bit_eq_cmp_12_out_3, four_bit_eq_cmp_13_out_3, four_bit_eq_cmp_14_out_3,
       four_bit_eq_cmp_15_out_3, four_bit_eq_cmp_16_out_3, four_bit_eq_cmp_17_out_3,
       four_bit_eq_cmp_18_out_3, four_bit_eq_cmp_19_out_3, four_bit_eq_cmp_20_out_3,
       four_bit_eq_cmp_21_out_3, four_bit_eq_cmp_22_out_3, four_bit_eq_cmp_23_out_3,
       four_bit_eq_cmp_24_out_3, four_bit_eq_cmp_25_out_3, four_bit_eq_cmp_26_out_3,
       four_bit_eq_cmp_27_out_3, four_bit_eq_cmp_28_out_3, four_bit_eq_cmp_29_out_3,
       four_bit_eq_cmp_30_out_3, four_bit_eq_cmp_31_out_3, four_bit_eq_cmp_32_out_3, or_1_out, or_2_out,
       or_3_out, or_4_out, or_5_out, or_6_out, or_7_out;
  wire [3:0] or_8_out, or_9_out;
  wire [7:0] undriven;
  wire [15:0] and_17_out, and_18_out, and_19_out, and_20_out, and_21_out, and_22_out, and_23_out, and_24_out,
       and_25_out, and_26_out, and_27_out, and_28_out, and_29_out, and_30_out, and_31_out, and_32_out,
       and_33_out, and_34_out, and_35_out, and_36_out, and_37_out, and_38_out, and_39_out, and_40_out,
       and_41_out, and_42_out, and_43_out, and_44_out, and_45_out, and_46_out, and_47_out, and_48_out,
       bit_extender_1_out, bit_extender_2_out, bit_extender_3_out, bit_extender_4_out, bit_extender_5_out,
       bit_extender_6_out, bit_extender_7_out, bit_extender_8_out, bit_extender_9_out, bit_extender_10_out,
       bit_extender_11_out, bit_extender_12_out, bit_extender_13_out, bit_extender_14_out,
       bit_extender_15_out, bit_extender_16_out, bit_extender_17_out, bit_extender_18_out,
       bit_extender_19_out, bit_extender_20_out, bit_extender_21_out, bit_extender_22_out,
       bit_extender_23_out, bit_extender_24_out, bit_extender_25_out, bit_extender_26_out,
       bit_extender_27_out, bit_extender_28_out, bit_extender_29_out, bit_extender_30_out,
       bit_extender_31_out, bit_extender_32_out, or_10_out, or_11_out, or_12_out, or_13_out, or_14_out,
       or_15_out, or_16_out, or_17_out, or_18_out, or_19_out, or_20_out, or_21_out, or_22_out, or_23_out,
       or_24_out, or_26_out, or_27_out, or_28_out, or_29_out, or_30_out, or_31_out, or_32_out, or_33_out,
       or_34_out, or_35_out, or_36_out, or_37_out, or_38_out, or_39_out, or_40_out, register_1_q,
       register_2_q, register_3_q, register_4_q, register_5_q, register_6_q, register_7_q, register_8_q,
       register_9_q, register_10_q, register_11_q, register_12_q, register_13_q, register_14_q,
       register_15_q, register_16_q, register_17_q;

  Register #(.trigger("falling"), .width(16)) register_1 (
    .D(data_bus_in), .clk(clock), .Q(register_1_q), .clr(reset));  // open: en
  eight_bit_eq_cmp eight_bit_eq_cmp_1 (.in_1(undriven), .in_2(8'h20), .out_3(eight_bit_eq_cmp_1_out_3));
  eight_bit_eq_cmp eight_bit_eq_cmp_2 (.in_1(undriven), .in_2(8'h21), .out_3(eight_bit_eq_cmp_2_out_3));
  eight_bit_eq_cmp eight_bit_eq_cmp_3 (.in_1(undriven), .in_2(8'h22), .out_3(eight_bit_eq_cmp_3_out_3));
  eight_bit_eq_cmp eight_bit_eq_cmp_4 (.in_1(undriven), .in_2(8'h23), .out_3(eight_bit_eq_cmp_4_out_3));
  eight_bit_eq_cmp eight_bit_eq_cmp_5 (.in_1(undriven), .in_2(8'h24), .out_3(eight_bit_eq_cmp_5_out_3));
  eight_bit_eq_cmp eight_bit_eq_cmp_6 (.in_1(control_bus_2[7:0]), .in_2(8'h20), .out_3(eight_bit_eq_cmp_6_out_3));
  eight_bit_eq_cmp eight_bit_eq_cmp_7 (.in_1(control_bus_2[7:0]), .in_2(8'h21), .out_3(eight_bit_eq_cmp_7_out_3));
  eight_bit_eq_cmp eight_bit_eq_cmp_8 (.in_1(control_bus_2[7:0]), .in_2(8'h22), .out_3(eight_bit_eq_cmp_8_out_3));
  eight_bit_eq_cmp eight_bit_eq_cmp_9 (.in_1(control_bus_2[7:0]), .in_2(8'h23), .out_3(eight_bit_eq_cmp_9_out_3));
  eight_bit_eq_cmp eight_bit_eq_cmp_10 (.in_1(control_bus_2[7:0]), .in_2(8'h24), .out_3(eight_bit_eq_cmp_10_out_3));
  or or_1 (or_1_out, eight_bit_eq_cmp_2_out_3, or_2_out);
  or or_2 (or_2_out, eight_bit_eq_cmp_3_out_3, eight_bit_eq_cmp_4_out_3);
  or or_3 (or_3_out, eight_bit_eq_cmp_7_out_3, or_4_out);
  or or_4 (or_4_out, eight_bit_eq_cmp_8_out_3, eight_bit_eq_cmp_9_out_3);
  or or_5 (or_5_out, eight_bit_eq_cmp_1_out_3, eight_bit_eq_cmp_6_out_3);
  or or_6 (or_6_out, or_1_out, or_3_out);
  or or_7 (or_7_out, eight_bit_eq_cmp_5_out_3, eight_bit_eq_cmp_10_out_3);
  assign or_8_out = control_bus_1[11:8] | control_bus_2[11:8];  // OR_Gate or_8, 4 bits wide
  assign or_9_out = control_bus_1[15:12] | control_bus_2[15:12];  // OR_Gate or_9, 4 bits wide
  assign bit_extender_1_out = {{15{four_bit_eq_cmp_1_out_3}}, four_bit_eq_cmp_1_out_3};  // Bit_Extender bit_extender_1
  four_bit_eq_cmp four_bit_eq_cmp_1 (.in_1(or_9_out), .in_2(4'b0000), .out_3(four_bit_eq_cmp_1_out_3));
  four_bit_eq_cmp four_bit_eq_cmp_2 (.in_1(or_8_out), .in_2(4'b0000), .out_3(four_bit_eq_cmp_2_out_3));
  assign bit_extender_2_out = {{15{four_bit_eq_cmp_2_out_3}}, four_bit_eq_cmp_2_out_3};  // Bit_Extender bit_extender_2
  assign bit_extender_3_out = {{15{four_bit_eq_cmp_3_out_3}}, four_bit_eq_cmp_3_out_3};  // Bit_Extender bit_extender_3
  four_bit_eq_cmp four_bit_eq_cmp_3 (.in_1(or_9_out), .in_2(4'b0001), .out_3(four_bit_eq_cmp_3_out_3));
  four_bit_eq_cmp four_bit_eq_cmp_4 (.in_1(or_8_out), .in_2(4'b0001), .out_3(four_bit_eq_cmp_4_out_3));
  assign bit_extender_4_out = {{15{four_bit_eq_cmp_4_out_3}}, four_bit_eq_cmp_4_out_3};  // Bit_Extender bit_extender_4
  assign bit_extender_5_out = {{15{four_bit_eq_cmp_5_out_3}}, four_bit_eq_cmp_5_out_3};  // Bit_Extender bit_extender_5
  four_bit_eq_cmp four_bit_eq_cmp_5 (.in_1(or_9_out), .in_2(4'b0010), .out_3(four_bit_eq_cmp_5_out_3));
  four_bit_eq_cmp four_bit_eq_cmp_6 (.in_1(or_8_out), .in_2(4'b0010), .out_3(four_bit_eq_cmp_6_out_3));
  assign bit_extender_6_out = {{15{four_bit_eq_cmp_6_out_3}}, four_bit_eq_cmp_6_out_3};  // Bit_Extender bit_extender_6
  assign bit_extender_7_out = {{15{four_bit_eq_cmp_7_out_3}}, four_bit_eq_cmp_7_out_3};  // Bit_Extender bit_extender_7
  four_bit_eq_cmp four_bit_eq_cmp_7 (.in_1(or_9_out), .in_2(4'b0011), .out_3(four_bit_eq_cmp_7_out_3));
  four_bit_eq_cmp four_bit_eq_cmp_8 (.in_1(or_8_out), .in_2(4'b0011), .out_3(four_bit_eq_cmp_8_out_3));
  assign bit_extender_8_out = {{15{four_bit_eq_cmp_8_out_3}}, four_bit_eq_cmp_8_out_3};  // Bit_Extender bit_extender_8
  assign bit_extender_9_out = {{15{four_bit_eq_cmp_9_out_3}}, four_bit_eq_cmp_9_out_3};  // Bit_Extender bit_extender_9
  four_bit_eq_cmp four_bit_eq_cmp_9 (.in_1(or_9_out), .in_2(4'b0100), .out_3(four_bit_eq_cmp_9_out_3));
  four_bit_eq_cmp four_bit_eq_cmp_10 (.in_1(or_8_out), .in_2(4'b0100), .out_3(four_bit_eq_cmp_10_out_3));
  assign bit_extender_10_out = {{15{four_bit_eq_cmp_10_out_3}}, four_bit_eq_cmp_10_out_3};  // Bit_Extender bit_extender_10
  assign bit_extender_11_out = {{15{four_bit_eq_cmp_11_out_3}}, four_bit_eq_cmp_11_out_3};  // Bit_Extender bit_extender_11
  four_bit_eq_cmp four_bit_eq_cmp_11 (.in_1(or_9_out), .in_2(4'b0101), .out_3(four_bit_eq_cmp_11_out_3));
  four_bit_eq_cmp four_bit_eq_cmp_12 (.in_1(or_8_out), .in_2(4'b0101), .out_3(four_bit_eq_cmp_12_out_3));
  assign bit_extender_12_out = {{15{four_bit_eq_cmp_12_out_3}}, four_bit_eq_cmp_12_out_3};  // Bit_Extender bit_extender_12
  assign bit_extender_13_out = {{15{four_bit_eq_cmp_13_out_3}}, four_bit_eq_cmp_13_out_3};  // Bit_Extender bit_extender_13
  four_bit_eq_cmp four_bit_eq_cmp_13 (.in_1(or_9_out), .in_2(4'b0110), .out_3(four_bit_eq_cmp_13_out_3));
  four_bit_eq_cmp four_bit_eq_cmp_14 (.in_1(or_8_out), .in_2(4'b0110), .out_3(four_bit_eq_cmp_14_out_3));
  assign bit_extender_14_out = {{15{four_bit_eq_cmp_14_out_3}}, four_bit_eq_cmp_14_out_3};  // Bit_Extender bit_extender_14
  assign bit_extender_15_out = {{15{four_bit_eq_cmp_15_out_3}}, four_bit_eq_cmp_15_out_3};  // Bit_Extender bit_extender_15
  four_bit_eq_cmp four_bit_eq_cmp_15 (.in_1(or_9_out), .in_2(4'b0111), .out_3(four_bit_eq_cmp_15_out_3));
  four_bit_eq_cmp four_bit_eq_cmp_16 (.in_1(or_8_out), .in_2(4'b0111), .out_3(four_bit_eq_cmp_16_out_3));
  assign bit_extender_16_out = {{15{four_bit_eq_cmp_16_out_3}}, four_bit_eq_cmp_16_out_3};  // Bit_Extender bit_extender_16
  assign bit_extender_17_out = {{15{four_bit_eq_cmp_17_out_3}}, four_bit_eq_cmp_17_out_3};  // Bit_Extender bit_extender_17
  four_bit_eq_cmp four_bit_eq_cmp_17 (.in_1(or_9_out), .in_2(4'b1000), .out_3(four_bit_eq_cmp_17_out_3));
  four_bit_eq_cmp four_bit_eq_cmp_18 (.in_1(or_8_out), .in_2(4'b1000), .out_3(four_bit_eq_cmp_18_out_3));
  assign bit_extender_18_out = {{15{four_bit_eq_cmp_18_out_3}}, four_bit_eq_cmp_18_out_3};  // Bit_Extender bit_extender_18
  assign bit_extender_19_out = {{15{four_bit_eq_cmp_19_out_3}}, four_bit_eq_cmp_19_out_3};  // Bit_Extender bit_extender_19
  four_bit_eq_cmp four_bit_eq_cmp_19 (.in_1(or_9_out), .in_2(4'b1001), .out_3(four_bit_eq_cmp_19_out_3));
  four_bit_eq_cmp four_bit_eq_cmp_20 (.in_1(or_8_out), .in_2(4'b1001), .out_3(four_bit_eq_cmp_20_out_3));
  assign bit_extender_20_out = {{15{four_bit_eq_cmp_20_out_3}}, four_bit_eq_cmp_20_out_3};  // Bit_Extender bit_extender_20
  assign bit_extender_21_out = {{15{four_bit_eq_cmp_21_out_3}}, four_bit_eq_cmp_21_out_3};  // Bit_Extender bit_extender_21
  four_bit_eq_cmp four_bit_eq_cmp_21 (.in_1(or_9_out), .in_2(4'b1010), .out_3(four_bit_eq_cmp_21_out_3));
  four_bit_eq_cmp four_bit_eq_cmp_22 (.in_1(or_8_out), .in_2(4'b1010), .out_3(four_bit_eq_cmp_22_out_3));
  assign bit_extender_22_out = {{15{four_bit_eq_cmp_22_out_3}}, four_bit_eq_cmp_22_out_3};  // Bit_Extender bit_extender_22
  assign bit_extender_23_out = {{15{four_bit_eq_cmp_23_out_3}}, four_bit_eq_cmp_23_out_3};  // Bit_Extender bit_extender_23
  four_bit_eq_cmp four_bit_eq_cmp_23 (.in_1(or_9_out), .in_2(4'b1011), .out_3(four_bit_eq_cmp_23_out_3));
  four_bit_eq_cmp four_bit_eq_cmp_24 (.in_1(or_8_out), .in_2(4'b1011), .out_3(four_bit_eq_cmp_24_out_3));
  assign bit_extender_24_out = {{15{four_bit_eq_cmp_24_out_3}}, four_bit_eq_cmp_24_out_3};  // Bit_Extender bit_extender_24
  assign bit_extender_25_out = {{15{four_bit_eq_cmp_25_out_3}}, four_bit_eq_cmp_25_out_3};  // Bit_Extender bit_extender_25
  four_bit_eq_cmp four_bit_eq_cmp_25 (.in_1(or_9_out), .in_2(4'b1100), .out_3(four_bit_eq_cmp_25_out_3));
  four_bit_eq_cmp four_bit_eq_cmp_26 (.in_1(or_8_out), .in_2(4'b1100), .out_3(four_bit_eq_cmp_26_out_3));
  assign bit_extender_26_out = {{15{four_bit_eq_cmp_26_out_3}}, four_bit_eq_cmp_26_out_3};  // Bit_Extender bit_extender_26
  assign bit_extender_27_out = {{15{four_bit_eq_cmp_27_out_3}}, four_bit_eq_cmp_27_out_3};  // Bit_Extender bit_extender_27
  four_bit_eq_cmp four_bit_eq_cmp_27 (.in_1(or_9_out), .in_2(4'b1101), .out_3(four_bit_eq_cmp_27_out_3));
  four_bit_eq_cmp four_bit_eq_cmp_28 (.in_1(or_8_out), .in_2(4'b1101), .out_3(four_bit_eq_cmp_28_out_3));
  assign bit_extender_28_out = {{15{four_bit_eq_cmp_28_out_3}}, four_bit_eq_cmp_28_out_3};  // Bit_Extender bit_extender_28
  assign bit_extender_29_out = {{15{four_bit_eq_cmp_29_out_3}}, four_bit_eq_cmp_29_out_3};  // Bit_Extender bit_extender_29
  four_bit_eq_cmp four_bit_eq_cmp_29 (.in_1(or_9_out), .in_2(4'b1110), .out_3(four_bit_eq_cmp_29_out_3));
  four_bit_eq_cmp four_bit_eq_cmp_30 (.in_1(or_8_out), .in_2(4'b1110), .out_3(four_bit_eq_cmp_30_out_3));
  assign bit_extender_30_out = {{15{four_bit_eq_cmp_30_out_3}}, four_bit_eq_cmp_30_out_3};  // Bit_Extender bit_extender_30
  assign bit_extender_31_out = {{15{four_bit_eq_cmp_31_out_3}}, four_bit_eq_cmp_31_out_3};  // Bit_Extender bit_extender_31
  four_bit_eq_cmp four_bit_eq_cmp_31 (.in_1(or_9_out), .in_2(4'b1111), .out_3(four_bit_eq_cmp_31_out_3));
  four_bit_eq_cmp four_bit_eq_cmp_32 (.in_1(or_8_out), .in_2(4'b1111), .out_3(four_bit_eq_cmp_32_out_3));
  assign bit_extender_32_out = {{15{four_bit_eq_cmp_32_out_3}}, four_bit_eq_cmp_32_out_3};  // Bit_Extender bit_extender_32
  and and_1 (and_1_out, or_7_out, four_bit_eq_cmp_1_out_3);
  and and_2 (and_2_out, or_7_out, four_bit_eq_cmp_3_out_3);
  and and_3 (and_3_out, or_7_out, four_bit_eq_cmp_5_out_3);
  and and_4 (and_4_out, or_7_out, four_bit_eq_cmp_7_out_3);
  and and_5 (and_5_out, or_7_out, four_bit_eq_cmp_9_out_3);
  and and_6 (and_6_out, or_7_out, four_bit_eq_cmp_11_out_3);
  and and_7 (and_7_out, or_7_out, four_bit_eq_cmp_13_out_3);
  and and_8 (and_8_out, or_7_out, four_bit_eq_cmp_15_out_3);
  and and_9 (and_9_out, or_7_out, four_bit_eq_cmp_17_out_3);
  and and_10 (and_10_out, or_7_out, four_bit_eq_cmp_19_out_3);
  and and_11 (and_11_out, or_7_out, four_bit_eq_cmp_21_out_3);
  and and_12 (and_12_out, or_7_out, four_bit_eq_cmp_23_out_3);
  and and_13 (and_13_out, or_7_out, four_bit_eq_cmp_25_out_3);
  and and_14 (and_14_out, or_7_out, four_bit_eq_cmp_27_out_3);
  and and_15 (and_15_out, or_7_out, four_bit_eq_cmp_29_out_3);
  and and_16 (and_16_out, or_7_out, four_bit_eq_cmp_31_out_3);
  Register #(.width(16)) register_2 (.D(register_1_q), .en(and_1_out), .clk(clock), .Q(register_2_q), .clr(reset));
  Register #(.width(16)) register_3 (.D(register_1_q), .en(and_2_out), .clk(clock), .Q(register_3_q), .clr(reset));
  Register #(.width(16)) register_4 (.D(register_1_q), .en(and_3_out), .clk(clock), .Q(register_4_q), .clr(reset));
  Register #(.width(16)) register_5 (.D(register_1_q), .en(and_4_out), .clk(clock), .Q(register_5_q), .clr(reset));
  Register #(.width(16)) register_6 (.D(register_1_q), .en(and_5_out), .clk(clock), .Q(register_6_q), .clr(reset));
  Register #(.width(16)) register_7 (.D(register_1_q), .en(and_6_out), .clk(clock), .Q(register_7_q), .clr(reset));
  Register #(.width(16)) register_8 (.D(register_1_q), .en(and_7_out), .clk(clock), .Q(register_8_q), .clr(reset));
  Register #(.width(16)) register_9 (.D(register_1_q), .en(and_8_out), .clk(clock), .Q(register_9_q), .clr(reset));
  Register #(.width(16)) register_10 (.D(register_1_q), .en(and_9_out), .clk(clock), .Q(register_10_q), .clr(reset));
  Register #(.width(16)) register_11 (.D(register_1_q), .en(and_10_out), .clk(clock), .Q(register_11_q), .clr(reset));
  Register #(.width(16)) register_12 (.D(register_1_q), .en(and_11_out), .clk(clock), .Q(register_12_q), .clr(reset));
  Register #(.width(16)) register_13 (.D(register_1_q), .en(and_12_out), .clk(clock), .Q(register_13_q), .clr(reset));
  Register #(.width(16)) register_14 (.D(register_1_q), .en(and_13_out), .clk(clock), .Q(register_14_q), .clr(reset));
  Register #(.width(16)) register_15 (.D(register_1_q), .en(and_14_out), .clk(clock), .Q(register_15_q), .clr(reset));
  Register #(.width(16)) register_16 (.D(register_1_q), .en(and_15_out), .clk(clock), .Q(register_16_q), .clr(reset));
  Register #(.width(16)) register_17 (.D(register_1_q), .en(and_16_out), .clk(clock), .Q(register_17_q), .clr(reset));
  assign and_17_out = register_2_q & bit_extender_1_out;  // AND_Gate and_17, 16 bits wide
  assign or_10_out = and_17_out | and_17_out;  // OR_Gate or_10, 16 bits wide
  assign and_18_out = register_3_q & bit_extender_3_out;  // AND_Gate and_18, 16 bits wide
  assign or_11_out = and_18_out | or_10_out;  // OR_Gate or_11, 16 bits wide
  assign and_19_out = register_4_q & bit_extender_5_out;  // AND_Gate and_19, 16 bits wide
  assign or_12_out = and_19_out | or_11_out;  // OR_Gate or_12, 16 bits wide
  assign and_20_out = register_5_q & bit_extender_7_out;  // AND_Gate and_20, 16 bits wide
  assign or_13_out = and_20_out | or_12_out;  // OR_Gate or_13, 16 bits wide
  assign and_21_out = register_6_q & bit_extender_9_out;  // AND_Gate and_21, 16 bits wide
  assign or_14_out = and_21_out | or_13_out;  // OR_Gate or_14, 16 bits wide
  assign and_22_out = register_7_q & bit_extender_11_out;  // AND_Gate and_22, 16 bits wide
  assign or_15_out = and_22_out | or_14_out;  // OR_Gate or_15, 16 bits wide
  assign and_23_out = register_8_q & bit_extender_13_out;  // AND_Gate and_23, 16 bits wide
  assign or_16_out = and_23_out | or_15_out;  // OR_Gate or_16, 16 bits wide
  assign and_24_out = register_9_q & bit_extender_15_out;  // AND_Gate and_24, 16 bits wide
  assign or_17_out = and_24_out | or_16_out;  // OR_Gate or_17, 16 bits wide
  assign and_25_out = register_10_q & bit_extender_17_out;  // AND_Gate and_25, 16 bits wide
  assign or_18_out = and_25_out | or_17_out;  // OR_Gate or_18, 16 bits wide
  assign and_26_out = register_11_q & bit_extender_19_out;  // AND_Gate and_26, 16 bits wide
  assign or_19_out = and_26_out | or_18_out;  // OR_Gate or_19, 16 bits wide
  assign and_27_out = register_12_q & bit_extender_21_out;  // AND_Gate and_27, 16 bits wide
  assign or_20_out = and_27_out | or_19_out;  // OR_Gate or_20, 16 bits wide
  assign and_28_out = register_13_q & bit_extender_23_out;  // AND_Gate and_28, 16 bits wide
  assign or_21_out = and_28_out | or_20_out;  // OR_Gate or_21, 16 bits wide
  assign and_29_out = register_14_q & bit_extender_25_out;  // AND_Gate and_29, 16 bits wide
  assign or_22_out = and_29_out | or_21_out;  // OR_Gate or_22, 16 bits wide
  assign and_30_out = register_15_q & bit_extender_27_out;  // AND_Gate and_30, 16 bits wide
  assign or_23_out = and_30_out | or_22_out;  // OR_Gate or_23, 16 bits wide
  assign and_31_out = register_16_q & bit_extender_29_out;  // AND_Gate and_31, 16 bits wide
  assign or_24_out = and_31_out | or_23_out;  // OR_Gate or_24, 16 bits wide
  assign and_32_out = register_17_q & bit_extender_31_out;  // AND_Gate and_32, 16 bits wide
  assign alu1_out = and_32_out | or_24_out;  // OR_Gate or_25, 16 bits wide
  assign and_33_out = register_2_q & bit_extender_2_out;  // AND_Gate and_33, 16 bits wide
  assign or_26_out = and_33_out | and_33_out;  // OR_Gate or_26, 16 bits wide
  assign and_34_out = register_3_q & bit_extender_4_out;  // AND_Gate and_34, 16 bits wide
  assign or_27_out = and_34_out | or_26_out;  // OR_Gate or_27, 16 bits wide
  assign and_35_out = register_4_q & bit_extender_6_out;  // AND_Gate and_35, 16 bits wide
  assign or_28_out = and_35_out | or_27_out;  // OR_Gate or_28, 16 bits wide
  assign and_36_out = register_5_q & bit_extender_8_out;  // AND_Gate and_36, 16 bits wide
  assign or_29_out = and_36_out | or_28_out;  // OR_Gate or_29, 16 bits wide
  assign and_37_out = register_6_q & bit_extender_10_out;  // AND_Gate and_37, 16 bits wide
  assign or_30_out = and_37_out | or_29_out;  // OR_Gate or_30, 16 bits wide
  assign and_38_out = register_7_q & bit_extender_12_out;  // AND_Gate and_38, 16 bits wide
  assign or_31_out = and_38_out | or_30_out;  // OR_Gate or_31, 16 bits wide
  assign and_39_out = register_8_q & bit_extender_14_out;  // AND_Gate and_39, 16 bits wide
  assign or_32_out = and_39_out | or_31_out;  // OR_Gate or_32, 16 bits wide
  assign and_40_out = register_9_q & bit_extender_16_out;  // AND_Gate and_40, 16 bits wide
  assign or_33_out = and_40_out | or_32_out;  // OR_Gate or_33, 16 bits wide
  assign and_41_out = register_10_q & bit_extender_18_out;  // AND_Gate and_41, 16 bits wide
  assign or_34_out = and_41_out | or_33_out;  // OR_Gate or_34, 16 bits wide
  assign and_42_out = register_11_q & bit_extender_20_out;  // AND_Gate and_42, 16 bits wide
  assign or_35_out = and_42_out | or_34_out;  // OR_Gate or_35, 16 bits wide
  assign and_43_out = register_12_q & bit_extender_22_out;  // AND_Gate and_43, 16 bits wide
  assign or_36_out = and_43_out | or_35_out;  // OR_Gate or_36, 16 bits wide
  assign and_44_out = register_13_q & bit_extender_24_out;  // AND_Gate and_44, 16 bits wide
  assign or_37_out = and_44_out | or_36_out;  // OR_Gate or_37, 16 bits wide
  assign and_45_out = register_14_q & bit_extender_26_out;  // AND_Gate and_45, 16 bits wide
  assign or_38_out = and_45_out | or_37_out;  // OR_Gate or_38, 16 bits wide
  assign and_46_out = register_15_q & bit_extender_28_out;  // AND_Gate and_46, 16 bits wide
  assign or_39_out = and_46_out | or_38_out;  // OR_Gate or_39, 16 bits wide
  assign and_47_out = register_16_q & bit_extender_30_out;  // AND_Gate and_47, 16 bits wide
  assign or_40_out = and_47_out | or_39_out;  // OR_Gate or_40, 16 bits wide
  assign and_48_out = register_17_q & bit_extender_32_out;  // AND_Gate and_48, 16 bits wide
  assign alu2_out = and_48_out | or_40_out;  // OR_Gate or_41, 16 bits wide
  sixt_bit_gatekeeper sixt_bit_gatekeeper_1 (.in_1(or_5_out), .in_2(alu1_out), .out_3(data_bus_out));
  sixt_bit_gatekeeper sixt_bit_gatekeeper_2 (.in_1(or_6_out), .in_2(alu2_out), .out_3(addr_bus_out));
endmodule

module registers_controller (
  input  [15:0] control_bus,
  output Write,
  output Data_bus,
  output Addr_bus,
  output [3:0] selector,
  output [3:0] out_6,
  output [3:0] out_7
);

  wire eight_bit_eq_cmp_2_out_3, eight_bit_eq_cmp_3_out_3, eight_bit_eq_cmp_4_out_3, or_1_out;

  eight_bit_eq_cmp eight_bit_eq_cmp_1 (.in_1(control_bus[7:0]), .in_2(8'h20), .out_3(Data_bus));
  eight_bit_eq_cmp eight_bit_eq_cmp_2 (.in_1(control_bus[7:0]), .in_2(8'h21), .out_3(eight_bit_eq_cmp_2_out_3));
  or or_1 (or_1_out, eight_bit_eq_cmp_3_out_3, eight_bit_eq_cmp_4_out_3);
  eight_bit_eq_cmp eight_bit_eq_cmp_3 (.in_1(control_bus[7:0]), .in_2(8'h22), .out_3(eight_bit_eq_cmp_3_out_3));
  eight_bit_eq_cmp eight_bit_eq_cmp_4 (.in_1(control_bus[7:0]), .in_2(8'h23), .out_3(eight_bit_eq_cmp_4_out_3));
  eight_bit_eq_cmp eight_bit_eq_cmp_5 (.in_1(control_bus[7:0]), .in_2(8'h24), .out_3(Write));
  or or_2 (Addr_bus, eight_bit_eq_cmp_2_out_3, or_1_out);

  assign out_6 = control_bus[15:12];
  assign out_7 = control_bus[11:8];
  assign selector = control_bus[15:12];

  // Notes on the sheet:
  //   ALU 1
  //   ALU 2
endmodule

module control_unit (
  input  [15:0] data_bus_in,
  input  [15:0] program_kounter,
  input  clock,
  input  [15:0] stack_pointer,
  input  reset,
  input  [15:0] addr_bus,
  input  [15:0] control_bus_1,
  input  [15:0] control_bus_2,
  output [15:0] data_bus_out,
  output [15:0] control_bus_1_out,
  output [15:0] addr_bus_out,
  output [15:0] to_pk,
  output [15:0] control_bus_2_out
);

  wire and_1_out, button_1_out, comparator_1_lt, or_1_out, or_2_out, pulse_extender_1_out_6,
       sixt_bit_eq_cmp_1_out_3, sixt_bit_eq_cmp_2_out_3, sixt_bit_eq_cmp_3_out_3;
  wire [15:0] multiplexer_1_out, multiplexer_2_out, register_1_q, register_4_q, rom_1_data, rom_2_data,
       sixt_bit_incrementer_1_out_2, tmp_regs_unit_1_out_8, tmp_regs_unit_1_out_10;
  wire [31:0] adder_1_out, adder_2_out, adder_3_out, register_2_q, register_3_q;

  Button button_1 (.out(button_1_out));
  or or_1 (or_1_out, button_1_out, reset);
  // Probe on data_bus_in
  pulse_extender pulse_extender_1 (
    .in_1(or_1_out), .in_2(clock), .out_6(pulse_extender_1_out_6));  // open: in_3, out_4, out_5
  // Probe on control_bus_1
  // Probe on control_bus_2
  and and_1 (and_1_out, clock, ~pulse_extender_1_out_6);  // AND_Gate
  Register #(.trigger("falling"), .width(16)) register_1 (
    .D(data_bus_in), .en(sixt_bit_eq_cmp_1_out_3), .clk(and_1_out), .Q(register_1_q), .clr(or_1_out));
  sixt_bit_eq_cmp sixt_bit_eq_cmp_1 (.in_1(rom_2_data), .in_2(16'h1), .out_3(sixt_bit_eq_cmp_1_out_3));
  Register #(.width(32)) register_2 (.D(adder_1_out), .clk(clock), .Q(register_2_q), .clr(or_1_out));  // open: en
  Adder #(.width(32)) adder_1 (.a(register_2_q), .b(32'h1), .out(adder_1_out));  // open: cin, cout
  Register #(.trigger("falling"), .width(32)) register_3 (
    .D(adder_2_out), .clk(clock), .Q(register_3_q), .clr(or_1_out));  // open: en
  Adder #(.width(32)) adder_2 (.a(register_3_q), .b(32'h1), .out(adder_2_out));  // open: cin, cout
  ROM #(.addrWidth(16), .dataWidth(16)) rom_1 (.addr(data_bus_in), .data(rom_1_data));
  // Probe on tmp_regs_unit_1_out_8
  // Probe on tmp_regs_unit_1_out_10
  tmp_regs_unit tmp_regs_unit_1 (
    .clock(and_1_out), .reset(or_1_out), .control_bus_1(control_bus_1), .control_bus_2(control_bus_2),
    .data_bus_in(data_bus_in), .out_8(tmp_regs_unit_1_out_8), .out_10(tmp_regs_unit_1_out_10),
    .data_bus_out(data_bus_out), .addr_bus_out(addr_bus_out), .to_pk(to_pk));
  Adder #(.width(32)) adder_3 (.a(register_2_q), .b(register_3_q), .out(adder_3_out));  // open: cin, cout
  Comparator #(.width(32)) comparator_1 (.a(adder_3_out), .b({32{1'b0}}), .lt(comparator_1_lt));  // open: gt, eq
  ROM #(.addrWidth(16), .dataWidth(16)) rom_2 (.addr(register_4_q), .data(rom_2_data));
  ROM #(.addrWidth(16), .dataWidth(16)) rom_3 (.addr(register_4_q), .data(control_bus_2_out));
  Multiplexer #(.width(16)) multiplexer_1 (
    .in0(sixt_bit_incrementer_1_out_2), .in1(rom_1_data), .out(multiplexer_1_out),
    .sel(sixt_bit_eq_cmp_2_out_3));
  Multiplexer #(.width(16)) multiplexer_2 (
    .in0(multiplexer_1_out), .in1({16{1'b1}}), .out(multiplexer_2_out), .sel(comparator_1_lt));
  sixt_bit_eq_cmp sixt_bit_eq_cmp_2 (.in_1(rom_2_data), .in_2(16'h1), .out_3(sixt_bit_eq_cmp_2_out_3));
  Register #(.trigger("falling"), .width(16)) register_4 (
    .D(multiplexer_2_out), .clk(and_1_out), .Q(register_4_q), .clr(or_2_out));  // open: en
  or or_2 (or_2_out, or_1_out, sixt_bit_eq_cmp_3_out_3);
  sixt_bit_eq_cmp sixt_bit_eq_cmp_3 (.in_1(rom_2_data), .in_2(16'hfffe), .out_3(sixt_bit_eq_cmp_3_out_3));
  sixt_bit_incrementer sixt_bit_incrementer_1 (.in_1(register_4_q), .out_2(sixt_bit_incrementer_1_out_2));
  Multiplexer #(.width(16)) multiplexer_3 (
    .in0(rom_2_data), .in1({16{1'b0}}), .out(control_bus_1_out), .sel(comparator_1_lt));
  // Probe on program_kounter
  // Probe on stack_pointer
  // Probe on addr_bus

  // Notes on the sheet:
  //   contents of rom_1 (hex, n*v repeats v):
  //   2 4 7 c 19e7 19ed 19f0 1ba5 8*0 1e7 1ea 1ed 1f0 1f3 1f6 1f9 1fc 24*0 1e10 1e23 0 1f5c 1f60 1f74 1f77
  //   1f7a 2154 2157 215a 1f66 1f6d 1f80 1f85 1f8a 2160 2165 216a 1f74 1f92 1f92 1f92 2172 2172 2172 483c
  //   4850 4850 4850 48c0 48c0 48c0 483c 4850 4850 4850 48c0 48c0 48c0 483c 4845 4850 4857 4857 48c0 48c0
  //   48c0 64*0 4ad0 4ad2 4ad4 4ad6 4ad8 4adb 92*0 11 16 0 0 19f2 9*0 1ff 202 205 208 20b 20e 211 214 24*0
  //   1e19 1e29 0 0 0 1f92 1f95 1f98 2172 2175 2178 0 0 1f9e 1fa3 1fa8 217e 2183 2188 45c6 1fb0 1fb0 1fb0
  //   2190 2190 2190 483c 4857 4857 4857 48c0 48c0 48c0 483c 4857 4857 4857 48c0 48c0 48c0 0 0 4857 485e
  //   485e 48c0 48c0 48c0 68*0 4ade 4ae1 92*0 1b 20 0 0 19f8 1ba7 8*0 217 21a 21d 220 223 226 229 22c 25*0
  //   1e30 0 0 0 1fb0 1fb3 1fb6 2190 2193 2196 0 0 1fbc 1fc1 1fc6 219c 21a1 21a6 0 1fce 1fce 1fce 21ae
  //   21ae 21ae 0 485e 485e 485e 48c0 48c0 48c0 0 485e 485e 485e 48c0 48c0 48c0 0 0 485e 4865 4865 48c0
  //   48c0 48c0 68*0 4ae4 4ae7 96*0 1b41 1bb0 8*0 22f 232 235 238 23b 23e 241 244 25*0 1ef3 0 0 0 1fce
  //   1fd1 1fd4 21ae 21b1 21b4 0 0 1fda 1fdf 1fe4 21ba 21bf 21c4 0 1fec 1fec 1fec 21cc 21cc 21cc 0 4865
  //   4865 4865 48c0 48c0 48c0 0 4865 4865 4865 48c0 48c0 48c0 0 0 4865 486c 486c 48c0 48c0 48c0 68*0 4aea
  //   4aed 96*0 1b46 1bb4 8*0 247 24a 24d 250 253 256 259 25c 25*0 1ef9 0 0 0 1fec 1fef 1ff2 21cc 21cf
  //   21d2 0 0 1ff8 1ffd 2002 21d8 21dd 21e2 0 200a 200a 200a 21ea 21ea 21ea 0 486c 486c 486c 48c0 48c0
  //   48c0 0 486c 486c 486c 48c0 48c0 48c0 0 0 486c 4873 4873 48c0 48c0 48c0 68*0 4af0 4af3 96*0 1b4c 1bba
  //   8*0 25f 262 265 268 26b 26e 271 274 25*0 1f00 0 0 0 200a 200d 2010 5*0 2016 201b 2020 4*0 2028 2028
  //   2028 4*0 4873 4873 4873 4*0 4873 4873 4873 5*0 4873 487a 487a 71*0 4af6 4af9 97*0 1ce0 8*0 277 27a
  //   27d 280 283 286 289 28c 29*0 2028 202b 202e 5*0 2034 2039 203e 4*0 2046 2046 2046 4*0 487a 487a 487a
  //   4*0 487a 487a 487a 5*0 487a 4881 4881 71*0 4afc 4aff 97*0 1ce4 8*0 28f 292 295 298 29b 29e 2a1 2a4
  //   29*0 2046 2049 204c 5*0 2052 2057 205c 4*0 2064 2064 2064 4*0 4881 4881 4881 4*0 4881 4881 4881 5*0
  //   4881 4888 4888 71*0 4b02 4b05 97*0 1cea 8*0 2a7 2aa 2ad 2b0 2b3 2b6 2b9 2bc 29*0 2064 2067 206a 5*0
  //   2070 2075 207a 4*0 2082 2082 2082 4*0 4888 4888 4888 4*0 4888 4888 4888 5*0 4888 488f 488f 71*0 4b08
  //   4b0b 106*0 2bf 2c2 2c5 2c8 2cb 2ce 2d1 2d4 29*0 2082 2085 2088 5*0 208e 2093 2098 4*0 20a0 20a0 20a0
  //   4*0 488f 488f 488f 4*0 488f 488f 488f 5*0 488f 4896 4896 71*0 4b0e 4b11 106*0 2d7 2da 2dd 2e0 2e3
  //   2e6 2e9 2ec 29*0 20a0 20a3 20a6 5*0 20ac 20b1 20b6 4*0 20be 20be 20be 4*0 4896 4896 4896 4*0 4896
  //   4896 4896 5*0 4896 489d 489d 71*0 4b14 4b17 106*0 2ef 2f2 2f5 2f8 2fb 2fe 301 304 29*0 20be 20c1
  //   20c4 5*0 20ca 20cf 20d4 4*0 20dc 20dc 20dc 4*0 489d 489d 489d 4*0 489d 489d 489d 5*0 489d 48a4 48a4
  //   71*0 4b1a 4b1d 106*0 307 30a 30d 310 313 316 319 31c 29*0 20dc 20df 20e2 5*0 20e8 20ed 20f2 4*0 20fa
  //   20fa 20fa 4*0 48a4 48a4 48a4 4*0 48a4 48a4 48a4 5*0 48a4 48ab 48ab 71*0 4b20 4b23 106*0 31f 322 325
  //   328 32b 32e 331 334 29*0 20fa 20fd 2100 5*0 2106 210b 2110 4*0 2118 2118 2118 4*0 48ab 48ab 48ab 4*0
  //   48ab 48ab 48ab 5*0 48ab 48b2 48b2 71*0 4b26 4b29 106*0 337 33a 33d 340 343 346 349 34c 29*0 2118
  //   211b 211e 5*0 2124 2129 212e 4*0 2136 2136 2136 4*0 48b2 48b2 48b2 4*0 48b2 48b2 48b2 5*0 48b2 48b9
  //   48b9 71*0 4b2c 4b2f 106*0 34f 352 355 358 35b 35e 361 364 29*0 2136 2139 213c 5*0 2142 2147 214c 4*0
  //   2154 2154 2154 4*0 48b9 48b9 48b9 4*0 48b9 48b9 48b9 5*0 48b9 48c0 48c0 71*0 4b32 4b35 92*0 25 2a
  //   12*0 367 36a 36d 370 373 376 379 37c 25*0 1e30 0 21ea 21ee 2202 2205 2208 23e2 23e5 23e8 21f4 21fb
  //   220e 2213 2218 23ee 23f3 23f8 2202 2220 2220 2220 2400 2400 2400 48c0 48d4 48d4 48d4 4944 4944 4944
  //   48c0 48d4 48d4 48d4 4944 4944 4944 48c0 48c9 48d4 48db 48db 4944 4944 4944 64*0 4b38 4b3a 4b3c 4b3e
  //   4b40 4b43 92*0 2f 34 12*0 37f 382 385 388 38b 38e 391 394 25*0 1e36 0 0 0 2220 2223 2226 2400 2403
  //   2406 0 0 222c 2231 2236 240c 2411 2416 0 223e 223e 223e 241e 241e 241e 48c0 48db 48db 48db 4944 4944
  //   4944 48c0 48db 48db 48db 4944 4944 4944 0 0 48db 48e2 48e2 4944 4944 4944 68*0 4b46 4b49 92*0 39 3e
  //   12*0 397 39a 39d 3a0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
  //   contents of rom_2 (hex, n*v repeats v):
  //   11 1 0 fffe 4 6 fffe 4 2006 20 14 fffe 4 2006 20 15 fffe 4 2006 20 16 fffe 4 2006 20 17 fffe 4 2006
  //   20 18 fffe 4 2006 20 19 fffe 4 2006 1020 14 fffe 4 2006 1020 15 fffe 4 2006 1020 16 fffe 4 2006 1020
  //   17 fffe 4 2006 1020 18 fffe 4 2006 1020 19 fffe 4 2006 2020 14 fffe 4 2006 2020 15 fffe 4 2006 2020
  //   16 fffe 4 2006 2020 17 fffe 4 2006 2020 18 fffe 4 2006 2020 19 fffe 4 2006 3020 14 fffe 4 2006 3020
  //   15 fffe 4 2006 3020 16 fffe 4 2006 3020 17 fffe 4 2006 3020 18 fffe 4 2006 3020 19 fffe 4 2006 4020
  //   14 fffe 4 2006 4020 15 fffe 4 2006 4020 16 fffe 4 2006 4020 17 fffe 4 2006 4020 18 fffe 4 2006 4020
  //   19 fffe 4 2006 5020 14 fffe 4 2006 5020 15 fffe 4 2006 5020 16 fffe 4 2006 5020 17 fffe 4 2006 5020
  //   18 fffe 4 2006 5020 19 fffe 4 2006 6020 14 fffe 4 2006 6020 15 fffe 4 2006 6020 16 fffe 4 2006 6020
  //   17 fffe 4 2006 6020 18 fffe 4 2006 6020 19 fffe 4 2006 7020 14 fffe 4 2006 7020 15 fffe 4 2006 7020
  //   16 fffe 4 2006 7020 17 fffe 4 2006 7020 18 fffe 4 2006 7020 19 fffe 4 2006 8020 14 fffe 4 2006 8020
  //   15 fffe 4 2006 8020 16 fffe 4 2006 8020 17 fffe 4 2006 8020 18 fffe 4 2006 8020 19 fffe 4 2006 9020
  //   14 fffe 4 2006 9020 15 fffe 4 2006 9020 16 fffe 4 2006 9020 17 fffe 4 2006 9020 18 fffe 4 2006 9020
  //   19 fffe 4 2006 a020 14 fffe 4 2006 a020 15 fffe 4 2006 a020 16 fffe 4 2006 a020 17 fffe 4 2006 a020
  //   18 fffe 4 2006 a020 19 fffe 4 2006 b020 14 fffe 4 2006 b020 15 fffe 4 2006 b020 16 fffe 4 2006 b020
  //   17 fffe 4 2006 b020 18 fffe 4 2006 b020 19 fffe 4 2006 c020 14 fffe 4 2006 c020 15 fffe 4 2006 c020
  //   16 fffe 4 2006 c020 17 fffe 4 2006 c020 18 fffe 4 2006 c020 19 fffe 4 2006 d020 14 fffe 4 2006 d020
  //   15 fffe 4 2006 d020 16 fffe 4 2006 d020 17 fffe 4 2006 d020 18 fffe 4 2006 d020 19 fffe 4 2006 e020
  //   14 fffe 4 2006 e020 15 fffe 4 2006 e020 16 fffe 4 2006 e020 17 fffe 4 2006 e020 18 fffe 4 2006 e020
  //   19 fffe 4 2006 f020 14 fffe 4 2006 f020 15 fffe 4 2006 f020 16 fffe 4 2006 f020 17 fffe 4 2006 f020
  //   18 fffe 4 2006 f020 19 fffe 40 24 fffe 41 24 fffe 42 24 fffe 43 24 fffe 44 24 fffe 45 24 fffe 46 24
  //   fffe 47 24 fffe 140 24 fffe 141 24 fffe 142 24 fffe 143 24 fffe 144 24 fffe 145 24 fffe 146 24 fffe
  //   147 24 fffe 240 24 fffe 241 24 fffe 242 24 fffe 243 24 fffe 244 24 fffe 245 24 fffe 246 24 fffe 247
  //   24 fffe 340 24 fffe 341 24 fffe 342 24 fffe 343 24 fffe 344 24 fffe 345 24 fffe 346 24 fffe 347 24
  //   fffe 440 24 fffe 441 24 fffe 442 24 fffe 443 24 fffe 444 24 fffe 445 24 fffe 446 24 fffe 447 24 fffe
  //   540 24 fffe 541 24 fffe 542 24 fffe 543 24 fffe 544 24 fffe 545 24 fffe 546 24 fffe 547 24 fffe 640
  //   24 fffe 641 24 fffe 642 24 fffe 643 24 fffe 644 24 fffe 645 24 fffe 646 24 fffe 647 24 fffe 740 24
  //   fffe 741 24 fffe 742 24 fffe 743 24 fffe 744 24 fffe 745 24 fffe 746 24 fffe 747 24 fffe 840 24 fffe
  //   841 24 fffe 842 24 fffe 843 24 fffe 844 24 fffe 845 24 fffe 846 24 fffe 847 24 fffe 940 24 fffe 941
  //   24 fffe 942 24 fffe 943 24 fffe 944 24 fffe 945 24 fffe 946 24 fffe 947 24 fffe a40 24 fffe a41 24
  //   fffe a42 24 fffe a43 24 fffe a44 24 fffe a45 24 fffe a46 24 fffe a47 24 fffe b40 24 fffe b41 24 fffe
  //   b42 24 fffe b43 24 fffe b44 24 fffe b45 24 fffe b46 24 fffe b47 24 fffe c40 24 fffe c41 24 fffe c42
  //   24 fffe c43 24 fffe c44 24 fffe c45 24 fffe c46 24 fffe c47 24 fffe d40 24 fffe d41 24 fffe d42 24
  //   fffe d43 24 fffe d44 24 fffe d45 24 fffe d46 24 fffe d47 24 fffe e40 24 fffe e41 24 fffe e42 24 fffe
  //   e43 24 fffe e44 24 fffe e45 24 fffe e46 24 fffe e47 24 fffe f40 24 fffe f41 24 fffe f42 24 fffe f43
  //   24 fffe f44 24 fffe f45 24 fffe f46 24 fffe f47 24 fffe 1040 1024 fffe 1041 1024 fffe 1042 1024 fffe
  //   1043 1024 fffe 1044 1024 fffe 1045 1024 fffe 1046 1024 fffe 1047 1024 fffe 1140 1024 fffe 1141 1024
  //   fffe 1142 1024 fffe 1143 1024 fffe 1144 1024 fffe 1145 1024 fffe 1146 1024 fffe 1147 1024 fffe 1240
  //   1024 fffe 1241 1024 fffe 1242 1024 fffe 1243 1024 fffe 1244 1024 fffe 1245 1024 fffe 1246 1024 fffe
  //   1247 1024 fffe 1340 1024 fffe 1341 1024 fffe 1342 1024 fffe 1343 1024 fffe 1344 1024 fffe 1345 1024
  //   fffe 1346 1024 fffe 1347 1024 fffe 1440 1024 fffe 1441 1024 fffe 1442 1024 fffe 1443 1024 fffe 144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
  //   contents of rom_3 (hex, n*v repeats v):
  //   6632*0 1011 1003 2002 0 0 0 1010 5*0 1003 1292*0 11 0 0 0 2003 16*0 11 0 0 0 2003 16*0 11 0 0 0 2003
  //   16*0 11 0 0 0 2003 16*0 11 0 0 0 2003
endmodule

module counting_register (
  input  [15:0] data_in,
  input  increment,
  input  decrement,
  input  write,
  input  clk,
  input  reset,
  output [15:0] out_7
);

  wire or_1_out;
  wire [15:0] multiplexer_1_out, sixt_bit_adder_subtractor_1_out_4;

  Multiplexer #(.width(16)) multiplexer_1 (
    .in0(sixt_bit_adder_subtractor_1_out_4), .in1(data_in), .out(multiplexer_1_out), .sel(write));
  Register #(.width(16)) register_1 (.D(multiplexer_1_out), .en(or_1_out), .clk(clk), .Q(out_7), .clr(reset));
  or or_1 (or_1_out, increment, decrement, write);
  sixt_bit_adder_subtractor sixt_bit_adder_subtractor_1 (
    .in_3(decrement), .in_1(out_7), .in_2(16'h1), .out_4(sixt_bit_adder_subtractor_1_out_4));  // open: out_5
endmodule

module PK_control (
  input  [15:0] in_1,
  input  in_2,
  input  Restart,
  input  [15:0] in_4,
  input  [15:0] in_5,
  output [15:0] out_6,
  output out_7,
  output out_8,
  output out_9,
  output out_10,
  output out_11
);

  wire and_1_out, and_2_out, and_3_out, and_4_out, or_1_out, or_2_out, or_3_out, pulse_extender_1_out_6,
       sixt_bit_eq_cmp_1_out_3, sixt_bit_eq_cmp_2_out_3, sixt_bit_eq_cmp_3_out_3, sixt_bit_eq_cmp_4_out_3,
       sixt_bit_eq_zero_1_out_2;
  wire [5:0] rom_1_data;

  ROM #(.addrWidth(16), .dataWidth(6)) rom_1 (.addr(in_1), .data({rom_1_data[5:4], out_10, rom_1_data[2:0]}));
  sixt_bit_eq_zero sixt_bit_eq_zero_1 (.in_1(in_4), .out_2(sixt_bit_eq_zero_1_out_2));
  sixt_bit_eq_cmp sixt_bit_eq_cmp_1 (.in_1(in_1), .in_2(16'h20), .out_3(sixt_bit_eq_cmp_1_out_3));
  sixt_bit_eq_cmp sixt_bit_eq_cmp_2 (.in_1(in_1), .in_2(16'h21), .out_3(sixt_bit_eq_cmp_2_out_3));
  sixt_bit_eq_cmp sixt_bit_eq_cmp_3 (.in_1(in_1), .in_2(16'h22), .out_3(sixt_bit_eq_cmp_3_out_3));
  sixt_bit_eq_cmp sixt_bit_eq_cmp_4 (.in_1(in_1), .in_2(16'h23), .out_3(sixt_bit_eq_cmp_4_out_3));
  and and_1 (and_1_out, sixt_bit_eq_zero_1_out_2, sixt_bit_eq_cmp_1_out_3);
  or or_1 (or_1_out, and_1_out, and_2_out);
  and and_2 (and_2_out, ~sixt_bit_eq_zero_1_out_2, sixt_bit_eq_cmp_2_out_3);  // AND_Gate
  and and_3 (and_3_out, sixt_bit_eq_zero_1_out_2, sixt_bit_eq_cmp_3_out_3);
  or or_2 (or_2_out, and_3_out, and_4_out);
  and and_4 (and_4_out, ~sixt_bit_eq_zero_1_out_2, sixt_bit_eq_cmp_4_out_3);  // AND_Gate
  sixt_bit_selector sixt_bit_selector_1 (.in_3(in_5), .in_1(or_1_out), .in_2(in_4), .out_4(out_6));
  or or_3 (or_3_out, rom_1_data[4], pulse_extender_1_out_6);
  pulse_extender pulse_extender_1 (
    .in_1(rom_1_data[5]), .in_2(in_2), .out_6(pulse_extender_1_out_6));  // open: in_3, out_4, out_5
  pulse_extender pulse_extender_2 (.in_1(or_3_out), .in_2(in_2), .out_6(out_11));  // open: in_3, out_4, out_5
  or or_4 (out_8, rom_1_data[1], or_1_out);
  or or_5 (out_9, rom_1_data[2], Restart);
  or or_6 (out_7, rom_1_data[0], or_2_out);

  // Notes on the sheet:
  //   contents of rom_1 (hex, n*v repeats v):
  //   0 10 0 0 1 2 65528*0 1
  //   data input
  //   Increment
  //   Write
  //   Reset
  //   Data bus
  //   Addr Bus
endmodule

module memory_ctrl (
  input  [15:0] data_bus_in,
  input  [15:0] pk_in,
  input  [15:0] mem_in,
  input  [15:0] addr_in,
  input  [15:0] offset_in,
  input  clock,
  input  reset,
  input  [15:0] control_bus_1,
  input  [15:0] control_bus_2,
  output [15:0] data_to_mem,
  output [15:0] data_bus_out,
  output [15:0] mem_addr_out,
  output mem_write,
  output [1:0] reg_select,
  output reg_write
);

  wire and_1_out, comparator_1_eq, comparator_2_lt, eight_bit_eq_cmp_1_out_3, eight_bit_eq_cmp_2_out_3,
       eight_bit_eq_cmp_3_out_3, eight_bit_eq_cmp_4_out_3, eight_bit_eq_cmp_5_out_3,
       eight_bit_eq_cmp_6_out_3, eight_bit_eq_cmp_7_out_3, eight_bit_eq_cmp_8_out_3,
       eight_bit_eq_cmp_9_out_3, eight_bit_eq_cmp_10_out_3, eight_bit_eq_cmp_11_out_3,
       eight_bit_eq_cmp_12_out_3, eight_bit_eq_cmp_13_out_3, eight_bit_eq_cmp_14_out_3,
       eight_bit_eq_cmp_15_out_3, eight_bit_eq_cmp_16_out_3, eight_bit_eq_cmp_17_out_3,
       eight_bit_eq_cmp_18_out_3, nor_1_out, or_2_out, or_3_out, or_4_out, or_5_out, or_6_out, or_7_out,
       or_8_out, or_9_out, or_10_out, or_11_out, or_12_out, or_13_out, or_14_out, or_15_out, or_16_out,
       or_17_out, or_18_out, or_19_out, or_20_out, or_21_out, or_22_out, or_23_out, or_24_out,
       use_offset_out, write_out;
  wire [15:0] multiplexer_3_out, register_1_q, register_2_q, register_3_q, sixt_bit_adder_1_out_3;
  wire [15:2] multiplexer_1_out;

  Register #(.trigger("falling"), .width(16)) register_1 (
    .D(data_bus_in), .clk(clock), .Q(register_1_q), .clr(reset));  // open: en
  // OR_Gate or_1 has open pins: in0=control_bus_2[11:8], in1=control_bus_1[11:8], out=open
  Register #(.width(16)) register_2 (.D(addr_in), .clk(or_15_out), .Q(register_2_q), .clr(reset));  // open: en
  or or_2 (or_2_out, eight_bit_eq_cmp_1_out_3, or_3_out);
  eight_bit_eq_cmp eight_bit_eq_cmp_1 (.in_1(control_bus_1[7:0]), .in_2(8'h4), .out_3(eight_bit_eq_cmp_1_out_3));
  or or_3 (or_3_out, eight_bit_eq_cmp_2_out_3, or_4_out);
  eight_bit_eq_cmp eight_bit_eq_cmp_2 (.in_1(control_bus_1[7:0]), .in_2(8'h5), .out_3(eight_bit_eq_cmp_2_out_3));
  or or_4 (or_4_out, eight_bit_eq_cmp_3_out_3, or_5_out);
  eight_bit_eq_cmp eight_bit_eq_cmp_3 (.in_1(control_bus_1[7:0]), .in_2(8'h11), .out_3(eight_bit_eq_cmp_3_out_3));
  or or_5 (or_5_out, eight_bit_eq_cmp_4_out_3, or_6_out);
  eight_bit_eq_cmp eight_bit_eq_cmp_4 (.in_1(control_bus_1[7:0]), .in_2(8'h22), .out_3(eight_bit_eq_cmp_4_out_3));
  or or_6 (or_6_out, eight_bit_eq_cmp_5_out_3, or_7_out);
  eight_bit_eq_cmp eight_bit_eq_cmp_5 (.in_1(control_bus_1[7:0]), .in_2(8'h23), .out_3(eight_bit_eq_cmp_5_out_3));
  eight_bit_eq_cmp eight_bit_eq_cmp_6 (.in_1(control_bus_1[7:0]), .in_2(8'h25), .out_3(eight_bit_eq_cmp_6_out_3));
  eight_bit_eq_cmp eight_bit_eq_cmp_7 (.in_1(control_bus_1[7:0]), .in_2(8'h26), .out_3(eight_bit_eq_cmp_7_out_3));
  or or_7 (or_7_out, eight_bit_eq_cmp_8_out_3, or_8_out);
  or or_8 (or_8_out, or_9_out, eight_bit_eq_cmp_9_out_3);
  eight_bit_eq_cmp eight_bit_eq_cmp_8 (.in_1(control_bus_1[7:0]), .in_2(8'h27), .out_3(eight_bit_eq_cmp_8_out_3));
  eight_bit_eq_cmp eight_bit_eq_cmp_9 (.in_1(control_bus_1[7:0]), .in_2(8'h28), .out_3(eight_bit_eq_cmp_9_out_3));
  or or_9 (or_9_out, eight_bit_eq_cmp_10_out_3, or_10_out);
  eight_bit_eq_cmp eight_bit_eq_cmp_10 (.in_1(control_bus_2[7:0]), .in_2(8'h4), .out_3(eight_bit_eq_cmp_10_out_3));
  or or_10 (or_10_out, eight_bit_eq_cmp_11_out_3, or_11_out);
  eight_bit_eq_cmp eight_bit_eq_cmp_11 (.in_1(control_bus_2[7:0]), .in_2(8'h5), .out_3(eight_bit_eq_cmp_11_out_3));
  or or_11 (or_11_out, eight_bit_eq_cmp_12_out_3, or_12_out);
  eight_bit_eq_cmp eight_bit_eq_cmp_12 (.in_1(control_bus_2[7:0]), .in_2(8'h11), .out_3(eight_bit_eq_cmp_12_out_3));
  or or_12 (or_12_out, eight_bit_eq_cmp_13_out_3, or_13_out);
  eight_bit_eq_cmp eight_bit_eq_cmp_13 (.in_1(control_bus_2[7:0]), .in_2(8'h22), .out_3(eight_bit_eq_cmp_13_out_3));
  or or_13 (or_13_out, eight_bit_eq_cmp_14_out_3, or_14_out);
  eight_bit_eq_cmp eight_bit_eq_cmp_14 (.in_1(control_bus_2[7:0]), .in_2(8'h23), .out_3(eight_bit_eq_cmp_14_out_3));
  eight_bit_eq_cmp eight_bit_eq_cmp_15 (.in_1(control_bus_2[7:0]), .in_2(8'h25), .out_3(eight_bit_eq_cmp_15_out_3));
  eight_bit_eq_cmp eight_bit_eq_cmp_16 (.in_1(control_bus_2[7:0]), .in_2(8'h26), .out_3(eight_bit_eq_cmp_16_out_3));
  or or_14 (or_14_out, eight_bit_eq_cmp_17_out_3, eight_bit_eq_cmp_18_out_3);
  eight_bit_eq_cmp eight_bit_eq_cmp_17 (.in_1(control_bus_2[7:0]), .in_2(8'h27), .out_3(eight_bit_eq_cmp_17_out_3));
  eight_bit_eq_cmp eight_bit_eq_cmp_18 (.in_1(control_bus_2[7:0]), .in_2(8'h28), .out_3(eight_bit_eq_cmp_18_out_3));
  Register #(.width(16)) register_3 (.D(data_bus_in), .clk(or_15_out), .Q(register_3_q), .clr(reset));  // open: en
  Multiplexer #(.width(16)) multiplexer_1 (
    .in0(addr_in), .in1(register_2_q), .out({multiplexer_1_out, reg_select}), .sel(or_15_out));
  or or_15 (or_15_out, write_out, or_19_out);
  or write (write_out, eight_bit_eq_cmp_6_out_3, eight_bit_eq_cmp_7_out_3);
  or or_16 (or_16_out, eight_bit_eq_cmp_11_out_3, or_17_out);
  or or_17 (or_17_out, eight_bit_eq_cmp_14_out_3, or_18_out);
  or or_18 (or_18_out, eight_bit_eq_cmp_16_out_3, eight_bit_eq_cmp_18_out_3);
  or or_19 (or_19_out, eight_bit_eq_cmp_15_out_3, eight_bit_eq_cmp_16_out_3);
  Multiplexer #(.width(16)) multiplexer_2 (.in0(register_1_q), .in1(register_3_q), .out(data_to_mem), .sel(or_15_out));
  Comparator #(.mode("unsigned"), .width(16)) comparator_1 (
    .a({multiplexer_1_out, reg_select}), .b({16{1'b0}}), .eq(comparator_1_eq));  // open: gt, lt
  or use_offset (use_offset_out, eight_bit_eq_cmp_2_out_3, or_20_out);
  or or_20 (or_20_out, eight_bit_eq_cmp_5_out_3, or_21_out);
  or or_21 (or_21_out, eight_bit_eq_cmp_7_out_3, or_22_out);
  or or_22 (or_22_out, eight_bit_eq_cmp_9_out_3, or_16_out);
  sixt_bit_adder sixt_bit_adder_1 (
    .in_1({multiplexer_1_out, reg_select}), .in_2(offset_in), .out_3(sixt_bit_adder_1_out_3));  // open: out_4
  Comparator #(.mode("unsigned"), .width(16)) comparator_2 (
    .a({multiplexer_1_out, reg_select}), .b(16'hfffb), .lt(comparator_2_lt));  // open: gt, eq
  Multiplexer #(.width(16)) multiplexer_3 (
    .in0({multiplexer_1_out, reg_select}), .in1(sixt_bit_adder_1_out_3), .out(multiplexer_3_out),
    .sel(use_offset_out));
  and and_1 (and_1_out, comparator_2_lt, or_2_out);
  and and_2 (mem_write, comparator_2_lt, or_15_out);
  and and_3 (reg_write, ~comparator_2_lt, or_15_out);  // AND_Gate
  nor nor_1 (nor_1_out, and_1_out, mem_write);
  or or_23 (or_23_out, nor_1_out, ~comparator_2_lt);  // OR_Gate
  or or_24 (or_24_out, or_23_out, comparator_1_eq);
  Multiplexer #(.width(16)) multiplexer_4 (.in0(multiplexer_3_out), .in1(pk_in), .out(mem_addr_out), .sel(or_24_out));
  sixt_bit_gatekeeper sixt_bit_gatekeeper_1 (.in_1(and_1_out), .in_2(mem_in), .out_3(data_bus_out));
  // Probe on mem_addr_out
endmodule
module ALU (
  input  [15:0] control_bus,
  input  [15:0] argument1,
  input  [15:0] argument2,
  input  clock,
  input  reset,
  output [15:0] out_6,
  output out_7
);

  wire and_3_out, comparator_1_gt, comparator_1_lt, comparator_2_gt, comparator_2_lt,
       eight_bit_eq_cmp_1_out_3, eight_bit_eq_cmp_2_out_3, eight_bit_eq_cmp_3_out_3,
       eight_bit_eq_cmp_4_out_3, eight_bit_eq_cmp_5_out_3, eight_bit_eq_cmp_6_out_3,
       eight_bit_eq_cmp_7_out_3, eight_bit_eq_cmp_8_out_3, eight_bit_eq_cmp_9_out_3,
       eight_bit_eq_cmp_10_out_3, eight_bit_eq_cmp_11_out_3, eight_bit_eq_cmp_12_out_3,
       eight_bit_eq_cmp_13_out_3, eight_bit_eq_cmp_14_out_3, eight_bit_eq_cmp_15_out_3,
       eight_bit_eq_cmp_16_out_3, four_bit_eq_cmp_1_out_3, nor_1_out, or_1_out,
       sixt_bit_adder_subtractor_1_out_5, sixt_bit_comparator_1_out_3, sixt_bit_comparator_1_out_4,
       sixt_bit_eq_cmp_1_out_3;
  wire [15:0] and_2_out, multiplexer_1_out, not_1_out, not_2_out, not_3_out, or_2_out, or_3_out, or_4_out,
       or_5_out, or_6_out, or_7_out, or_8_out, or_9_out, or_10_out, or_11_out, or_12_out, or_13_out,
       or_14_out, or_15_out, or_16_out, or_17_out, or_18_out, shifter_1_out, shifter_2_out, shifter_3_out,
       sixt_bit_adder_subtractor_1_out_4, sixt_bit_decrementer_1_out_2, sixt_bit_gatekeeper_1_out_3,
       sixt_bit_gatekeeper_2_out_3, sixt_bit_gatekeeper_3_out_3, sixt_bit_gatekeeper_4_out_3,
       sixt_bit_gatekeeper_5_out_3, sixt_bit_gatekeeper_6_out_3, sixt_bit_gatekeeper_7_out_3,
       sixt_bit_gatekeeper_8_out_3, sixt_bit_gatekeeper_9_out_3, sixt_bit_gatekeeper_10_out_3,
       sixt_bit_gatekeeper_11_out_3, sixt_bit_gatekeeper_12_out_3, sixt_bit_gatekeeper_13_out_3,
       sixt_bit_gatekeeper_14_out_3, sixt_bit_gatekeeper_15_out_3, sixt_bit_gatekeeper_16_out_3,
       sixt_bit_gatekeeper_17_out_3, sixt_bit_gatekeeper_18_out_3, sixt_bit_gatekeeper_20_out_3,
       sixt_bit_gatekeeper_21_out_3, sixt_bit_incrementer_1_out_2, sixt_bit_incrementer_2_out_2,
       sixt_bit_incrementer_3_out_2, sixt_bit_multuiplier_1_out_3, xor_1_out;

  sixt_bit_eq_cmp sixt_bit_eq_cmp_1 (.in_1(16'hfffe), .in_2(control_bus), .out_3(sixt_bit_eq_cmp_1_out_3));
  four_bit_eq_cmp four_bit_eq_cmp_1 (.in_1(control_bus[7:4]), .in_2(4'b0100), .out_3(four_bit_eq_cmp_1_out_3));
  eight_bit_eq_cmp eight_bit_eq_cmp_1 (
    .in_1({4'b0000, control_bus[3:0]}), .in_2({8{1'b0}}), .out_3(eight_bit_eq_cmp_1_out_3));
  eight_bit_eq_cmp eight_bit_eq_cmp_2 (
    .in_1({4'b0000, control_bus[3:0]}), .in_2(8'h1), .out_3(eight_bit_eq_cmp_2_out_3));
  eight_bit_eq_cmp eight_bit_eq_cmp_3 (
    .in_1({4'b0000, control_bus[3:0]}), .in_2(8'h2), .out_3(eight_bit_eq_cmp_3_out_3));
  eight_bit_eq_cmp eight_bit_eq_cmp_4 (
    .in_1({4'b0000, control_bus[3:0]}), .in_2(8'h3), .out_3(eight_bit_eq_cmp_4_out_3));
  eight_bit_eq_cmp eight_bit_eq_cmp_5 (
    .in_1({4'b0000, control_bus[3:0]}), .in_2(8'h4), .out_3(eight_bit_eq_cmp_5_out_3));
  eight_bit_eq_cmp eight_bit_eq_cmp_6 (
    .in_1({4'b0000, control_bus[3:0]}), .in_2(8'h5), .out_3(eight_bit_eq_cmp_6_out_3));
  eight_bit_eq_cmp eight_bit_eq_cmp_7 (
    .in_1({4'b0000, control_bus[3:0]}), .in_2(8'h6), .out_3(eight_bit_eq_cmp_7_out_3));
  eight_bit_eq_cmp eight_bit_eq_cmp_8 (
    .in_1({4'b0000, control_bus[3:0]}), .in_2(8'h7), .out_3(eight_bit_eq_cmp_8_out_3));
  eight_bit_eq_cmp eight_bit_eq_cmp_9 (
    .in_1({4'b0000, control_bus[3:0]}), .in_2(8'h8), .out_3(eight_bit_eq_cmp_9_out_3));
  eight_bit_eq_cmp eight_bit_eq_cmp_10 (
    .in_1({4'b0000, control_bus[3:0]}), .in_2(8'h9), .out_3(eight_bit_eq_cmp_10_out_3));
  eight_bit_eq_cmp eight_bit_eq_cmp_11 (
    .in_1({4'b0000, control_bus[3:0]}), .in_2(8'ha), .out_3(eight_bit_eq_cmp_11_out_3));
  eight_bit_eq_cmp eight_bit_eq_cmp_12 (
    .in_1({4'b0000, control_bus[3:0]}), .in_2(8'hb), .out_3(eight_bit_eq_cmp_12_out_3));
  eight_bit_eq_cmp eight_bit_eq_cmp_13 (
    .in_1({4'b0000, control_bus[3:0]}), .in_2(8'hc), .out_3(eight_bit_eq_cmp_13_out_3));
  eight_bit_eq_cmp eight_bit_eq_cmp_14 (
    .in_1({4'b0000, control_bus[3:0]}), .in_2(8'hd), .out_3(eight_bit_eq_cmp_14_out_3));
  eight_bit_eq_cmp eight_bit_eq_cmp_15 (
    .in_1({4'b0000, control_bus[3:0]}), .in_2(8'he), .out_3(eight_bit_eq_cmp_15_out_3));
  eight_bit_eq_cmp eight_bit_eq_cmp_16 (
    .in_1({4'b0000, control_bus[3:0]}), .in_2(8'he), .out_3(eight_bit_eq_cmp_16_out_3));
  sixt_bit_adder_subtractor sixt_bit_adder_subtractor_1 (
    .in_3(eight_bit_eq_cmp_2_out_3), .in_1(argument1), .in_2(argument2),
    .out_5(sixt_bit_adder_subtractor_1_out_5), .out_4(sixt_bit_adder_subtractor_1_out_4));
  // Probe on argument1
  // Probe on argument2
  or or_1 (or_1_out, eight_bit_eq_cmp_2_out_3, eight_bit_eq_cmp_1_out_3);
  sixt_bit_gatekeeper sixt_bit_gatekeeper_1 (
    .in_1(or_1_out), .in_2(sixt_bit_adder_subtractor_1_out_4), .out_3(sixt_bit_gatekeeper_1_out_3));
  and and_1 (out_7, or_1_out, sixt_bit_adder_subtractor_1_out_5);
  sixt_bit_multuiplier sixt_bit_multuiplier_1 (
    .in_1(argument1), .in_2(argument2), .out_3(sixt_bit_multuiplier_1_out_3));
  sixt_bit_gatekeeper sixt_bit_gatekeeper_2 (
    .in_1(eight_bit_eq_cmp_3_out_3), .in_2(sixt_bit_multuiplier_1_out_3), .out_3(sixt_bit_gatekeeper_2_out_3));
  sixt_bit_incrementer sixt_bit_incrementer_1 (.in_1(argument1), .out_2(sixt_bit_incrementer_1_out_2));
  sixt_bit_gatekeeper sixt_bit_gatekeeper_3 (
    .in_1(eight_bit_eq_cmp_4_out_3), .in_2(sixt_bit_incrementer_1_out_2), .out_3(sixt_bit_gatekeeper_3_out_3));
  sixt_bit_decrementer sixt_bit_decrementer_1 (.in_1(argument1), .out_2(sixt_bit_decrementer_1_out_2));
  sixt_bit_gatekeeper sixt_bit_gatekeeper_4 (
    .in_1(eight_bit_eq_cmp_5_out_3), .in_2(sixt_bit_decrementer_1_out_2), .out_3(sixt_bit_gatekeeper_4_out_3));
  assign not_1_out = ~argument1;  // NOT_Gate not_1, 16 bits wide
  sixt_bit_incrementer sixt_bit_incrementer_2 (.in_1(not_1_out), .out_2(sixt_bit_incrementer_2_out_2));
  sixt_bit_gatekeeper sixt_bit_gatekeeper_5 (
    .in_1(eight_bit_eq_cmp_6_out_3), .in_2(sixt_bit_incrementer_2_out_2), .out_3(sixt_bit_gatekeeper_5_out_3));
  sixt_bit_comparator sixt_bit_comparator_1 (
    .in_1(argument1), .in_2(argument2), .out_3(sixt_bit_comparator_1_out_3),
    .out_4(sixt_bit_comparator_1_out_4));
  Comparator #(.width(16)) comparator_1 (
    .a(argument1), .b(argument2), .gt(comparator_1_gt), .lt(comparator_1_lt));  // open: eq
  Comparator #(.width(16)) comparator_2 (
    .a(argument1), .b({16{1'b0}}), .gt(comparator_2_gt), .lt(comparator_2_lt));  // open: eq
  assign and_2_out = argument1 & argument2;  // AND_Gate and_2, 16 bits wide
  sixt_bit_gatekeeper sixt_bit_gatekeeper_6 (
    .in_1(eight_bit_eq_cmp_10_out_3), .in_2(and_2_out), .out_3(sixt_bit_gatekeeper_6_out_3));
  assign or_2_out = argument1 | argument2;  // OR_Gate or_2, 16 bits wide
  sixt_bit_gatekeeper sixt_bit_gatekeeper_7 (
    .in_1(eight_bit_eq_cmp_11_out_3), .in_2(or_2_out), .out_3(sixt_bit_gatekeeper_7_out_3));
  assign xor_1_out = argument1 ^ argument2;  // XOR_Gate xor_1, 16 bits wide
  sixt_bit_gatekeeper sixt_bit_gatekeeper_8 (
    .in_1(eight_bit_eq_cmp_12_out_3), .in_2(xor_1_out), .out_3(sixt_bit_gatekeeper_8_out_3));
  assign not_2_out = ~argument2;  // NOT_Gate not_2, 16 bits wide
  sixt_bit_gatekeeper sixt_bit_gatekeeper_9 (
    .in_1(eight_bit_eq_cmp_13_out_3), .in_2(not_2_out), .out_3(sixt_bit_gatekeeper_9_out_3));
  Shifter #(.width(16)) shifter_1 (.in(argument1), .\dist (4'b0001), .out(shifter_1_out));
  sixt_bit_gatekeeper sixt_bit_gatekeeper_10 (
    .in_1(eight_bit_eq_cmp_14_out_3), .in_2(shifter_1_out), .out_3(sixt_bit_gatekeeper_10_out_3));
  Shifter #(.shift("lr"), .width(16)) shifter_2 (.in(argument1), .\dist (4'b0001), .out(shifter_2_out));
  sixt_bit_gatekeeper sixt_bit_gatekeeper_11 (
    .in_1(eight_bit_eq_cmp_15_out_3), .in_2(shifter_2_out), .out_3(sixt_bit_gatekeeper_11_out_3));
  Multiplexer #(.width(16)) multiplexer_1 (
    .in0(argument2), .in1(sixt_bit_incrementer_3_out_2), .out(multiplexer_1_out), .sel(argument2[15]));
  assign not_3_out = ~argument2;  // NOT_Gate not_3, 16 bits wide
  sixt_bit_incrementer sixt_bit_incrementer_3 (.in_1(not_3_out), .out_2(sixt_bit_incrementer_3_out_2));
  assign or_3_out = sixt_bit_gatekeeper_1_out_3 | sixt_bit_gatekeeper_2_out_3;  // OR_Gate or_3, 16 bits wide
  sixt_bit_gatekeeper sixt_bit_gatekeeper_12 (
    .in_1(sixt_bit_comparator_1_out_3), .in_2(16'h1), .out_3(sixt_bit_gatekeeper_12_out_3));
  sixt_bit_gatekeeper sixt_bit_gatekeeper_13 (
    .in_1(sixt_bit_comparator_1_out_4), .in_2({16{1'b1}}), .out_3(sixt_bit_gatekeeper_13_out_3));
  sixt_bit_gatekeeper sixt_bit_gatekeeper_14 (
    .in_1(comparator_1_gt), .in_2(16'h1), .out_3(sixt_bit_gatekeeper_14_out_3));
  sixt_bit_gatekeeper sixt_bit_gatekeeper_15 (
    .in_1(comparator_1_lt), .in_2({16{1'b1}}), .out_3(sixt_bit_gatekeeper_15_out_3));
  sixt_bit_gatekeeper sixt_bit_gatekeeper_16 (
    .in_1(comparator_2_gt), .in_2(16'h1), .out_3(sixt_bit_gatekeeper_16_out_3));
  sixt_bit_gatekeeper sixt_bit_gatekeeper_17 (
    .in_1(comparator_2_lt), .in_2({16{1'b1}}), .out_3(sixt_bit_gatekeeper_17_out_3));
  nor nor_1 (nor_1_out, multiplexer_1_out[4], multiplexer_1_out[5], multiplexer_1_out[6], multiplexer_1_out[7], multiplexer_1_out[8], multiplexer_1_out[9], multiplexer_1_out[10], multiplexer_1_out[11], multiplexer_1_out[12], multiplexer_1_out[13], multiplexer_1_out[14]);
  assign or_4_out = or_3_out | sixt_bit_gatekeeper_3_out_3;  // OR_Gate or_4, 16 bits wide
  assign or_5_out = sixt_bit_gatekeeper_12_out_3 | sixt_bit_gatekeeper_13_out_3;  // OR_Gate or_5, 16 bits wide
  sixt_bit_gatekeeper sixt_bit_gatekeeper_18 (
    .in_1(eight_bit_eq_cmp_7_out_3), .in_2(or_5_out), .out_3(sixt_bit_gatekeeper_18_out_3));
  assign or_6_out = sixt_bit_gatekeeper_14_out_3 | sixt_bit_gatekeeper_15_out_3;  // OR_Gate or_6, 16 bits wide
  sixt_bit_gatekeeper sixt_bit_gatekeeper_19 (.in_1(eight_bit_eq_cmp_8_out_3), .in_2(or_6_out));  // open: out_3
  assign or_7_out = sixt_bit_gatekeeper_16_out_3 | sixt_bit_gatekeeper_17_out_3;  // OR_Gate or_7, 16 bits wide
  sixt_bit_gatekeeper sixt_bit_gatekeeper_20 (
    .in_1(eight_bit_eq_cmp_9_out_3), .in_2(or_7_out), .out_3(sixt_bit_gatekeeper_20_out_3));
  and and_3 (and_3_out, eight_bit_eq_cmp_16_out_3, nor_1_out);
  Shifter #(.width(16)) shifter_3 (.in(argument1), .\dist (multiplexer_1_out[3:0]), .out(shifter_3_out));
  assign or_8_out = or_4_out | sixt_bit_gatekeeper_4_out_3;  // OR_Gate or_8, 16 bits wide
  sixt_bit_gatekeeper sixt_bit_gatekeeper_21 (
    .in_1(and_3_out), .in_2(shifter_3_out), .out_3(sixt_bit_gatekeeper_21_out_3));
  assign or_9_out = or_8_out | sixt_bit_gatekeeper_5_out_3;  // OR_Gate or_9, 16 bits wide
  assign or_10_out = or_9_out | sixt_bit_gatekeeper_18_out_3;  // OR_Gate or_10, 16 bits wide
  assign or_11_out = or_10_out | sixt_bit_gatekeeper_20_out_3;  // OR_Gate or_11, 16 bits wide
  assign or_12_out = or_11_out | sixt_bit_gatekeeper_6_out_3;  // OR_Gate or_12, 16 bits wide
  assign or_13_out = or_12_out | sixt_bit_gatekeeper_7_out_3;  // OR_Gate or_13, 16 bits wide
  assign or_14_out = or_13_out | sixt_bit_gatekeeper_8_out_3;  // OR_Gate or_14, 16 bits wide
  assign or_15_out = or_14_out | sixt_bit_gatekeeper_9_out_3;  // OR_Gate or_15, 16 bits wide
  assign or_16_out = or_15_out | sixt_bit_gatekeeper_10_out_3;  // OR_Gate or_16, 16 bits wide
  assign or_17_out = or_16_out | sixt_bit_gatekeeper_11_out_3;  // OR_Gate or_17, 16 bits wide
  assign or_18_out = or_17_out | sixt_bit_gatekeeper_21_out_3;  // OR_Gate or_18, 16 bits wide
  sixt_bit_gatekeeper sixt_bit_gatekeeper_22 (.in_1(four_bit_eq_cmp_1_out_3), .in_2(or_18_out), .out_3(out_6));

  // Notes on the sheet:
  //   Unsigned Cmp
  //   Signed Cmp
  //   Add
  //   Subtract
  //   Multiply
  //   Increment
  //   Decrement
  //   Negate
  //   cmp0
  //   AND
  //   OR
  //   XOR
  //   NOT
  //   <<
  //   >>
  //   Bit shift
endmodule

module ALU_control (
  input  [15:0] control_bus,
  input  clock,
  input  reset,
  output [7:0] operation,
  output enable
);

  wire falling_edge_pe_1_p4, four_bit_eq_cmp_1_out_3, or_1_out, sixt_bit_eq_cmp_1_out_3, two_ticker_1_out_4;
  wire [15:4] extra_sticky_gate_1_out_6;

  sixt_bit_eq_cmp sixt_bit_eq_cmp_1 (.in_1(16'hfffe), .in_2(control_bus), .out_3(sixt_bit_eq_cmp_1_out_3));
  four_bit_eq_cmp four_bit_eq_cmp_1 (.in_1(control_bus[7:4]), .in_2(4'b0100), .out_3(four_bit_eq_cmp_1_out_3));
  or or_1 (or_1_out, sixt_bit_eq_cmp_1_out_3, reset);
  two_ticker two_ticker_1 (
    .signal_in(four_bit_eq_cmp_1_out_3), .clock(clock), .reset(or_1_out), .out_4(two_ticker_1_out_4));
  extra_sticky_gate extra_sticky_gate_1 (
    .Reset(or_1_out), .in_1(control_bus), .Clock(clock), .Activate(two_ticker_1_out_4),
    .out_6({extra_sticky_gate_1_out_6, operation[3:0]}));  // open: out_5
  // falling_edge_PE falling_edge_pe_1: pin names not known; wires that end beside it: four_bit_eq_cmp_1_out_3, or_1_out, clock, falling_edge_pe_1_p4
  falling_edge_PE falling_edge_pe_2 (
    .clock(clock), .reset(or_1_out), .signal_in(falling_edge_pe_1_p4), .signal_out(enable));  // open: propagate_reset, propagate_clock

  assign operation[7:4] = 4'b0000;
endmodule

module pulse_extender (
  input  in_1,
  input  in_2,
  input  in_3,
  output out_4,
  output out_5,
  output out_6
);

  wire not_1_out;

  S_R_Flip_Flop s_r_ff_1 (.S(1'b0), .R(not_1_out), .clk(in_2), .Q(out_6), .reset(in_3), .preset(in_1));  // open: Qn
  not not_1 (not_1_out, in_1);

  assign out_4 = in_3;
  assign out_5 = in_2;
endmodule

module double_pulse_extender (
  input  in_1,
  input  in_2,
  input  in_3,
  output out_4,
  output out_5,
  output out_6
);

  wire not_1_out, not_2_out, s_r_ff_1_q;

  S_R_Flip_Flop s_r_ff_1 (
    .S(1'b0), .R(not_1_out), .clk(in_2), .Q(s_r_ff_1_q), .reset(in_3), .preset(in_1));  // open: Qn
  not not_1 (not_1_out, in_1);
  S_R_Flip_Flop s_r_ff_2 (.S(1'b0), .R(not_2_out), .clk(in_2), .Q(out_6), .reset(in_3), .preset(in_1));  // open: Qn
  not not_2 (not_2_out, s_r_ff_1_q);

  assign out_4 = in_3;
  assign out_5 = in_2;
endmodule

module VPE_three (
  input  in_1,
  input  [3:0] in_2,
  input  [3:0] in_3,
  input  in_4,
  output out_5
);

  wire and_5_out, and_6_out, and_7_out, and_8_out, and_9_out, and_10_out, and_11_out, and_12_out, j_k_ff_1_q,
       j_k_ff_2_q, j_k_ff_3_q, j_k_ff_4_q, or_3_out;
  wire [3:0] and_1_out, and_2_out, and_3_out, and_4_out, four_bit_incrementer_1_out_2, not_1_out, not_2_out,
       or_1_out, or_2_out;
  wire [3:3] four_bit_eq_cmp_1_out_3, four_bit_eq_cmp_2_out_3;

  four_bit_eq_cmp four_bit_eq_cmp_1 (.in_1(in_2), .in_2(4'b0000), .out_3(four_bit_eq_cmp_1_out_3[3]));
  four_bit_eq_cmp four_bit_eq_cmp_2 (.in_1(in_3), .in_2(4'b0000), .out_3(four_bit_eq_cmp_2_out_3[3]));
  assign and_1_out = 4'b0010 & {4{four_bit_eq_cmp_1_out_3[3]}};  // AND_Gate and_1, 4 bits wide
  assign or_1_out = and_1_out | and_2_out;  // OR_Gate or_1, 4 bits wide
  assign and_2_out = in_2 & ~{4{four_bit_eq_cmp_1_out_3[3]}};  // AND_Gate and_2, 4 bits wide
  assign and_3_out = or_1_out & {4{four_bit_eq_cmp_2_out_3[3]}};  // AND_Gate and_3, 4 bits wide
  assign or_2_out = and_3_out | and_4_out;  // OR_Gate or_2, 4 bits wide
  assign and_4_out = in_3 & ~{4{four_bit_eq_cmp_2_out_3[3]}};  // AND_Gate and_4, 4 bits wide
  assign not_1_out = ~or_2_out;  // NOT_Gate not_1, 4 bits wide
  assign not_2_out = ~four_bit_incrementer_1_out_2;  // NOT_Gate not_2, 4 bits wide
  four_bit_incrementer four_bit_incrementer_1 (.in_1(not_1_out), .out_2(four_bit_incrementer_1_out_2));
  and and_5 (and_5_out, not_2_out[0], in_1);
  J_K_Flip_Flop j_k_ff_1 (
    .J(or_3_out), .K(or_3_out), .clk(in_4), .Q(j_k_ff_1_q), .preset(and_5_out), .reset(and_6_out));  // open: Qn
  and and_6 (and_6_out, ~not_2_out[0], in_1);  // AND_Gate
  and and_7 (and_7_out, not_2_out[1], in_1);
  J_K_Flip_Flop j_k_ff_2 (
    .J(or_3_out), .K(or_3_out), .clk(j_k_ff_1_q), .Q(j_k_ff_2_q), .preset(and_7_out), .reset(and_8_out));  // open: Qn
  and and_8 (and_8_out, ~not_2_out[1], in_1);  // AND_Gate
  J_K_Flip_Flop j_k_ff_3 (
    .J(or_3_out), .K(or_3_out), .clk(j_k_ff_2_q), .Q(j_k_ff_3_q), .preset(and_9_out), .reset(and_10_out));  // open: Qn
  and and_9 (and_9_out, not_2_out[2], in_1);
  and and_10 (and_10_out, ~not_2_out[2], in_1);  // AND_Gate
  and and_11 (and_11_out, not_2_out[3], in_1);
  J_K_Flip_Flop j_k_ff_4 (
    .J(or_3_out), .K(or_3_out), .clk(j_k_ff_3_q), .Q(j_k_ff_4_q), .preset(and_11_out), .reset(and_12_out));  // open: Qn
  and and_12 (and_12_out, ~not_2_out[3], in_1);  // AND_Gate
  or or_3 (or_3_out, j_k_ff_4_q, j_k_ff_3_q, j_k_ff_2_q, j_k_ff_1_q);
  or or_4 (out_5, in_1, or_3_out);
endmodule

module micro_instr_passthrough (
  input  [15:0] in_1,
  output [3:0] out_2,
  output [3:0] out_3,
  output [3:0] out_4
);

  wire and_1_out, and_2_out, and_3_out, and_4_out, and_5_out, and_6_out, and_7_out, undriven, undriven_2,
       undriven_3, undriven_4, undriven_5, undriven_6, undriven_7, undriven_8;
  wire [3:0] and_29_out, and_30_out, and_31_out, and_32_out, and_33_out, and_34_out, and_35_out, and_36_out,
       and_37_out, and_38_out, and_39_out, and_40_out, and_41_out, and_42_out, and_43_out, and_44_out,
       and_45_out, and_46_out, and_47_out, and_48_out, and_49_out, or_2_out, or_3_out, or_4_out, or_5_out,
       or_6_out, or_7_out, or_10_out, or_11_out, or_12_out, or_13_out, or_14_out, or_15_out, or_16_out,
       or_17_out, or_18_out, or_19_out, or_20_out, or_21_out;
  wire [3:3] and_8_out, and_9_out, and_10_out, and_11_out, and_12_out, and_13_out, and_14_out, and_15_out,
       and_16_out, and_17_out, and_18_out, and_19_out, and_20_out, and_21_out, and_22_out, and_23_out,
       and_24_out, and_25_out, and_26_out, and_27_out, and_28_out;

  and and_1 (and_1_out, in_1[0], ~in_1[1], ~in_1[2], ~in_1[3], ~in_1[4], ~in_1[5], ~in_1[6], ~in_1[7], 1'b1, 1'b1, 1'b1, 1'b1, ~in_1[12], ~in_1[13], ~in_1[14], ~in_1[15]);  // AND_Gate
  and and_2 (and_2_out, ~in_1[0], in_1[1], ~in_1[2], ~in_1[3], ~in_1[4], ~in_1[5], ~in_1[6], ~in_1[7], 1'b1, 1'b1, 1'b1, 1'b1, ~in_1[12], ~in_1[13], ~in_1[14], ~in_1[15]);  // AND_Gate
  and and_3 (and_3_out, in_1[0], in_1[1], in_1[2], ~in_1[3], ~in_1[4], ~in_1[5], ~in_1[6], ~in_1[7], 1'b1, 1'b1, 1'b1, 1'b1, 1'b1, 1'b1, 1'b1, 1'b1);  // AND_Gate
  and and_4 (and_4_out, ~in_1[0], ~in_1[1], ~in_1[2], in_1[3], ~in_1[4], ~in_1[5], ~in_1[6], ~in_1[7], 1'b1, 1'b1, 1'b1, 1'b1, 1'b1, 1'b1, 1'b1, 1'b1);  // AND_Gate
  and and_5 (and_5_out, in_1[0], ~in_1[1], ~in_1[2], in_1[3], ~in_1[4], ~in_1[5], ~in_1[6], ~in_1[7], in_1[8], in_1[9], in_1[10], in_1[11], 1'b1, 1'b1, 1'b1, 1'b1);  // AND_Gate
  and and_6 (and_6_out, ~in_1[0], in_1[1], ~in_1[2], in_1[3], ~in_1[4], ~in_1[5], ~in_1[6], ~in_1[7], 1'b1, 1'b1, 1'b1, 1'b1, ~in_1[12], ~in_1[13], ~in_1[14], ~in_1[15]);  // AND_Gate
  and and_7 (and_7_out, in_1[0], in_1[1], ~in_1[2], in_1[3], ~in_1[4], ~in_1[5], ~in_1[6], ~in_1[7], 1'b1, 1'b1, 1'b1, 1'b1, ~in_1[12], ~in_1[13], ~in_1[14], ~in_1[15]);  // AND_Gate
  and and_8 (and_8_out[3], and_1_out, ~1'b1);  // AND_Gate
  and and_9 (and_9_out[3], and_1_out, 1'b1);
  and and_10 (and_10_out[3], and_1_out, ~1'b1);  // AND_Gate
  and and_11 (and_11_out[3], and_2_out, ~1'b1);  // AND_Gate
  and and_12 (and_12_out[3], and_2_out, 1'b1);
  and and_13 (and_13_out[3], and_2_out, ~1'b1);  // AND_Gate
  and and_14 (and_14_out[3], and_3_out, ~1'b1);  // AND_Gate
  and and_15 (and_15_out[3], and_3_out, 1'b1);
  and and_16 (and_16_out[3], and_3_out, 1'b1);
  and and_17 (and_17_out[3], and_4_out, ~1'b1);  // AND_Gate
  and and_18 (and_18_out[3], and_4_out, 1'b1);
  and and_19 (and_19_out[3], and_4_out, 1'b1);
  and and_20 (and_20_out[3], and_5_out, ~1'b1);  // AND_Gate
  and and_21 (and_21_out[3], and_5_out, ~1'b1);  // AND_Gate
  and and_22 (and_22_out[3], and_5_out, 1'b1);
  and and_23 (and_23_out[3], and_6_out, ~1'b1);  // AND_Gate
  and and_24 (and_24_out[3], and_6_out, 1'b1);
  and and_25 (and_25_out[3], and_6_out, ~1'b1);  // AND_Gate
  and and_26 (and_26_out[3], and_7_out, ~1'b1);  // AND_Gate
  and and_27 (and_27_out[3], and_7_out, 1'b1);
  and and_28 (and_28_out[3], and_7_out, ~1'b1);  // AND_Gate
  assign out_2 = and_29_out | or_2_out;  // OR_Gate or_1, 4 bits wide
  assign and_29_out = {4{and_8_out[3]}} & in_1[7:4];  // AND_Gate and_29, 4 bits wide
  assign and_30_out = {4{and_9_out[3]}} & in_1[11:8];  // AND_Gate and_30, 4 bits wide
  assign and_31_out = {4{and_10_out[3]}} & in_1[15:12];  // AND_Gate and_31, 4 bits wide
  assign or_2_out = and_32_out | or_3_out;  // OR_Gate or_2, 4 bits wide
  assign and_32_out = {4{and_11_out[3]}} & in_1[7:4];  // AND_Gate and_32, 4 bits wide
  assign and_33_out = {4{and_12_out[3]}} & in_1[11:8];  // AND_Gate and_33, 4 bits wide
  assign and_34_out = {4{and_13_out[3]}} & in_1[15:12];  // AND_Gate and_34, 4 bits wide
  assign or_3_out = and_35_out | or_4_out;  // OR_Gate or_3, 4 bits wide
  assign and_35_out = {4{and_14_out[3]}} & in_1[7:4];  // AND_Gate and_35, 4 bits wide
  assign and_36_out = {4{and_15_out[3]}} & in_1[11:8];  // AND_Gate and_36, 4 bits wide
  assign and_37_out = {4{and_16_out[3]}} & in_1[15:12];  // AND_Gate and_37, 4 bits wide
  assign or_4_out = and_38_out | or_5_out;  // OR_Gate or_4, 4 bits wide
  assign and_38_out = {4{and_17_out[3]}} & in_1[7:4];  // AND_Gate and_38, 4 bits wide
  assign and_39_out = {4{and_18_out[3]}} & in_1[11:8];  // AND_Gate and_39, 4 bits wide
  assign and_40_out = {4{and_19_out[3]}} & in_1[15:12];  // AND_Gate and_40, 4 bits wide
  assign or_5_out = and_41_out | or_6_out;  // OR_Gate or_5, 4 bits wide
  assign and_41_out = {4{and_20_out[3]}} & in_1[7:4];  // AND_Gate and_41, 4 bits wide
  assign and_42_out = {4{and_21_out[3]}} & in_1[11:8];  // AND_Gate and_42, 4 bits wide
  assign and_43_out = {4{and_22_out[3]}} & in_1[15:12];  // AND_Gate and_43, 4 bits wide
  assign or_6_out = and_44_out | or_7_out;  // OR_Gate or_6, 4 bits wide
  assign and_44_out = {4{and_23_out[3]}} & in_1[7:4];  // AND_Gate and_44, 4 bits wide
  assign and_45_out = {4{and_24_out[3]}} & in_1[11:8];  // AND_Gate and_45, 4 bits wide
  assign and_46_out = {4{and_25_out[3]}} & in_1[15:12];  // AND_Gate and_46, 4 bits wide
  assign or_7_out = and_47_out | and_48_out;  // OR_Gate or_7, 4 bits wide
  assign and_47_out = {4{and_26_out[3]}} & in_1[7:4];  // AND_Gate and_47, 4 bits wide
  assign and_48_out = {4{and_27_out[3]}} & in_1[11:8];  // AND_Gate and_48, 4 bits wide
  assign and_49_out = {4{and_28_out[3]}} & in_1[15:12];  // AND_Gate and_49, 4 bits wide
  assign out_3 = and_30_out | or_10_out;  // OR_Gate or_8, 4 bits wide
  assign out_4 = and_31_out | or_11_out;  // OR_Gate or_9, 4 bits wide
  assign or_10_out = and_33_out | or_12_out;  // OR_Gate or_10, 4 bits wide
  assign or_11_out = and_34_out | or_13_out;  // OR_Gate or_11, 4 bits wide
  assign or_12_out = and_36_out | or_14_out;  // OR_Gate or_12, 4 bits wide
  assign or_13_out = and_37_out | or_15_out;  // OR_Gate or_13, 4 bits wide
  assign or_14_out = and_39_out | or_16_out;  // OR_Gate or_14, 4 bits wide
  assign or_15_out = and_40_out | or_17_out;  // OR_Gate or_15, 4 bits wide
  assign or_16_out = and_42_out | or_18_out;  // OR_Gate or_16, 4 bits wide
  assign or_17_out = and_43_out | or_19_out;  // OR_Gate or_17, 4 bits wide
  assign or_18_out = and_45_out | or_20_out;  // OR_Gate or_18, 4 bits wide
  assign or_19_out = and_46_out | or_21_out;  // OR_Gate or_19, 4 bits wide
  assign or_20_out = and_48_out | 4'b0000;  // OR_Gate or_20, 4 bits wide
  assign or_21_out = and_49_out | 4'b0000;  // OR_Gate or_21, 4 bits wide
  // AND_Gate and_50 has open pins: in0=undriven, in1=undriven_2, out=open
  // AND_Gate and_51 has open pins: in0=undriven, in1=undriven_2, out=open
  // AND_Gate and_52 has open pins: in0=undriven, in1=undriven_2, out=open
  // AND_Gate and_53 has open pins: in0=undriven_3, in1=undriven_4, out=open
  // AND_Gate and_54 has open pins: in0=undriven_3, in1=undriven_4, out=open
  // AND_Gate and_55 has open pins: in0=undriven_3, in1=undriven_4, out=open
  // AND_Gate and_56 has open pins: in0=undriven_5, in1=undriven_6, out=open
  // AND_Gate and_57 has open pins: in0=undriven_5, in1=undriven_6, out=open
  // AND_Gate and_58 has open pins: in0=undriven_5, in1=undriven_6, out=open
  // AND_Gate and_59 has open pins: in0=undriven_7, in1=undriven_8, out=open
  // AND_Gate and_60 has open pins: in0=undriven_7, in1=undriven_8, out=open
  // AND_Gate and_61 has open pins: in0=undriven_7, in1=undriven_8, out=open
  // also tied to GND on the sheet: {and_48_out[0], and_48_out[1], and_48_out[2], and_48_out[3]}

  // Notes on the sheet:
  //   0D01
  //   0D02
  //   ND07
  //   ND08
  //   N009
  //   0D0a
  //   0D0a
endmodule

module contextualiser (
  input  [15:0] in_1,
  input  [15:0] in_2,
  input  [15:0] in_3,
  output [15:0] out_4
);

  wire and_1_out, and_2_out, and_3_out, and_4_out, and_5_out, and_6_out, and_7_out, and_8_out,
       eight_bit_eq_cmp_1_out_3, eight_bit_eq_cmp_2_out_3, four_bit_eq_cmp_1_out_3, four_bit_eq_cmp_2_out_3,
       four_bit_eq_cmp_3_out_3, four_bit_eq_cmp_4_out_3, four_bit_eq_cmp_5_out_3, four_bit_eq_cmp_6_out_3,
       not_1_out, or_1_out, or_2_out, or_3_out, or_4_out, or_6_out, or_8_out;
  wire [3:0] four_bit_g8_upwards_1_out_3, four_bit_g8_upwards_2_out_3, four_bit_g8_upwards_3_out_3,
       four_bit_g8_upwards_4_out_3, four_bit_g8_upwards_5_out_3, four_bit_g8_upwards_6_out_3,
       four_bit_g8_upwards_7_out_3, four_bit_g8_upwards_8_out_3, four_bit_g8_upwards_9_out_3,
       four_bit_g8_upwards_10_out_3, four_bit_g8_upwards_11_out_3, four_bit_g8_upwards_12_out_3,
       four_bit_g8_upwards_13_out_3, four_bit_g8_upwards_15_out_3, four_bit_g8_upwards_16_out_3;
  wire [15:0] or_5_out, or_7_out, or_9_out, sixt_bit_gatekeeper_1_out_3;
  wire [15:12] four_bit_g8_upwards_14_out_3;

  eight_bit_eq_cmp eight_bit_eq_cmp_1 (.in_1(in_2[7:0]), .in_2(8'h3), .out_3(eight_bit_eq_cmp_1_out_3));
  eight_bit_eq_cmp eight_bit_eq_cmp_2 (.in_1(in_1[7:0]), .in_2(8'h31), .out_3(eight_bit_eq_cmp_2_out_3));
  four_bit_eq_cmp four_bit_eq_cmp_1 (.in_1(in_2[11:8]), .in_2(4'b0000), .out_3(four_bit_eq_cmp_1_out_3));
  four_bit_g8_upwards four_bit_g8_upwards_1 (.in_1(and_3_out), .in_2(in_1[15:12]), .out_3(four_bit_g8_upwards_1_out_3));
  four_bit_g8_upwards four_bit_g8_upwards_2 (.in_1(and_3_out), .in_2(in_2[11:8]), .out_3(four_bit_g8_upwards_2_out_3));
  and and_1 (and_1_out, eight_bit_eq_cmp_1_out_3, and_4_out);
  and and_2 (and_2_out, ~in_2[8], ~in_2[9]);  // AND_Gate
  four_bit_eq_cmp four_bit_eq_cmp_2 (.in_1(in_1[7:4]), .in_2(4'b0001), .out_3(four_bit_eq_cmp_2_out_3));
  four_bit_eq_cmp four_bit_eq_cmp_3 (.in_1(in_2[7:4]), .in_2(4'b0001), .out_3(four_bit_eq_cmp_3_out_3));
  four_bit_eq_cmp four_bit_eq_cmp_4 (.in_1(in_2[3:0]), .in_2(4'b0011), .out_3(four_bit_eq_cmp_4_out_3));
  four_bit_eq_cmp four_bit_eq_cmp_5 (.in_1(in_2[7:4]), .in_2(4'b0000), .out_3(four_bit_eq_cmp_5_out_3));
  four_bit_eq_cmp four_bit_eq_cmp_6 (.in_1(in_2[11:8]), .in_2(4'b0100), .out_3(four_bit_eq_cmp_6_out_3));
  four_bit_g8_upwards four_bit_g8_upwards_3 (.in_1(and_3_out), .in_2(in_2[7:4]), .out_3(four_bit_g8_upwards_3_out_3));
  four_bit_g8_upwards four_bit_g8_upwards_4 (.in_1(and_3_out), .in_2(in_2[3:0]), .out_3(four_bit_g8_upwards_4_out_3));
  and and_3 (and_3_out, and_1_out, ~or_2_out);  // AND_Gate
  or or_1 (or_1_out, and_2_out, ~in_2[10]);  // OR_Gate
  and and_4 (and_4_out, or_1_out, ~in_2[11]);  // AND_Gate
  or or_2 (or_2_out, and_5_out, and_7_out);
  and and_5 (and_5_out, eight_bit_eq_cmp_1_out_3, eight_bit_eq_cmp_2_out_3, ~four_bit_eq_cmp_1_out_3);  // AND_Gate
  and and_6 (and_6_out, four_bit_eq_cmp_2_out_3, four_bit_eq_cmp_3_out_3);
  and and_7 (and_7_out, four_bit_eq_cmp_2_out_3, and_8_out);
  and and_8 (and_8_out, four_bit_eq_cmp_4_out_3, four_bit_eq_cmp_5_out_3, four_bit_eq_cmp_6_out_3);
  four_bit_g8_upwards four_bit_g8_upwards_5 (.in_1(or_4_out), .in_2(in_1[11:8]), .out_3(four_bit_g8_upwards_5_out_3));
  or or_3 (or_3_out, and_3_out, or_4_out);
  or or_4 (or_4_out, 1'b0, and_5_out);
  four_bit_g8_upwards four_bit_g8_upwards_6 (.in_1(or_4_out), .in_2(in_2[11:8]), .out_3(four_bit_g8_upwards_6_out_3));
  four_bit_g8_upwards four_bit_g8_upwards_7 (.in_1(or_4_out), .in_2(in_2[7:4]), .out_3(four_bit_g8_upwards_7_out_3));
  assign or_5_out = {four_bit_g8_upwards_1_out_3, four_bit_g8_upwards_2_out_3, four_bit_g8_upwards_3_out_3, four_bit_g8_upwards_4_out_3} | {four_bit_g8_upwards_5_out_3, four_bit_g8_upwards_6_out_3, four_bit_g8_upwards_7_out_3, four_bit_g8_upwards_8_out_3};  // OR_Gate or_5, 16 bits wide
  four_bit_g8_upwards four_bit_g8_upwards_8 (.in_1(or_4_out), .in_2(in_2[3:0]), .out_3(four_bit_g8_upwards_8_out_3));
  or or_6 (or_6_out, or_3_out, and_6_out);
  four_bit_g8_upwards four_bit_g8_upwards_9 (.in_1(and_6_out), .in_2(in_1[15:12]), .out_3(four_bit_g8_upwards_9_out_3));
  four_bit_g8_upwards four_bit_g8_upwards_10 (
    .in_1(and_6_out), .in_2(in_1[11:8]), .out_3(four_bit_g8_upwards_10_out_3));
  four_bit_g8_upwards four_bit_g8_upwards_11 (.in_1(and_6_out), .in_2(in_2[7:4]), .out_3(four_bit_g8_upwards_11_out_3));
  four_bit_g8_upwards four_bit_g8_upwards_12 (.in_1(and_6_out), .in_2(in_1[3:0]), .out_3(four_bit_g8_upwards_12_out_3));
  assign or_7_out = or_5_out | {four_bit_g8_upwards_9_out_3, four_bit_g8_upwards_10_out_3, four_bit_g8_upwards_11_out_3, four_bit_g8_upwards_12_out_3};  // OR_Gate or_7, 16 bits wide
  four_bit_g8_upwards four_bit_g8_upwards_13 (
    .in_1(and_7_out), .in_2(in_2[11:8]), .out_3(four_bit_g8_upwards_13_out_3));
  four_bit_g8_upwards four_bit_g8_upwards_14 (
    .in_1(and_7_out), .in_2(in_1[11:8]), .out_3(four_bit_g8_upwards_14_out_3));
  or or_8 (or_8_out, or_6_out, and_7_out);
  four_bit_g8_upwards four_bit_g8_upwards_15 (.in_1(and_7_out), .in_2(in_2[7:4]), .out_3(four_bit_g8_upwards_15_out_3));
  four_bit_g8_upwards four_bit_g8_upwards_16 (.in_1(and_7_out), .in_2(in_2[3:0]), .out_3(four_bit_g8_upwards_16_out_3));
  assign or_9_out = or_7_out | {four_bit_g8_upwards_14_out_3, four_bit_g8_upwards_13_out_3, four_bit_g8_upwards_15_out_3, four_bit_g8_upwards_16_out_3};  // OR_Gate or_9, 16 bits wide
  not not_1 (not_1_out, or_8_out);
  sixt_bit_gatekeeper sixt_bit_gatekeeper_1 (.in_1(not_1_out), .in_2(in_2), .out_3(sixt_bit_gatekeeper_1_out_3));
  assign out_4 = sixt_bit_gatekeeper_1_out_3 | or_9_out;  // OR_Gate or_10, 16 bits wide

  // Notes on the sheet:
  //   instruction
  //   micro-instruction
  //   tmp
endmodule

module four_bit_g8 (
  input  in_1,
  input  [3:0] in_2,
  output [3:0] out_3
);

  assign out_3 = {4{in_1}} & in_2;  // AND_Gate and_1, 4 bits wide
endmodule

module four_bit_g8_upwards (
  input  in_1,
  input  [3:0] in_2,
  output [3:0] out_3
);

  assign out_3 = {4{in_1}} & in_2;  // AND_Gate and_1, 4 bits wide
endmodule

module instruction_decoder (
  input  [15:0] in_1,
  output [15:0] out_2
);

  wire and_1_out, and_2_out, and_3_out, eight_bit_eq_cmp_1_out_3, four_bit_eq_cmp_1_out_3,
       four_bit_eq_cmp_2_out_3, four_bit_eq_cmp_3_out_3, four_bit_eq_cmp_4_out_3, four_bit_eq_cmp_5_out_3,
       four_bit_eq_cmp_6_out_3, four_bit_eq_cmp_7_out_3;
  wire [3:0] undriven, undriven_2;
  wire [15:0] or_1_out, rom_1_data, rom_2_data, rom_3_data, sixt_bit_gatekeeper_1_out_3,
       sixt_bit_gatekeeper_2_out_3, sixt_bit_gatekeeper_3_out_3, sixt_bit_gatekeeper_4_out_3;

  ROM #(.addrWidth(16), .dataWidth(16)) rom_1 (.addr(in_1), .data(rom_1_data));
  ROM #(.addrWidth(12), .dataWidth(16)) rom_2 (.addr(in_1[11:0]), .data(rom_2_data));
  ROM #(.dataWidth(16)) rom_3 (.addr(in_1[7:0]), .data(rom_3_data));
  four_bit_eq_cmp four_bit_eq_cmp_1 (.in_1(in_1[7:4]), .in_2(4'b0001), .out_3(four_bit_eq_cmp_1_out_3));
  four_bit_eq_cmp four_bit_eq_cmp_2 (.in_2(4'b0001), .out_3(four_bit_eq_cmp_2_out_3));  // open: in_1
  eight_bit_eq_cmp eight_bit_eq_cmp_1 (.in_1({undriven_2, undriven}), .in_2(8'h11), .out_3(eight_bit_eq_cmp_1_out_3));
  four_bit_eq_cmp four_bit_eq_cmp_3 (.in_2(4'b0001), .out_3(four_bit_eq_cmp_3_out_3));  // open: in_1
  four_bit_eq_cmp four_bit_eq_cmp_4 (.in_2(4'b0001), .out_3(four_bit_eq_cmp_4_out_3));  // open: in_1
  four_bit_eq_cmp four_bit_eq_cmp_5 (.in_2(4'b0001), .out_3(four_bit_eq_cmp_5_out_3));  // open: in_1
  four_bit_eq_cmp four_bit_eq_cmp_6 (.in_2(4'b0001), .out_3(four_bit_eq_cmp_6_out_3));  // open: in_1
  four_bit_eq_cmp four_bit_eq_cmp_7 (.in_1(4'b0001), .out_3(four_bit_eq_cmp_7_out_3));  // open: in_2
  sixt_bit_gatekeeper sixt_bit_gatekeeper_1 (
    .in_1(four_bit_eq_cmp_1_out_3), .in_2(16'h100), .out_3(sixt_bit_gatekeeper_1_out_3));
  and and_1 (and_1_out, four_bit_eq_cmp_2_out_3, eight_bit_eq_cmp_1_out_3);
  sixt_bit_gatekeeper sixt_bit_gatekeeper_2 (.in_1(and_1_out), .in_2(16'h2f), .out_3(sixt_bit_gatekeeper_2_out_3));
  and and_2 (and_2_out, four_bit_eq_cmp_3_out_3, four_bit_eq_cmp_4_out_3);
  sixt_bit_gatekeeper sixt_bit_gatekeeper_3 (.in_1(and_2_out), .in_2(16'h47), .out_3(sixt_bit_gatekeeper_3_out_3));
  and and_3 (and_3_out, four_bit_eq_cmp_5_out_3, four_bit_eq_cmp_6_out_3, four_bit_eq_cmp_7_out_3);
  sixt_bit_gatekeeper sixt_bit_gatekeeper_4 (.in_1(and_3_out), .in_2(16'h47), .out_3(sixt_bit_gatekeeper_4_out_3));
  assign or_1_out = sixt_bit_gatekeeper_1_out_3;  // OR_Gate or_1, 16 bits wide OR_Gate
  assign out_2 = rom_1_data | rom_2_data | rom_3_data | or_1_out;  // OR_Gate or_2, 16 bits wide

  // Notes on the sheet:
  //   contents of rom_1 (hex, n*v repeats v):
  //   2 0 0 0 16 1e 32*0 4b 55
  //   contents of rom_2 (hex, n*v repeats v):
  //   0 4 7 c 44*0 a4 8*0 b0 200*0 11 16 254*0 1b 20
  //   contents of rom_3 (hex, n*v repeats v):
  //   49*0 a0
endmodule

module instruction_decdoer_v2 (
  input  [15:0] in_1,
  input  [7:0] in_2,
  output [15:0] out_3
);

  wire comparator_1_eq, comparator_2_eq, comparator_3_eq, comparator_4_eq, comparator_5_eq, comparator_6_eq,
       comparator_7_eq, comparator_8_eq, comparator_9_eq, comparator_10_eq, comparator_11_eq,
       comparator_12_eq, comparator_13_eq;
  wire [15:0] acc1, acc2, or_1_out, or_2_out, or_3_out, or_4_out, or_5_out, or_6_out, or_8_out, or_9_out,
       or_10_out, rom_1_data, rom_2_data, rom_3_data, rom_4_data, rom_5_data, rom_7_data, rom_8_data,
       rom_9_data, rom_10_data, rom_11_data, rom_12_data, rom_13_data, sixt_bit_gatekeeper_1_out_3,
       sixt_bit_gatekeeper_2_out_3, sixt_bit_gatekeeper_3_out_3, sixt_bit_gatekeeper_4_out_3,
       sixt_bit_gatekeeper_5_out_3, sixt_bit_gatekeeper_6_out_3, sixt_bit_gatekeeper_7_out_3,
       sixt_bit_gatekeeper_8_out_3, sixt_bit_gatekeeper_9_out_3, sixt_bit_gatekeeper_10_out_3,
       sixt_bit_gatekeeper_11_out_3, sixt_bit_gatekeeper_12_out_3, sixt_bit_gatekeeper_13_out_3, undriven;

  Comparator #(.width(16)) comparator_1 (.a(in_1), .b({16{1'b0}}), .eq(comparator_1_eq));  // open: gt, lt
  ROM #(.addrWidth(2), .dataWidth(16)) rom_1 (.addr(in_2[1:0]), .data(rom_1_data));
  Comparator #(.width(16)) comparator_2 (.a(in_1), .b(16'h1), .eq(comparator_2_eq));  // open: gt, lt
  ROM #(.addrWidth(2), .dataWidth(16)) rom_2 (.addr(in_2[1:0]), .data(rom_2_data));
  Comparator #(.width(12)) comparator_3 (.a(in_1[11:0]), .b(12'h2), .eq(comparator_3_eq));  // open: gt, lt
  ROM #(.addrWidth(3), .dataWidth(16)) rom_3 (.addr(in_2[2:0]), .data(rom_3_data));
  Comparator #(.width(12)) comparator_4 (.a(in_1[11:0]), .b(12'h3), .eq(comparator_4_eq));  // open: gt, lt
  ROM #(.addrWidth(3), .dataWidth(16)) rom_4 (.addr(in_2[2:0]), .data(rom_4_data));
  Comparator #(.width(12)) comparator_5 (.a(in_1[11:0]), .b(12'h102), .eq(comparator_5_eq));  // open: gt, lt
  ROM #(.addrWidth(3), .dataWidth(16)) rom_5 (.addr(in_2[2:0]), .data(rom_5_data));
  Comparator #(.width(12)) comparator_6 (.a(in_1[11:0]), .b(12'h103), .eq(comparator_6_eq));  // open: gt, lt
  ROM #(.addrWidth(3), .dataWidth(16)) rom_6 ();  // open: addr, data
  Comparator #(.width(12)) comparator_7 (.a(in_1[11:0]), .b(12'h202), .eq(comparator_7_eq));  // open: gt, lt
  ROM #(.addrWidth(3), .dataWidth(16)) rom_7 (.addr(in_2[2:0]), .data(rom_7_data));
  Comparator #(.width(12)) comparator_8 (.a(in_1[11:0]), .b(12'h202), .eq(comparator_8_eq));  // open: gt, lt
  ROM #(.addrWidth(3), .dataWidth(16)) rom_8 (.addr(in_2[2:0]), .data(rom_8_data));
  sixt_bit_gatekeeper sixt_bit_gatekeeper_1 (
    .in_1(comparator_1_eq), .in_2(rom_1_data), .out_3(sixt_bit_gatekeeper_1_out_3));
  sixt_bit_gatekeeper sixt_bit_gatekeeper_2 (
    .in_1(comparator_2_eq), .in_2(rom_2_data), .out_3(sixt_bit_gatekeeper_2_out_3));
  sixt_bit_gatekeeper sixt_bit_gatekeeper_3 (
    .in_1(comparator_3_eq), .in_2(rom_3_data), .out_3(sixt_bit_gatekeeper_3_out_3));
  sixt_bit_gatekeeper sixt_bit_gatekeeper_4 (
    .in_1(comparator_4_eq), .in_2(rom_4_data), .out_3(sixt_bit_gatekeeper_4_out_3));
  sixt_bit_gatekeeper sixt_bit_gatekeeper_5 (
    .in_1(comparator_5_eq), .in_2(rom_5_data), .out_3(sixt_bit_gatekeeper_5_out_3));
  sixt_bit_gatekeeper sixt_bit_gatekeeper_6 (
    .in_1(comparator_6_eq), .in_2(undriven), .out_3(sixt_bit_gatekeeper_6_out_3));
  sixt_bit_gatekeeper sixt_bit_gatekeeper_7 (
    .in_1(comparator_7_eq), .in_2(rom_7_data), .out_3(sixt_bit_gatekeeper_7_out_3));
  sixt_bit_gatekeeper sixt_bit_gatekeeper_8 (
    .in_1(comparator_8_eq), .in_2(rom_8_data), .out_3(sixt_bit_gatekeeper_8_out_3));
  assign or_1_out = sixt_bit_gatekeeper_2_out_3 | sixt_bit_gatekeeper_1_out_3;  // OR_Gate or_1, 16 bits wide
  assign or_2_out = sixt_bit_gatekeeper_3_out_3 | or_1_out;  // OR_Gate or_2, 16 bits wide
  assign or_3_out = sixt_bit_gatekeeper_4_out_3 | or_2_out;  // OR_Gate or_3, 16 bits wide
  assign or_4_out = sixt_bit_gatekeeper_5_out_3 | or_3_out;  // OR_Gate or_4, 16 bits wide
  assign or_5_out = sixt_bit_gatekeeper_6_out_3 | or_4_out;  // OR_Gate or_5, 16 bits wide
  assign or_6_out = sixt_bit_gatekeeper_7_out_3 | or_5_out;  // OR_Gate or_6, 16 bits wide
  assign acc1 = sixt_bit_gatekeeper_8_out_3 | or_6_out;  // OR_Gate or_7, 16 bits wide
  Comparator #(.width(16)) comparator_9 (.a(in_1), .b(16'h4), .eq(comparator_9_eq));  // open: gt, lt
  Comparator #(.width(16)) comparator_10 (.a(in_1), .b(16'h5), .eq(comparator_10_eq));  // open: gt, lt
  Comparator #(.width(16)) comparator_11 (.a(in_1), .b(16'h6), .eq(comparator_11_eq));  // open: gt, lt
  Comparator #(.width(16)) comparator_12 (.a(in_1), .b(16'h106), .eq(comparator_12_eq));  // open: gt, lt
  ROM #(.addrWidth(4), .dataWidth(16)) rom_9 (.addr(in_2[3:0]), .data(rom_9_data));
  ROM #(.addrWidth(3), .dataWidth(16)) rom_10 (.addr(in_2[2:0]), .data(rom_10_data));
  ROM #(.addrWidth(3), .dataWidth(16)) rom_11 (.addr(in_2[2:0]), .data(rom_11_data));
  ROM #(.addrWidth(4), .dataWidth(16)) rom_12 (.addr(in_2[3:0]), .data(rom_12_data));
  sixt_bit_gatekeeper sixt_bit_gatekeeper_9 (
    .in_1(comparator_9_eq), .in_2(rom_9_data), .out_3(sixt_bit_gatekeeper_9_out_3));
  assign or_8_out = sixt_bit_gatekeeper_9_out_3 | acc1;  // OR_Gate or_8, 16 bits wide
  sixt_bit_gatekeeper sixt_bit_gatekeeper_10 (
    .in_1(comparator_10_eq), .in_2(rom_10_data), .out_3(sixt_bit_gatekeeper_10_out_3));
  assign or_9_out = sixt_bit_gatekeeper_10_out_3 | or_8_out;  // OR_Gate or_9, 16 bits wide
  sixt_bit_gatekeeper sixt_bit_gatekeeper_11 (
    .in_1(comparator_11_eq), .in_2(rom_11_data), .out_3(sixt_bit_gatekeeper_11_out_3));
  assign or_10_out = sixt_bit_gatekeeper_11_out_3 | or_9_out;  // OR_Gate or_10, 16 bits wide
  sixt_bit_gatekeeper sixt_bit_gatekeeper_12 (
    .in_1(comparator_12_eq), .in_2(rom_12_data), .out_3(sixt_bit_gatekeeper_12_out_3));
  assign acc2 = sixt_bit_gatekeeper_12_out_3 | or_10_out;  // OR_Gate or_11, 16 bits wide
  Comparator #(.width(4)) comparator_13 (.a(in_1[7:4]), .b(4'b0001), .eq(comparator_13_eq));  // open: gt, lt
  ROM #(.addrWidth(3), .dataWidth(16)) rom_13 (.addr(in_2[2:0]), .data(rom_13_data));
  sixt_bit_gatekeeper sixt_bit_gatekeeper_13 (
    .in_1(comparator_13_eq), .in_2(rom_13_data), .out_3(sixt_bit_gatekeeper_13_out_3));
  assign out_3 = sixt_bit_gatekeeper_13_out_3 | acc2;  // OR_Gate or_12, 16 bits wide

  // Other names for the same wires on the sheet: ctr[7:0] = in_2; instr[15:0] = in_1

  // Notes on the sheet:
  //   contents of rom_1 (hex, n*v repeats v):
  //   202 1 fffe fffe
  //   contents of rom_2 (hex, n*v repeats v):
  //   202 402 fffe fffe
  //   contents of rom_3 (hex, n*v repeats v):
  //   202 2402 3 602 fffe
  //   contents of rom_4 (hex, n*v repeats v):
  //   202 2402 3 702 fffe
  //   contents of rom_5 (hex, n*v repeats v):
  //   202 2402 3 802 fffe
  //   contents of rom_6 (hex, n*v repeats v):
  //   202 2402 3 902 fffe
  //   contents of rom_7 (hex, n*v repeats v):
  //   202 2402 3 a02 fffe
  //   contents of rom_8 (hex, n*v repeats v):
  //   202 2402 3 b02 fffe
  //   Call
  //   Return
  //   Push nothing
  //   Push constant
  //   contents of rom_9 (hex, n*v repeats v):
  //   202 2402 502 1602 1102 2 4 2202 402 fffe
  //   contents of rom_10 (hex, n*v repeats v):
  //   1202 402 1502 fffe
  //   contents of rom_11 (hex, n*v repeats v):
  //   1602 fffe
  //   contents of rom_12 (hex, n*v repeats v):
  //   202 2402 1602 1102 2202 25 1102 4 fffe
  //   ALU
  //   contents of rom_13 (hex, n*v repeats v):
  //   10 403 fffe
endmodule

module two_ticker (
  input  signal_in,
  input  clock,
  input  reset,
  output out_4
);

  wire and_1_out, and_2_out, and_3_out, and_4_out, and_5_out, and_6_out, and_7_out, buffer_1_out,
       buffer_2_out, buffer_3_out, buffer_4_out, buffer_5_out, buffer_6_out, buffer_7_out, buffer_8_out,
       buffer_9_out, buffer_10_out, buffer_11_out, buffer_12_out, buffer_13_out, buffer_14_out,
       buffer_15_out, buffer_16_out, buffer_17_out, buffer_18_out, clk_at_signal_q, fall_next_q, not_1_out,
       or_1_out, or_2_out, or_3_out, xor_1_out;

  not not_1 (not_1_out, clock);
  buf buffer_1 (buffer_1_out, signal_in);
  buf buffer_2 (buffer_2_out, buffer_1_out);
  buf buffer_3 (buffer_3_out, clock);
  buf buffer_4 (buffer_4_out, buffer_3_out);
  buf buffer_5 (buffer_5_out, not_1_out);
  buf buffer_6 (buffer_6_out, buffer_5_out);
  buf buffer_7 (buffer_7_out, buffer_2_out);
  and and_1 (and_1_out, ~buffer_7_out, signal_in);  // AND_Gate
  buf buffer_8 (buffer_8_out, buffer_4_out);
  and and_2 (and_2_out, ~buffer_8_out, clock);  // AND_Gate
  buf buffer_9 (buffer_9_out, buffer_6_out);
  and and_3 (and_3_out, ~buffer_9_out, not_1_out);  // AND_Gate
  or or_1 (or_1_out, and_2_out, and_3_out);
  and and_4 (and_4_out, ~out_4, and_1_out);  // AND_Gate
  xor xor_1 (xor_1_out, clock, clk_at_signal_q);
  and and_5 (and_5_out, signal_in, and_4_out);
  or or_2 (or_2_out, and_5_out, and_6_out);
  and and_6 (and_6_out, fall_next_q, out_4, or_1_out);
  or or_3 (or_3_out, and_6_out, and_4_out);
  and and_7 (and_7_out, xor_1_out, out_4);
  D_Flip_Flop signal_out (.D(or_2_out), .clk(buffer_12_out), .Q(out_4), .reset(reset));  // open: Qn, preset
  buf buffer_10 (buffer_10_out, or_3_out);
  buf buffer_11 (buffer_11_out, buffer_10_out);
  buf buffer_12 (buffer_12_out, buffer_11_out);
  D_Flip_Flop clk_at_signal (.D(clock), .clk(buffer_15_out), .Q(clk_at_signal_q), .reset(reset));  // open: Qn, preset
  buf buffer_13 (buffer_13_out, and_4_out);
  buf buffer_14 (buffer_14_out, buffer_13_out);
  buf buffer_15 (buffer_15_out, buffer_14_out);
  D_Flip_Flop fall_next (.D(and_7_out), .clk(buffer_18_out), .Q(fall_next_q), .reset(reset));  // open: Qn, preset
  buf buffer_16 (buffer_16_out, or_1_out);
  buf buffer_17 (buffer_17_out, buffer_16_out);
  buf buffer_18 (buffer_18_out, buffer_17_out);
endmodule

module special_registers (
  input  [15:0] data_bus_in,
  input  [15:0] control_bus_1,
  input  [15:0] control_bus_2,
  input  [15:0] temp_register,
  input  [15:0] sp_reset_value,
  input  clock,
  input  reset,
  output [15:0] program_kounter,
  output [15:0] data_bus_out,
  output [15:0] addr_bus_out,
  output [15:0] stack_pointer,
  output [15:0] offset_out
);

  wire and_1_out, and_2_out, and_3_out, buffer_1_out, buffer_2_out, buffer_3_out, buffer_4_out, buffer_5_out,
       buffer_6_out, buffer_7_out, d_ff_1_q, not_1_out, or_1_out, or_2_out, or_3_out, or_5_out, or_6_out,
       or_7_out, or_8_out, or_9_out, or_10_out, or_11_out, or_12_out, or_13_out, or_14_out, or_15_out,
       s_r_ff_1_qn, s_r_ff_2_q, s_r_ff_3_q, sixt_bit_eq_zero_1_out_2, special_registers_opdec_1_offs_to_addr,
       special_registers_opdec_1_offs_to_data, special_registers_opdec_1_offs_write,
       special_registers_opdec_1_pk_inc, special_registers_opdec_1_pk_to_addr,
       special_registers_opdec_1_pk_to_data, special_registers_opdec_1_pk_write,
       special_registers_opdec_1_sp_dec, special_registers_opdec_1_sp_inc,
       special_registers_opdec_1_sp_to_addr, special_registers_opdec_1_sp_to_data,
       special_registers_opdec_1_sp_write, special_registers_opdec_2_offs_to_addr,
       special_registers_opdec_2_offs_to_data, special_registers_opdec_2_offs_write,
       special_registers_opdec_2_pk_inc, special_registers_opdec_2_pk_to_addr,
       special_registers_opdec_2_pk_to_data, special_registers_opdec_2_pk_write,
       special_registers_opdec_2_sp_dec, special_registers_opdec_2_sp_inc,
       special_registers_opdec_2_sp_to_addr, special_registers_opdec_2_sp_to_data,
       special_registers_opdec_2_sp_write;
  wire [15:0] multiplexer_1_out, multiplexer_2_out, or_4_out, or_18_out, or_19_out, or_20_out, or_21_out,
       sixt_bit_gatekeeper_1_out_3, sixt_bit_gatekeeper_2_out_3, sixt_bit_gatekeeper_3_out_3,
       sixt_bit_gatekeeper_4_out_3, sixt_bit_gatekeeper_5_out_3, sixt_bit_gatekeeper_6_out_3,
       special_registers_opdec_1_data_to_pk, special_registers_opdec_2_data_to_pk;

  Pull_Resistor pull_resistor_1 (.node(sp_reset_value));
  S_R_Flip_Flop s_r_ff_1 (.Qn(s_r_ff_1_qn), .preset(clock));  // open: S, R, clk, Q, reset
  Multiplexer #(.width(16)) multiplexer_1 (
    .in0(16'hff00), .in1(sp_reset_value), .out(multiplexer_1_out), .sel(not_1_out));
  not not_1 (not_1_out, sixt_bit_eq_zero_1_out_2);
  sixt_bit_eq_zero sixt_bit_eq_zero_1 (.in_1(sp_reset_value), .out_2(sixt_bit_eq_zero_1_out_2));
  or or_1 (or_1_out, s_r_ff_1_qn, reset);
  buf buffer_1 (buffer_1_out, clock);
  buf buffer_2 (buffer_2_out, buffer_1_out);
  buf buffer_3 (buffer_3_out, buffer_2_out);
  buf buffer_4 (buffer_4_out, buffer_3_out);
  S_R_Flip_Flop s_r_ff_2 (.Q(s_r_ff_2_q), .reset(and_1_out), .preset(or_1_out));  // open: S, R, clk, Qn
  and and_1 (and_1_out, ~s_r_ff_3_q, buffer_7_out, s_r_ff_2_q);  // AND_Gate
  special_registers_opdec special_registers_opdec_1 (
    .temp_in(temp_register), .control(control_bus_2), .data_in(data_bus_in),
    .pk_to_data(special_registers_opdec_1_pk_to_data), .pk_to_addr(special_registers_opdec_1_pk_to_addr),
    .data_to_pk(special_registers_opdec_1_data_to_pk), .pk_inc(special_registers_opdec_1_pk_inc),
    .pk_write(special_registers_opdec_1_pk_write), .sp_to_data(special_registers_opdec_1_sp_to_data),
    .sp_to_addr(special_registers_opdec_1_sp_to_addr), .sp_write(special_registers_opdec_1_sp_write),
    .sp_inc(special_registers_opdec_1_sp_inc), .sp_dec(special_registers_opdec_1_sp_dec),
    .offs_to_data(special_registers_opdec_1_offs_to_data),
    .offs_to_addr(special_registers_opdec_1_offs_to_addr), .offs_write(special_registers_opdec_1_offs_write));
  Multiplexer #(.width(16)) multiplexer_2 (
    .in0(data_bus_in), .in1(multiplexer_1_out), .out(multiplexer_2_out), .sel(s_r_ff_2_q));
  and and_2 (and_2_out, clock, ~buffer_4_out);  // AND_Gate
  D_Flip_Flop d_ff_1 (.D(clock), .clk(s_r_ff_2_q), .Q(d_ff_1_q), .reset(and_2_out));  // open: Qn, preset
  buf buffer_5 (buffer_5_out, and_2_out);
  buf buffer_6 (buffer_6_out, buffer_5_out);
  buf buffer_7 (buffer_7_out, buffer_6_out);
  special_registers_opdec special_registers_opdec_2 (
    .temp_in(temp_register), .control(control_bus_1), .data_in(data_bus_in),
    .pk_to_data(special_registers_opdec_2_pk_to_data), .pk_to_addr(special_registers_opdec_2_pk_to_addr),
    .data_to_pk(special_registers_opdec_2_data_to_pk), .pk_inc(special_registers_opdec_2_pk_inc),
    .pk_write(special_registers_opdec_2_pk_write), .sp_to_data(special_registers_opdec_2_sp_to_data),
    .sp_to_addr(special_registers_opdec_2_sp_to_addr), .sp_write(special_registers_opdec_2_sp_write),
    .sp_inc(special_registers_opdec_2_sp_inc), .sp_dec(special_registers_opdec_2_sp_dec),
    .offs_to_data(special_registers_opdec_2_offs_to_data),
    .offs_to_addr(special_registers_opdec_2_offs_to_addr), .offs_write(special_registers_opdec_2_offs_write));
  and and_3 (and_3_out, ~s_r_ff_3_q, d_ff_1_q);  // AND_Gate
  S_R_Flip_Flop s_r_ff_3 (.Q(s_r_ff_3_q), .reset(and_2_out), .preset(and_3_out));  // open: S, R, clk, Qn
  or or_2 (or_2_out, special_registers_opdec_2_pk_to_data, special_registers_opdec_1_pk_to_data);
  or or_3 (or_3_out, special_registers_opdec_2_pk_to_addr, special_registers_opdec_1_pk_to_addr);
  assign or_4_out = special_registers_opdec_2_data_to_pk | special_registers_opdec_1_data_to_pk;  // OR_Gate or_4, 16 bits wide
  or or_5 (or_5_out, special_registers_opdec_2_pk_inc, special_registers_opdec_1_pk_inc);
  or or_6 (or_6_out, special_registers_opdec_2_pk_write, special_registers_opdec_1_pk_write);
  or or_7 (or_7_out, special_registers_opdec_2_sp_to_data, special_registers_opdec_1_sp_to_data);
  or or_8 (or_8_out, special_registers_opdec_2_sp_to_addr, special_registers_opdec_1_sp_to_addr);
  or or_9 (or_9_out, special_registers_opdec_2_sp_inc, special_registers_opdec_1_sp_inc);
  or or_10 (or_10_out, special_registers_opdec_2_sp_dec, special_registers_opdec_1_sp_dec);
  or or_11 (or_11_out, special_registers_opdec_2_sp_write, special_registers_opdec_1_sp_write);
  or or_12 (or_12_out, special_registers_opdec_2_offs_to_data, special_registers_opdec_1_offs_to_data);
  or or_13 (or_13_out, special_registers_opdec_2_offs_to_addr, special_registers_opdec_1_offs_to_addr);
  or or_14 (or_14_out, special_registers_opdec_2_offs_write, special_registers_opdec_1_offs_write);
  or or_15 (or_15_out, or_11_out, s_r_ff_2_q);
  Register #(.width(16)) register_1 (.D(or_4_out), .en(or_14_out), .clk(clock), .Q(offset_out), .clr(or_1_out));
  counting_register counting_register_1 (
    .data_in(or_4_out), .increment(or_5_out), .write(or_6_out), .clk(clock), .reset(or_1_out),
    .out_7(program_kounter));  // open: decrement
  sixt_bit_gatekeeper sixt_bit_gatekeeper_1 (
    .in_1(or_2_out), .in_2(program_kounter), .out_3(sixt_bit_gatekeeper_1_out_3));
  sixt_bit_gatekeeper sixt_bit_gatekeeper_2 (
    .in_1(or_3_out), .in_2(program_kounter), .out_3(sixt_bit_gatekeeper_2_out_3));
  counting_register counting_register_2 (
    .data_in(multiplexer_2_out), .increment(or_9_out), .decrement(or_10_out), .write(or_15_out), .clk(clock),
    .out_7(stack_pointer));  // open: reset
  sixt_bit_gatekeeper sixt_bit_gatekeeper_3 (
    .in_1(or_7_out), .in_2(stack_pointer), .out_3(sixt_bit_gatekeeper_3_out_3));
  sixt_bit_gatekeeper sixt_bit_gatekeeper_4 (
    .in_1(or_8_out), .in_2(stack_pointer), .out_3(sixt_bit_gatekeeper_4_out_3));
  sixt_bit_gatekeeper sixt_bit_gatekeeper_5 (.in_1(or_13_out), .in_2(offset_out), .out_3(sixt_bit_gatekeeper_5_out_3));
  assign data_bus_out = sixt_bit_gatekeeper_1_out_3 | or_18_out;  // OR_Gate or_16, 16 bits wide
  assign addr_bus_out = sixt_bit_gatekeeper_2_out_3 | or_19_out;  // OR_Gate or_17, 16 bits wide
  assign or_18_out = sixt_bit_gatekeeper_3_out_3 | or_20_out;  // OR_Gate or_18, 16 bits wide
  assign or_19_out = sixt_bit_gatekeeper_4_out_3 | or_21_out;  // OR_Gate or_19, 16 bits wide
  assign or_20_out = sixt_bit_gatekeeper_6_out_3 | sixt_bit_gatekeeper_6_out_3;  // OR_Gate or_20, 16 bits wide
  sixt_bit_gatekeeper sixt_bit_gatekeeper_6 (.in_1(or_12_out), .in_2(offset_out), .out_3(sixt_bit_gatekeeper_6_out_3));
  assign or_21_out = sixt_bit_gatekeeper_5_out_3 | sixt_bit_gatekeeper_5_out_3;  // OR_Gate or_21, 16 bits wide
  // Probe on program_kounter
  // Probe on stack_pointer
endmodule

module special_register_opdec (
  input  [15:0] control,
  input  [3:0] id,
  output data_bus_enable,
  output addr_bus_enable,
  output write_enable,
  output [15:0] special_functions
);

  wire and_2_out, and_3_out, and_4_out, eight_bit_eq_cmp_1_out_3, eight_bit_eq_cmp_2_out_3,
       eight_bit_eq_cmp_3_out_3, eight_bit_eq_cmp_4_out_3, eight_bit_eq_cmp_5_out_3,
       eight_bit_eq_cmp_6_out_3, eight_bit_eq_cmp_7_out_3, eight_bit_eq_cmp_8_out_3,
       eight_bit_eq_cmp_9_out_3, eight_bit_eq_cmp_10_out_3, eight_bit_eq_cmp_11_out_3,
       eight_bit_eq_cmp_12_out_3, eight_bit_eq_cmp_13_out_3, eight_bit_eq_cmp_14_out_3,
       eight_bit_eq_cmp_15_out_3, eight_bit_eq_cmp_16_out_3, four_bit_eq_cmp_1_out_3, load_data_bus_out_3,
       to_addr_bus_out_3, to_data_bus_indirect_out_3, to_data_bus_indirect_w_offset_out_3, to_data_bus_out_3;

  four_bit_eq_cmp four_bit_eq_cmp_1 (.in_1(control[15:12]), .in_2(id), .out_3(four_bit_eq_cmp_1_out_3));
  eight_bit_eq_cmp to_data_bus (.in_1(control[7:0]), .in_2(8'h2), .out_3(to_data_bus_out_3));
  eight_bit_eq_cmp to_addr_bus (.in_1(control[7:0]), .in_2(8'h3), .out_3(to_addr_bus_out_3));
  eight_bit_eq_cmp to_data_bus_indirect (.in_1(control[7:0]), .in_2(8'h4), .out_3(to_data_bus_indirect_out_3));
  eight_bit_eq_cmp to_data_bus_indirect_w_offset (
    .in_1(control[7:0]), .in_2(8'h5), .out_3(to_data_bus_indirect_w_offset_out_3));
  eight_bit_eq_cmp load_data_bus (.in_1(control[7:0]), .in_2(8'h6), .out_3(load_data_bus_out_3));
  eight_bit_eq_cmp eight_bit_eq_cmp_1 (.in_1(control[7:0]), .in_2(8'h10), .out_3(eight_bit_eq_cmp_1_out_3));
  eight_bit_eq_cmp eight_bit_eq_cmp_2 (.in_1(control[7:0]), .in_2(8'h11), .out_3(eight_bit_eq_cmp_2_out_3));
  eight_bit_eq_cmp eight_bit_eq_cmp_3 (.in_1(control[7:0]), .in_2(8'h12), .out_3(eight_bit_eq_cmp_3_out_3));
  eight_bit_eq_cmp eight_bit_eq_cmp_4 (.in_1(control[7:0]), .in_2(8'h13), .out_3(eight_bit_eq_cmp_4_out_3));
  eight_bit_eq_cmp eight_bit_eq_cmp_5 (.in_1(control[7:0]), .in_2(8'h14), .out_3(eight_bit_eq_cmp_5_out_3));
  eight_bit_eq_cmp eight_bit_eq_cmp_6 (.in_1(control[7:0]), .in_2(8'h15), .out_3(eight_bit_eq_cmp_6_out_3));
  eight_bit_eq_cmp eight_bit_eq_cmp_7 (.in_1(control[7:0]), .in_2(8'h16), .out_3(eight_bit_eq_cmp_7_out_3));
  eight_bit_eq_cmp eight_bit_eq_cmp_8 (.in_1(control[7:0]), .in_2(8'h17), .out_3(eight_bit_eq_cmp_8_out_3));
  eight_bit_eq_cmp eight_bit_eq_cmp_9 (.in_1(control[7:0]), .in_2(8'h18), .out_3(eight_bit_eq_cmp_9_out_3));
  eight_bit_eq_cmp eight_bit_eq_cmp_10 (.in_1(control[7:0]), .in_2(8'h19), .out_3(eight_bit_eq_cmp_10_out_3));
  eight_bit_eq_cmp eight_bit_eq_cmp_11 (.in_1(control[7:0]), .in_2(8'h1a), .out_3(eight_bit_eq_cmp_11_out_3));
  eight_bit_eq_cmp eight_bit_eq_cmp_12 (.in_1(control[7:0]), .in_2(8'h1b), .out_3(eight_bit_eq_cmp_12_out_3));
  eight_bit_eq_cmp eight_bit_eq_cmp_13 (.in_1(control[7:0]), .in_2(8'h1c), .out_3(eight_bit_eq_cmp_13_out_3));
  eight_bit_eq_cmp eight_bit_eq_cmp_14 (.in_1(control[7:0]), .in_2(8'h1d), .out_3(eight_bit_eq_cmp_14_out_3));
  eight_bit_eq_cmp eight_bit_eq_cmp_15 (.in_1(control[7:0]), .in_2(8'h1e), .out_3(eight_bit_eq_cmp_15_out_3));
  eight_bit_eq_cmp eight_bit_eq_cmp_16 (.in_1(control[7:0]), .in_2(8'h1f), .out_3(eight_bit_eq_cmp_16_out_3));
  and and_1 (data_bus_enable, four_bit_eq_cmp_1_out_3, to_data_bus_out_3);
  and and_2 (and_2_out, four_bit_eq_cmp_1_out_3, to_addr_bus_out_3);
  and and_3 (and_3_out, four_bit_eq_cmp_1_out_3, to_data_bus_indirect_out_3);
  and and_4 (and_4_out, four_bit_eq_cmp_1_out_3, to_data_bus_indirect_w_offset_out_3);
  and and_5 (write_enable, four_bit_eq_cmp_1_out_3, load_data_bus_out_3);
  and and_6 (special_functions[0], four_bit_eq_cmp_1_out_3, eight_bit_eq_cmp_1_out_3);
  and and_7 (special_functions[1], four_bit_eq_cmp_1_out_3, eight_bit_eq_cmp_2_out_3);
  and and_8 (special_functions[2], four_bit_eq_cmp_1_out_3, eight_bit_eq_cmp_3_out_3);
  and and_9 (special_functions[3], four_bit_eq_cmp_1_out_3, eight_bit_eq_cmp_4_out_3);
  and and_10 (special_functions[4], four_bit_eq_cmp_1_out_3, eight_bit_eq_cmp_5_out_3);
  and and_11 (special_functions[5], four_bit_eq_cmp_1_out_3, eight_bit_eq_cmp_6_out_3);
  and and_12 (special_functions[6], four_bit_eq_cmp_1_out_3, eight_bit_eq_cmp_7_out_3);
  and and_13 (special_functions[7], four_bit_eq_cmp_1_out_3, eight_bit_eq_cmp_8_out_3);
  and and_14 (special_functions[8], four_bit_eq_cmp_1_out_3, eight_bit_eq_cmp_9_out_3);
  and and_15 (special_functions[9], four_bit_eq_cmp_1_out_3, eight_bit_eq_cmp_10_out_3);
  and and_16 (special_functions[10], four_bit_eq_cmp_1_out_3, eight_bit_eq_cmp_11_out_3);
  and and_17 (special_functions[11], four_bit_eq_cmp_1_out_3, eight_bit_eq_cmp_12_out_3);
  and and_18 (special_functions[12], four_bit_eq_cmp_1_out_3, eight_bit_eq_cmp_13_out_3);
  and and_19 (special_functions[13], four_bit_eq_cmp_1_out_3, eight_bit_eq_cmp_14_out_3);
  and and_20 (special_functions[14], four_bit_eq_cmp_1_out_3, eight_bit_eq_cmp_15_out_3);
  and and_21 (special_functions[15], four_bit_eq_cmp_1_out_3, eight_bit_eq_cmp_16_out_3);
  or or_1 (addr_bus_enable, and_2_out, and_3_out, and_4_out);

  // Notes on the sheet:
  //   special functions
endmodule

module special_register_dual_opdec (
  input  [15:0] control_bus_1,
  input  [15:0] control_bus_2,
  input  [3:0] id,
  output data_bus_enable,
  output addr_bus_enable,
  output write_enable,
  output [15:0] special_functions
);

  wire special_register_opdec_1_addr_bus_enable, special_register_opdec_1_data_bus_enable,
       special_register_opdec_1_write_enable, special_register_opdec_2_addr_bus_enable,
       special_register_opdec_2_data_bus_enable, special_register_opdec_2_write_enable;
  wire [15:0] special_register_opdec_1_special_functions, special_register_opdec_2_special_functions;

  special_register_opdec special_register_opdec_1 (
    .control(control_bus_1), .id(id), .data_bus_enable(special_register_opdec_1_data_bus_enable),
    .addr_bus_enable(special_register_opdec_1_addr_bus_enable),
    .write_enable(special_register_opdec_1_write_enable),
    .special_functions(special_register_opdec_1_special_functions));
  special_register_opdec special_register_opdec_2 (
    .control(control_bus_2), .id(id), .data_bus_enable(special_register_opdec_2_data_bus_enable),
    .addr_bus_enable(special_register_opdec_2_addr_bus_enable),
    .write_enable(special_register_opdec_2_write_enable),
    .special_functions(special_register_opdec_2_special_functions));
  or or_1 (data_bus_enable, special_register_opdec_2_data_bus_enable, special_register_opdec_1_data_bus_enable);
  or or_2 (addr_bus_enable, special_register_opdec_2_addr_bus_enable, special_register_opdec_1_addr_bus_enable);
  or or_3 (write_enable, special_register_opdec_2_write_enable, special_register_opdec_1_write_enable);
  assign special_functions = special_register_opdec_2_special_functions | special_register_opdec_1_special_functions;  // OR_Gate or_4, 16 bits wide
endmodule

module special_registers_opdec (
  input  [15:0] data_in,
  input  [15:0] temp_in,
  input  [15:0] control,
  output pk_to_data,
  output pk_to_addr,
  output sp_to_data,
  output [15:0] data_to_pk,
  output sp_to_addr,
  output sp_write,
  output pk_inc,
  output pk_write,
  output sp_inc,
  output sp_dec,
  output offs_to_data,
  output offs_to_addr,
  output offs_write
);

  wire and_1_out, and_2_out, and_3_out, and_4_out, and_5_out, and_6_out, and_7_out, and_8_out, and_9_out,
       and_10_out, and_11_out, and_12_out, comparator_1_eq, comparator_1_gt, comparator_1_lt, not_1_out,
       not_2_out, not_3_out, not_4_out, not_5_out, or_1_out, or_5_out,
       special_register_opdec_1_addr_bus_enable, special_register_opdec_1_write_enable;
  wire [15:0] special_register_opdec_1_special_functions;
  wire [15:2] special_register_opdec_2_special_functions;

  special_register_opdec special_register_opdec_1 (
    .control(control), .id(4'b0000), .data_bus_enable(pk_to_data),
    .addr_bus_enable(special_register_opdec_1_addr_bus_enable),
    .write_enable(special_register_opdec_1_write_enable),
    .special_functions(special_register_opdec_1_special_functions));
  special_register_opdec special_register_opdec_2 (
    .control(control), .id(4'b0001), .data_bus_enable(sp_to_data), .addr_bus_enable(sp_to_addr),
    .write_enable(sp_write), .special_functions({special_register_opdec_2_special_functions, sp_dec, sp_inc}));
  special_register_opdec special_register_opdec_3 (
    .control(control), .id(4'b0100), .data_bus_enable(offs_to_data), .addr_bus_enable(offs_to_addr),
    .write_enable(offs_write));  // open: special_functions
  or or_1 (or_1_out, special_register_opdec_1_special_functions[2], special_register_opdec_1_special_functions[3], special_register_opdec_1_special_functions[4], special_register_opdec_1_special_functions[5], special_register_opdec_1_special_functions[6], special_register_opdec_1_special_functions[7], special_register_opdec_1_special_functions[8], special_register_opdec_1_special_functions[9]);
  or or_2 (pk_to_addr, special_register_opdec_1_addr_bus_enable, special_register_opdec_1_special_functions[1]);
  Multiplexer #(.width(16)) multiplexer_1 (.in0(data_in), .in1(temp_in), .out(data_to_pk), .sel(or_1_out));
  Comparator #(.width(16)) comparator_1 (
    .a(data_in), .b({16{1'b0}}), .gt(comparator_1_gt), .eq(comparator_1_eq), .lt(comparator_1_lt));
  not not_1 (not_1_out, comparator_1_lt);
  not not_2 (not_2_out, comparator_1_gt);
  not not_3 (not_3_out, comparator_1_eq);
  not not_4 (not_4_out, not_2_out);
  not not_5 (not_5_out, not_1_out);
  and and_1 (and_1_out, special_register_opdec_1_special_functions[4], comparator_1_eq);
  and and_2 (and_2_out, special_register_opdec_1_special_functions[4], ~comparator_1_eq);  // AND_Gate
  and and_3 (and_3_out, special_register_opdec_1_special_functions[5], not_3_out);
  and and_4 (and_4_out, special_register_opdec_1_special_functions[5], ~not_3_out);  // AND_Gate
  and and_5 (and_5_out, special_register_opdec_1_special_functions[6], not_2_out);
  and and_6 (and_6_out, special_register_opdec_1_special_functions[6], ~not_2_out);  // AND_Gate
  and and_7 (and_7_out, special_register_opdec_1_special_functions[7], not_4_out);
  and and_8 (and_8_out, special_register_opdec_1_special_functions[7], ~not_4_out);  // AND_Gate
  and and_9 (and_9_out, special_register_opdec_1_special_functions[8], not_1_out);
  and and_10 (and_10_out, special_register_opdec_1_special_functions[8], ~not_1_out);  // AND_Gate
  and and_11 (and_11_out, special_register_opdec_1_special_functions[9], not_5_out);
  and and_12 (and_12_out, special_register_opdec_1_special_functions[9], ~not_5_out);  // AND_Gate
  or or_3 (pk_write, special_register_opdec_1_write_enable, special_register_opdec_1_special_functions[2], special_register_opdec_1_special_functions[3], and_1_out, and_3_out, and_5_out, and_7_out, and_9_out, and_11_out);
  or or_4 (pk_inc, special_register_opdec_1_special_functions[0], or_5_out);
  or or_5 (or_5_out, special_register_opdec_1_special_functions[1], and_2_out, and_4_out, and_6_out, and_8_out, and_10_out, and_12_out);

  // Notes on the sheet:
  //   <the combinatorial logic for conditional gotos
endmodule

module tmp_regs_unit (
  input  [15:0] data_bus_in,
  input  [15:0] control_bus_1,
  input  [15:0] control_bus_2,
  input  clock,
  input  reset,
  output [15:0] data_bus_out,
  output [15:0] addr_bus_out,
  output [15:0] out_8,
  output [15:0] to_pk,
  output [15:0] out_10
);

  wire or_1_out, or_2_out, or_3_out, special_register_dual_opdec_1_addr_bus_enable,
       special_register_dual_opdec_1_data_bus_enable, special_register_dual_opdec_1_write_enable,
       special_register_dual_opdec_2_addr_bus_enable, special_register_dual_opdec_2_data_bus_enable,
       special_register_dual_opdec_2_write_enable;
  wire [15:0] register_1_q, sixt_bit_gatekeeper_1_out_3, sixt_bit_gatekeeper_2_out_3,
       sixt_bit_gatekeeper_3_out_3, sixt_bit_gatekeeper_4_out_3, sixt_bit_gatekeeper_5_out_3,
       sixt_bit_gatekeeper_6_out_3, special_register_dual_opdec_1_special_functions,
       special_register_dual_opdec_2_special_functions, special_register_dual_opdec_3_special_functions;

  Register #(.trigger("falling"), .width(16)) register_1 (
    .D(data_bus_in), .clk(clock), .Q(register_1_q), .clr(reset));  // open: en
  special_register_dual_opdec special_register_dual_opdec_1 (
    .control_bus_2(control_bus_2), .id(4'b0010), .control_bus_1(control_bus_1),
    .data_bus_enable(special_register_dual_opdec_1_data_bus_enable),
    .addr_bus_enable(special_register_dual_opdec_1_addr_bus_enable),
    .write_enable(special_register_dual_opdec_1_write_enable),
    .special_functions(special_register_dual_opdec_1_special_functions));
  special_register_dual_opdec special_register_dual_opdec_2 (
    .control_bus_2(control_bus_2), .id(4'b0011), .control_bus_1(control_bus_1),
    .data_bus_enable(special_register_dual_opdec_2_data_bus_enable),
    .addr_bus_enable(special_register_dual_opdec_2_addr_bus_enable),
    .write_enable(special_register_dual_opdec_2_write_enable),
    .special_functions(special_register_dual_opdec_2_special_functions));
  special_register_dual_opdec special_register_dual_opdec_3 (
    .control_bus_2(control_bus_2), .id(4'b0000), .control_bus_1(control_bus_1),
    .special_functions(special_register_dual_opdec_3_special_functions));  // open: data_bus_enable, addr_bus_enable, write_enable
  Register #(.width(16)) register_2 (
    .D(register_1_q), .en(special_register_dual_opdec_1_write_enable), .clk(clock), .Q(out_8), .clr(reset));
  Register #(.width(16)) register_3 (
    .D(register_1_q), .en(special_register_dual_opdec_2_write_enable), .clk(clock), .Q(out_10), .clr(reset));
  or or_1 (or_1_out, special_register_dual_opdec_3_special_functions[2], special_register_dual_opdec_3_special_functions[4], special_register_dual_opdec_3_special_functions[5], special_register_dual_opdec_3_special_functions[6], special_register_dual_opdec_3_special_functions[7], special_register_dual_opdec_3_special_functions[8], special_register_dual_opdec_3_special_functions[9]);
  or or_2 (or_2_out, or_1_out, special_register_dual_opdec_1_special_functions[0]);
  or or_3 (or_3_out, special_register_dual_opdec_2_special_functions[0], special_register_dual_opdec_3_special_functions[3]);
  sixt_bit_gatekeeper sixt_bit_gatekeeper_1 (
    .in_1(special_register_dual_opdec_1_addr_bus_enable), .in_2(out_8), .out_3(sixt_bit_gatekeeper_1_out_3));
  sixt_bit_gatekeeper sixt_bit_gatekeeper_2 (.in_1(or_2_out), .in_2(out_8), .out_3(sixt_bit_gatekeeper_2_out_3));
  sixt_bit_gatekeeper sixt_bit_gatekeeper_3 (
    .in_1(special_register_dual_opdec_2_addr_bus_enable), .in_2(out_10), .out_3(sixt_bit_gatekeeper_3_out_3));
  sixt_bit_gatekeeper sixt_bit_gatekeeper_4 (
    .in_1(special_register_dual_opdec_1_data_bus_enable), .in_2(out_8), .out_3(sixt_bit_gatekeeper_4_out_3));
  sixt_bit_gatekeeper sixt_bit_gatekeeper_5 (
    .in_1(special_register_dual_opdec_2_data_bus_enable), .in_2(out_10), .out_3(sixt_bit_gatekeeper_5_out_3));
  sixt_bit_gatekeeper sixt_bit_gatekeeper_6 (.in_1(or_3_out), .in_2(out_10), .out_3(sixt_bit_gatekeeper_6_out_3));
  assign data_bus_out = sixt_bit_gatekeeper_4_out_3 | sixt_bit_gatekeeper_5_out_3;  // OR_Gate or_4, 16 bits wide
  assign addr_bus_out = sixt_bit_gatekeeper_1_out_3 | sixt_bit_gatekeeper_3_out_3;  // OR_Gate or_5, 16 bits wide
  assign to_pk = sixt_bit_gatekeeper_2_out_3 | sixt_bit_gatekeeper_6_out_3;  // OR_Gate or_6, 16 bits wide
endmodule

module sVPE (
  input  in_1,
  input  in_2,
  input  in_3,
  output out_4,
  output out_5,
  output out_6
);

  VPE_three vpe_three_1 (.in_3({3'b001, in_2}), .in_1(in_1), .in_4(in_3), .out_5(out_6));  // open: in_2

  assign out_4 = in_2;
  assign out_5 = in_3;
endmodule

module sad (
  input  in_1,
  input  in_2,
  output out_3
);

  wire not_1_out;

  S_R_Flip_Flop s_r_ff_1 (.S(1'b0), .R(not_1_out), .clk(in_2), .Q(out_3), .preset(in_1));  // open: reset, Qn
  not not_1 (not_1_out, in_1);
endmodule

module sticky_gate (
  input  enable,
  input  [15:0] data_in,
  input  clock,
  input  reset,
  output propagate_reset,
  output [15:0] out_6
);

  wire and_1_out, and_2_out, and_3_out, and_4_out, and_5_out, and_6_out, and_7_out, and_8_out, and_9_out,
       and_10_out, and_11_out, and_12_out, and_13_out, and_14_out, and_15_out, and_16_out, d_ff_1_q,
       d_ff_2_q, d_ff_3_q, d_ff_4_q, d_ff_5_q, d_ff_6_q, d_ff_7_q, d_ff_8_q, d_ff_9_q, d_ff_10_q, d_ff_11_q,
       d_ff_12_q, d_ff_13_q, d_ff_14_q, d_ff_15_q, d_ff_16_q, xor_1_out, xor_2_out, xor_3_out, xor_4_out,
       xor_5_out, xor_6_out, xor_7_out, xor_8_out, xor_9_out, xor_10_out, xor_11_out, xor_12_out, xor_13_out,
       xor_14_out, xor_15_out, xor_16_out;

  and and_1 (and_1_out, enable, data_in[0]);
  and and_2 (and_2_out, enable, data_in[1]);
  and and_3 (and_3_out, enable, data_in[2]);
  and and_4 (and_4_out, enable, data_in[3]);
  and and_5 (and_5_out, enable, data_in[4]);
  and and_6 (and_6_out, enable, data_in[5]);
  and and_7 (and_7_out, enable, data_in[6]);
  and and_8 (and_8_out, enable, data_in[7]);
  and and_9 (and_9_out, enable, data_in[8]);
  and and_10 (and_10_out, enable, data_in[9]);
  and and_11 (and_11_out, enable, data_in[10]);
  and and_12 (and_12_out, enable, data_in[11]);
  and and_13 (and_13_out, enable, data_in[12]);
  and and_14 (and_14_out, enable, data_in[13]);
  and and_15 (and_15_out, enable, data_in[14]);
  and and_16 (and_16_out, enable, data_in[15]);
  D_Flip_Flop #(.trigger("falling")) d_ff_1 (
    .D(and_1_out), .clk(xor_1_out), .Q(d_ff_1_q), .reset(reset));  // open: Qn, preset
  xor xor_1 (xor_1_out, clock, d_ff_1_q);
  D_Flip_Flop #(.trigger("falling")) d_ff_2 (
    .D(and_2_out), .clk(xor_2_out), .Q(d_ff_2_q), .reset(reset));  // open: Qn, preset
  xor xor_2 (xor_2_out, clock, d_ff_2_q);
  D_Flip_Flop #(.trigger("falling")) d_ff_3 (
    .D(and_3_out), .clk(xor_3_out), .Q(d_ff_3_q), .reset(reset));  // open: Qn, preset
  xor xor_3 (xor_3_out, clock, d_ff_3_q);
  D_Flip_Flop #(.trigger("falling")) d_ff_4 (
    .D(and_4_out), .clk(xor_4_out), .Q(d_ff_4_q), .reset(reset));  // open: Qn, preset
  xor xor_4 (xor_4_out, clock, d_ff_4_q);
  D_Flip_Flop #(.trigger("falling")) d_ff_5 (
    .D(and_5_out), .clk(xor_5_out), .Q(d_ff_5_q), .reset(reset));  // open: Qn, preset
  xor xor_5 (xor_5_out, clock, d_ff_5_q);
  D_Flip_Flop #(.trigger("falling")) d_ff_6 (
    .D(and_6_out), .clk(xor_6_out), .Q(d_ff_6_q), .reset(reset));  // open: Qn, preset
  xor xor_6 (xor_6_out, clock, d_ff_6_q);
  D_Flip_Flop #(.trigger("falling")) d_ff_7 (
    .D(and_7_out), .clk(xor_7_out), .Q(d_ff_7_q), .reset(reset));  // open: Qn, preset
  xor xor_7 (xor_7_out, clock, d_ff_7_q);
  D_Flip_Flop #(.trigger("falling")) d_ff_8 (
    .D(and_8_out), .clk(xor_8_out), .Q(d_ff_8_q), .reset(reset));  // open: Qn, preset
  xor xor_8 (xor_8_out, clock, d_ff_8_q);
  D_Flip_Flop #(.trigger("falling")) d_ff_9 (
    .D(and_9_out), .clk(xor_9_out), .Q(d_ff_9_q), .reset(reset));  // open: Qn, preset
  xor xor_9 (xor_9_out, clock, d_ff_9_q);
  D_Flip_Flop #(.trigger("falling")) d_ff_10 (
    .D(and_10_out), .clk(xor_10_out), .Q(d_ff_10_q), .reset(reset));  // open: Qn, preset
  xor xor_10 (xor_10_out, clock, d_ff_10_q);
  D_Flip_Flop #(.trigger("falling")) d_ff_11 (
    .D(and_11_out), .clk(xor_11_out), .Q(d_ff_11_q), .reset(reset));  // open: Qn, preset
  xor xor_11 (xor_11_out, clock, d_ff_11_q);
  D_Flip_Flop #(.trigger("falling")) d_ff_12 (
    .D(and_12_out), .clk(xor_12_out), .Q(d_ff_12_q), .reset(reset));  // open: Qn, preset
  xor xor_12 (xor_12_out, clock, d_ff_12_q);
  D_Flip_Flop #(.trigger("falling")) d_ff_13 (
    .D(and_13_out), .clk(xor_13_out), .Q(d_ff_13_q), .reset(reset));  // open: Qn, preset
  xor xor_13 (xor_13_out, clock, d_ff_13_q);
  D_Flip_Flop #(.trigger("falling")) d_ff_14 (
    .D(and_14_out), .clk(xor_14_out), .Q(d_ff_14_q), .reset(reset));  // open: Qn, preset
  xor xor_14 (xor_14_out, clock, d_ff_14_q);
  D_Flip_Flop #(.trigger("falling")) d_ff_15 (
    .D(and_15_out), .clk(xor_15_out), .Q(d_ff_15_q), .reset(reset));  // open: Qn, preset
  xor xor_15 (xor_15_out, clock, d_ff_15_q);
  D_Flip_Flop #(.trigger("falling")) d_ff_16 (
    .D(and_16_out), .clk(xor_16_out), .Q(d_ff_16_q), .reset(reset));  // open: Qn, preset
  xor xor_16 (xor_16_out, clock, d_ff_16_q);
  or or_1 (out_6[0], d_ff_1_q, and_1_out);
  or or_2 (out_6[1], d_ff_2_q, and_2_out);
  or or_3 (out_6[2], d_ff_3_q, and_3_out);
  or or_4 (out_6[3], d_ff_4_q, and_4_out);
  or or_5 (out_6[4], d_ff_5_q, and_5_out);
  or or_6 (out_6[5], d_ff_6_q, and_6_out);
  or or_7 (out_6[6], d_ff_7_q, and_7_out);
  or or_8 (out_6[7], d_ff_8_q, and_8_out);
  or or_9 (out_6[8], d_ff_9_q, and_9_out);
  or or_10 (out_6[9], d_ff_10_q, and_10_out);
  or or_11 (out_6[10], d_ff_11_q, and_11_out);
  or or_12 (out_6[11], d_ff_12_q, and_12_out);
  or or_13 (out_6[12], d_ff_13_q, and_13_out);
  or or_14 (out_6[13], d_ff_14_q, and_14_out);
  or or_15 (out_6[14], d_ff_15_q, and_15_out);
  or or_16 (out_6[15], d_ff_16_q, and_16_out);

  assign propagate_reset = reset;
endmodule

module extra_sticky_gate (
  input  [15:0] in_1,
  input  Clock,
  input  Activate,
  input  Reset,
  output out_5,
  output [15:0] out_6
);

  wire and_1_out, and_2_out, and_3_out, and_4_out, and_5_out, and_6_out, and_7_out, and_8_out, and_9_out,
       and_10_out, and_11_out, and_12_out, and_13_out, and_14_out, and_15_out, and_16_out, or_1_out,
       or_2_out, or_3_out, or_4_out, or_5_out, or_6_out, or_7_out, or_8_out, or_9_out, or_10_out, or_11_out,
       or_12_out, or_13_out, or_14_out, or_15_out, or_16_out, s_r_ff_1_q, s_r_ff_2_q, s_r_ff_3_q, s_r_ff_4_q,
       s_r_ff_5_q, s_r_ff_6_q, s_r_ff_7_q, s_r_ff_8_q, s_r_ff_9_q, s_r_ff_10_q, s_r_ff_11_q, s_r_ff_12_q,
       s_r_ff_13_q, s_r_ff_14_q, s_r_ff_15_q, s_r_ff_16_q, s_r_ff_17_q, s_r_ff_18_q, s_r_ff_19_q,
       s_r_ff_20_q, s_r_ff_21_q, s_r_ff_22_q, s_r_ff_23_q, s_r_ff_24_q, s_r_ff_25_q, s_r_ff_26_q,
       s_r_ff_27_q, s_r_ff_28_q, s_r_ff_29_q, s_r_ff_30_q, s_r_ff_31_q, s_r_ff_32_q, s_r_ff_33_q,
       s_r_ff_34_q, s_r_ff_35_q, s_r_ff_36_q, s_r_ff_37_q, s_r_ff_38_q, s_r_ff_39_q, s_r_ff_40_q,
       s_r_ff_41_q, s_r_ff_42_q, s_r_ff_43_q, s_r_ff_44_q, s_r_ff_45_q, s_r_ff_46_q, s_r_ff_47_q,
       s_r_ff_48_q, s_r_ff_49_q, s_r_ff_50_q, s_r_ff_51_q, s_r_ff_52_q, s_r_ff_53_q, s_r_ff_54_q,
       s_r_ff_55_q, s_r_ff_56_q, s_r_ff_57_q, s_r_ff_58_q, s_r_ff_59_q, s_r_ff_60_q, s_r_ff_61_q,
       s_r_ff_62_q, s_r_ff_63_q, s_r_ff_64_q;

  S_R_Flip_Flop #(.trigger("falling")) s_r_ff_1 (
    .S(and_1_out), .R(1'b0), .clk(Clock), .Q(s_r_ff_1_q), .reset(or_1_out));  // open: Qn, preset
  and and_1 (and_1_out, Activate, in_1[0]);
  S_R_Flip_Flop #(.trigger("falling")) s_r_ff_2 (
    .S(and_2_out), .R(1'b0), .clk(Clock), .Q(s_r_ff_2_q), .reset(or_2_out));  // open: Qn, preset
  and and_2 (and_2_out, Activate, in_1[1]);
  S_R_Flip_Flop #(.trigger("falling")) s_r_ff_3 (
    .S(and_3_out), .R(1'b0), .clk(Clock), .Q(s_r_ff_3_q), .reset(or_3_out));  // open: Qn, preset
  and and_3 (and_3_out, Activate, in_1[2]);
  S_R_Flip_Flop #(.trigger("falling")) s_r_ff_4 (
    .S(and_4_out), .R(1'b0), .clk(Clock), .Q(s_r_ff_4_q), .reset(or_4_out));  // open: Qn, preset
  and and_4 (and_4_out, Activate, in_1[3]);
  S_R_Flip_Flop #(.trigger("falling")) s_r_ff_5 (
    .S(and_5_out), .R(1'b0), .clk(Clock), .Q(s_r_ff_5_q), .reset(or_5_out));  // open: Qn, preset
  and and_5 (and_5_out, Activate, in_1[4]);
  S_R_Flip_Flop #(.trigger("falling")) s_r_ff_6 (
    .S(and_6_out), .R(1'b0), .clk(Clock), .Q(s_r_ff_6_q), .reset(or_6_out));  // open: Qn, preset
  and and_6 (and_6_out, Activate, in_1[5]);
  S_R_Flip_Flop #(.trigger("falling")) s_r_ff_7 (
    .S(and_7_out), .R(1'b0), .clk(Clock), .Q(s_r_ff_7_q), .reset(or_7_out));  // open: Qn, preset
  and and_7 (and_7_out, Activate, in_1[6]);
  S_R_Flip_Flop #(.trigger("falling")) s_r_ff_8 (
    .S(and_8_out), .R(1'b0), .clk(Clock), .Q(s_r_ff_8_q), .reset(or_8_out));  // open: Qn, preset
  and and_8 (and_8_out, Activate, in_1[7]);
  S_R_Flip_Flop #(.trigger("falling")) s_r_ff_9 (
    .S(and_9_out), .R(1'b0), .clk(Clock), .Q(s_r_ff_9_q), .reset(or_9_out));  // open: Qn, preset
  and and_9 (and_9_out, Activate, in_1[8]);
  S_R_Flip_Flop #(.trigger("falling")) s_r_ff_10 (
    .S(and_10_out), .R(1'b0), .clk(Clock), .Q(s_r_ff_10_q), .reset(or_10_out));  // open: Qn, preset
  and and_10 (and_10_out, Activate, in_1[9]);
  S_R_Flip_Flop #(.trigger("falling")) s_r_ff_11 (
    .S(and_11_out), .R(1'b0), .clk(Clock), .Q(s_r_ff_11_q), .reset(or_11_out));  // open: Qn, preset
  and and_11 (and_11_out, Activate, in_1[10]);
  S_R_Flip_Flop #(.trigger("falling")) s_r_ff_12 (
    .S(and_12_out), .R(1'b0), .clk(Clock), .Q(s_r_ff_12_q), .reset(or_12_out));  // open: Qn, preset
  and and_12 (and_12_out, Activate, in_1[11]);
  S_R_Flip_Flop #(.trigger("falling")) s_r_ff_13 (
    .S(and_13_out), .R(1'b0), .clk(Clock), .Q(s_r_ff_13_q), .reset(or_13_out));  // open: Qn, preset
  and and_13 (and_13_out, Activate, in_1[12]);
  S_R_Flip_Flop #(.trigger("falling")) s_r_ff_14 (
    .S(and_14_out), .R(1'b0), .clk(Clock), .Q(s_r_ff_14_q), .reset(or_14_out));  // open: Qn, preset
  and and_14 (and_14_out, Activate, in_1[13]);
  S_R_Flip_Flop #(.trigger("falling")) s_r_ff_15 (
    .S(and_15_out), .R(1'b0), .clk(Clock), .Q(s_r_ff_15_q), .reset(or_15_out));  // open: Qn, preset
  and and_15 (and_15_out, Activate, in_1[14]);
  S_R_Flip_Flop #(.trigger("falling")) s_r_ff_16 (
    .S(and_16_out), .R(1'b0), .clk(Clock), .Q(s_r_ff_16_q), .reset(or_16_out));  // open: Qn, preset
  and and_16 (and_16_out, Activate, in_1[15]);
  S_R_Flip_Flop s_r_ff_17 (
    .S(s_r_ff_1_q), .R(1'b0), .clk(Clock), .Q(s_r_ff_17_q), .reset(or_1_out));  // open: Qn, preset
  S_R_Flip_Flop s_r_ff_18 (
    .S(s_r_ff_2_q), .R(1'b0), .clk(Clock), .Q(s_r_ff_18_q), .reset(or_2_out));  // open: Qn, preset
  S_R_Flip_Flop s_r_ff_19 (
    .S(s_r_ff_3_q), .R(1'b0), .clk(Clock), .Q(s_r_ff_19_q), .reset(or_3_out));  // open: Qn, preset
  S_R_Flip_Flop s_r_ff_20 (
    .S(s_r_ff_4_q), .R(1'b0), .clk(Clock), .Q(s_r_ff_20_q), .reset(or_4_out));  // open: Qn, preset
  S_R_Flip_Flop s_r_ff_21 (
    .S(s_r_ff_5_q), .R(1'b0), .clk(Clock), .Q(s_r_ff_21_q), .reset(or_5_out));  // open: Qn, preset
  S_R_Flip_Flop s_r_ff_22 (
    .S(s_r_ff_6_q), .R(1'b0), .clk(Clock), .Q(s_r_ff_22_q), .reset(or_6_out));  // open: Qn, preset
  S_R_Flip_Flop s_r_ff_23 (
    .S(s_r_ff_7_q), .R(1'b0), .clk(Clock), .Q(s_r_ff_23_q), .reset(or_7_out));  // open: Qn, preset
  S_R_Flip_Flop s_r_ff_24 (
    .S(s_r_ff_8_q), .R(1'b0), .clk(Clock), .Q(s_r_ff_24_q), .reset(or_8_out));  // open: Qn, preset
  S_R_Flip_Flop s_r_ff_25 (
    .S(s_r_ff_9_q), .R(1'b0), .clk(Clock), .Q(s_r_ff_25_q), .reset(or_9_out));  // open: Qn, preset
  S_R_Flip_Flop s_r_ff_26 (
    .S(s_r_ff_10_q), .R(1'b0), .clk(Clock), .Q(s_r_ff_26_q), .reset(or_10_out));  // open: Qn, preset
  S_R_Flip_Flop s_r_ff_27 (
    .S(s_r_ff_11_q), .R(1'b0), .clk(Clock), .Q(s_r_ff_27_q), .reset(or_11_out));  // open: Qn, preset
  S_R_Flip_Flop s_r_ff_28 (
    .S(s_r_ff_12_q), .R(1'b0), .clk(Clock), .Q(s_r_ff_28_q), .reset(or_12_out));  // open: Qn, preset
  S_R_Flip_Flop s_r_ff_29 (
    .S(s_r_ff_13_q), .R(1'b0), .clk(Clock), .Q(s_r_ff_29_q), .reset(or_13_out));  // open: Qn, preset
  S_R_Flip_Flop s_r_ff_30 (
    .S(s_r_ff_14_q), .R(1'b0), .clk(Clock), .Q(s_r_ff_30_q), .reset(or_14_out));  // open: Qn, preset
  S_R_Flip_Flop s_r_ff_31 (
    .S(s_r_ff_15_q), .R(1'b0), .clk(Clock), .Q(s_r_ff_31_q), .reset(or_15_out));  // open: Qn, preset
  S_R_Flip_Flop s_r_ff_32 (
    .S(s_r_ff_16_q), .R(1'b0), .clk(Clock), .Q(s_r_ff_32_q), .reset(or_16_out));  // open: Qn, preset
  S_R_Flip_Flop s_r_ff_33 (
    .S(s_r_ff_17_q), .R(1'b0), .clk(Clock), .Q(s_r_ff_33_q), .reset(or_1_out));  // open: Qn, preset
  S_R_Flip_Flop s_r_ff_34 (
    .S(s_r_ff_18_q), .R(1'b0), .clk(Clock), .Q(s_r_ff_34_q), .reset(or_2_out));  // open: Qn, preset
  S_R_Flip_Flop s_r_ff_35 (
    .S(s_r_ff_19_q), .R(1'b0), .clk(Clock), .Q(s_r_ff_35_q), .reset(or_3_out));  // open: Qn, preset
  S_R_Flip_Flop s_r_ff_36 (
    .S(s_r_ff_20_q), .R(1'b0), .clk(Clock), .Q(s_r_ff_36_q), .reset(or_4_out));  // open: Qn, preset
  S_R_Flip_Flop s_r_ff_37 (
    .S(s_r_ff_21_q), .R(1'b0), .clk(Clock), .Q(s_r_ff_37_q), .reset(or_5_out));  // open: Qn, preset
  S_R_Flip_Flop s_r_ff_38 (
    .S(s_r_ff_22_q), .R(1'b0), .clk(Clock), .Q(s_r_ff_38_q), .reset(or_6_out));  // open: Qn, preset
  S_R_Flip_Flop s_r_ff_39 (
    .S(s_r_ff_23_q), .R(1'b0), .clk(Clock), .Q(s_r_ff_39_q), .reset(or_7_out));  // open: Qn, preset
  S_R_Flip_Flop s_r_ff_40 (
    .S(s_r_ff_24_q), .R(1'b0), .clk(Clock), .Q(s_r_ff_40_q), .reset(or_8_out));  // open: Qn, preset
  S_R_Flip_Flop s_r_ff_41 (
    .S(s_r_ff_25_q), .R(1'b0), .clk(Clock), .Q(s_r_ff_41_q), .reset(or_9_out));  // open: Qn, preset
  S_R_Flip_Flop s_r_ff_42 (
    .S(s_r_ff_26_q), .R(1'b0), .clk(Clock), .Q(s_r_ff_42_q), .reset(or_10_out));  // open: Qn, preset
  S_R_Flip_Flop s_r_ff_43 (
    .S(s_r_ff_27_q), .R(1'b0), .clk(Clock), .Q(s_r_ff_43_q), .reset(or_11_out));  // open: Qn, preset
  S_R_Flip_Flop s_r_ff_44 (
    .S(s_r_ff_28_q), .R(1'b0), .clk(Clock), .Q(s_r_ff_44_q), .reset(or_12_out));  // open: Qn, preset
  S_R_Flip_Flop s_r_ff_45 (
    .S(s_r_ff_29_q), .R(1'b0), .clk(Clock), .Q(s_r_ff_45_q), .reset(or_13_out));  // open: Qn, preset
  S_R_Flip_Flop s_r_ff_46 (
    .S(s_r_ff_30_q), .R(1'b0), .clk(Clock), .Q(s_r_ff_46_q), .reset(or_14_out));  // open: Qn, preset
  S_R_Flip_Flop s_r_ff_47 (
    .S(s_r_ff_31_q), .R(1'b0), .clk(Clock), .Q(s_r_ff_47_q), .reset(or_15_out));  // open: Qn, preset
  S_R_Flip_Flop s_r_ff_48 (
    .S(s_r_ff_32_q), .R(1'b0), .clk(Clock), .Q(s_r_ff_48_q), .reset(or_16_out));  // open: Qn, preset
  S_R_Flip_Flop s_r_ff_49 (
    .S(s_r_ff_33_q), .R(1'b0), .clk(Clock), .Q(s_r_ff_49_q), .reset(or_1_out));  // open: Qn, preset
  or or_1 (or_1_out, s_r_ff_49_q, Reset);
  S_R_Flip_Flop s_r_ff_50 (
    .S(s_r_ff_34_q), .R(1'b0), .clk(Clock), .Q(s_r_ff_50_q), .reset(or_2_out));  // open: Qn, preset
  or or_2 (or_2_out, s_r_ff_50_q, Reset);
  S_R_Flip_Flop s_r_ff_51 (
    .S(s_r_ff_35_q), .R(1'b0), .clk(Clock), .Q(s_r_ff_51_q), .reset(or_3_out));  // open: Qn, preset
  or or_3 (or_3_out, s_r_ff_51_q, Reset);
  S_R_Flip_Flop s_r_ff_52 (
    .S(s_r_ff_36_q), .R(1'b0), .clk(Clock), .Q(s_r_ff_52_q), .reset(or_4_out));  // open: Qn, preset
  or or_4 (or_4_out, s_r_ff_52_q, Reset);
  S_R_Flip_Flop s_r_ff_53 (
    .S(s_r_ff_37_q), .R(1'b0), .clk(Clock), .Q(s_r_ff_53_q), .reset(or_5_out));  // open: Qn, preset
  or or_5 (or_5_out, s_r_ff_53_q, Reset);
  S_R_Flip_Flop s_r_ff_54 (
    .S(s_r_ff_38_q), .R(1'b0), .clk(Clock), .Q(s_r_ff_54_q), .reset(or_6_out));  // open: Qn, preset
  or or_6 (or_6_out, s_r_ff_54_q, Reset);
  S_R_Flip_Flop s_r_ff_55 (
    .S(s_r_ff_39_q), .R(1'b0), .clk(Clock), .Q(s_r_ff_55_q), .reset(or_7_out));  // open: Qn, preset
  or or_7 (or_7_out, s_r_ff_55_q, Reset);
  S_R_Flip_Flop s_r_ff_56 (
    .S(s_r_ff_40_q), .R(1'b0), .clk(Clock), .Q(s_r_ff_56_q), .reset(or_8_out));  // open: Qn, preset
  or or_8 (or_8_out, s_r_ff_56_q, Reset);
  S_R_Flip_Flop s_r_ff_57 (
    .S(s_r_ff_41_q), .R(1'b0), .clk(Clock), .Q(s_r_ff_57_q), .reset(or_9_out));  // open: Qn, preset
  or or_9 (or_9_out, s_r_ff_57_q, Reset);
  S_R_Flip_Flop s_r_ff_58 (
    .S(s_r_ff_42_q), .R(1'b0), .clk(Clock), .Q(s_r_ff_58_q), .reset(or_10_out));  // open: Qn, preset
  or or_10 (or_10_out, s_r_ff_58_q, Reset);
  S_R_Flip_Flop s_r_ff_59 (
    .S(s_r_ff_43_q), .R(1'b0), .clk(Clock), .Q(s_r_ff_59_q), .reset(or_11_out));  // open: Qn, preset
  or or_11 (or_11_out, s_r_ff_59_q, Reset);
  S_R_Flip_Flop s_r_ff_60 (
    .S(s_r_ff_44_q), .R(1'b0), .clk(Clock), .Q(s_r_ff_60_q), .reset(or_12_out));  // open: Qn, preset
  or or_12 (or_12_out, s_r_ff_60_q, Reset);
  S_R_Flip_Flop s_r_ff_61 (
    .S(s_r_ff_45_q), .R(1'b0), .clk(Clock), .Q(s_r_ff_61_q), .reset(or_13_out));  // open: Qn, preset
  or or_13 (or_13_out, s_r_ff_61_q, Reset);
  S_R_Flip_Flop s_r_ff_62 (
    .S(s_r_ff_46_q), .R(1'b0), .clk(Clock), .Q(s_r_ff_62_q), .reset(or_14_out));  // open: Qn, preset
  or or_14 (or_14_out, s_r_ff_62_q, Reset);
  S_R_Flip_Flop s_r_ff_63 (
    .S(s_r_ff_47_q), .R(1'b0), .clk(Clock), .Q(s_r_ff_63_q), .reset(or_15_out));  // open: Qn, preset
  or or_15 (or_15_out, s_r_ff_63_q, Reset);
  S_R_Flip_Flop s_r_ff_64 (
    .S(s_r_ff_48_q), .R(1'b0), .clk(Clock), .Q(s_r_ff_64_q), .reset(or_16_out));  // open: Qn, preset
  or or_16 (or_16_out, s_r_ff_64_q, Reset);
  or or_17 (out_6[0], and_1_out, s_r_ff_1_q);
  or or_18 (out_6[1], and_2_out, s_r_ff_2_q);
  or or_19 (out_6[2], and_3_out, s_r_ff_3_q);
  or or_20 (out_6[3], and_4_out, s_r_ff_4_q);
  or or_21 (out_6[4], and_5_out, s_r_ff_5_q);
  or or_22 (out_6[5], and_6_out, s_r_ff_6_q);
  or or_23 (out_6[6], and_7_out, s_r_ff_7_q);
  or or_24 (out_6[7], and_8_out, s_r_ff_8_q);
  or or_25 (out_6[8], and_9_out, s_r_ff_9_q);
  or or_26 (out_6[9], and_10_out, s_r_ff_10_q);
  or or_27 (out_6[10], and_11_out, s_r_ff_11_q);
  or or_28 (out_6[11], and_12_out, s_r_ff_12_q);
  or or_29 (out_6[12], and_13_out, s_r_ff_13_q);
  or or_30 (out_6[13], and_14_out, s_r_ff_14_q);
  or or_31 (out_6[14], and_15_out, s_r_ff_15_q);
  or or_32 (out_6[15], and_16_out, s_r_ff_16_q);

  assign out_5 = Reset;
endmodule
module new_register_unit (
  input  Write,
  input  Data_out,
  input  Addr_out,
  input  ALU_Out,
  input  [3:0] in_5,
  input  [3:0] in_6,
  input  [3:0] in_7,
  input  [3:0] in_8,
  input  [15:0] in_9,
  input  in_10,
  input  in_11,
  output [15:0] out_12,
  output [15:0] out_13,
  output [15:0] out_14,
  output [15:0] out_15
);

  wire [15:0] my_register_1_out_10, my_register_1_out_11, my_register_1_out_12, my_register_1_out_13,
       my_register_1_out_14, my_register_2_out_10, my_register_2_out_11, my_register_2_out_12,
       my_register_2_out_13, my_register_2_out_14, my_register_3_out_10, my_register_3_out_11,
       my_register_3_out_12, my_register_3_out_13, my_register_3_out_14, my_register_4_out_10,
       my_register_4_out_11, my_register_4_out_12, my_register_4_out_13, my_register_4_out_14,
       my_register_5_out_10, my_register_5_out_11, my_register_5_out_12, my_register_5_out_13,
       my_register_5_out_14, my_register_6_out_10, my_register_6_out_11, my_register_6_out_12,
       my_register_6_out_13, my_register_6_out_14, my_register_7_out_10, my_register_7_out_11,
       my_register_7_out_12, my_register_7_out_13, my_register_7_out_14, my_register_8_out_10,
       my_register_8_out_11, my_register_8_out_12, my_register_8_out_13, my_register_8_out_14,
       my_register_9_out_10, my_register_9_out_11, my_register_9_out_12, my_register_9_out_13,
       my_register_9_out_14, my_register_10_out_10, my_register_10_out_11, my_register_10_out_12,
       my_register_10_out_13, my_register_10_out_14, my_register_11_out_10, my_register_11_out_11,
       my_register_11_out_12, my_register_11_out_13, my_register_11_out_14, my_register_12_out_10,
       my_register_12_out_11, my_register_12_out_12, my_register_12_out_13, my_register_12_out_14,
       my_register_13_out_10, my_register_13_out_11, my_register_13_out_12, my_register_13_out_13,
       my_register_13_out_14, my_register_14_out_10, my_register_14_out_11, my_register_14_out_12,
       my_register_14_out_13, my_register_14_out_14, my_register_15_out_10, my_register_15_out_11,
       my_register_15_out_12, my_register_15_out_13, my_register_15_out_14, my_register_16_out_10,
       my_register_16_out_11, my_register_16_out_12, my_register_16_out_13, my_register_16_out_14, or_3_out,
       or_4_out, or_5_out, or_6_out, or_7_out, or_8_out, or_9_out, or_10_out, or_11_out, or_12_out,
       or_13_out, or_14_out, or_15_out, or_16_out, or_17_out, or_18_out, or_19_out, or_20_out, or_21_out,
       or_22_out, or_23_out, or_24_out, or_25_out, or_26_out, or_27_out, or_28_out, or_29_out, or_30_out,
       or_33_out, or_34_out, or_35_out, or_36_out, or_37_out, or_38_out, or_39_out, or_40_out, or_41_out,
       or_42_out, or_43_out, or_44_out, or_45_out, or_46_out, or_47_out, or_48_out, or_49_out, or_50_out,
       or_51_out, or_52_out, or_53_out, or_54_out, or_55_out, or_56_out, or_57_out, or_58_out, or_59_out,
       or_60_out;

  // Probe on my_register_1_out_10
  // Probe on my_register_2_out_10
  // Probe on my_register_3_out_10
  // Probe on my_register_4_out_10
  // Probe on my_register_5_out_10
  // Probe on my_register_6_out_10
  // Probe on my_register_7_out_10
  // Probe on my_register_8_out_10
  // Probe on my_register_9_out_10
  // Probe on my_register_10_out_10
  // Probe on my_register_11_out_10
  // Probe on my_register_12_out_10
  // Probe on my_register_13_out_10
  // Probe on my_register_14_out_10
  // Probe on my_register_15_out_10
  // Probe on my_register_16_out_10
  assign out_12 = my_register_1_out_11 | or_3_out;  // OR_Gate or_1, 16 bits wide
  assign out_13 = my_register_1_out_12 | or_4_out;  // OR_Gate or_2, 16 bits wide
  my_register my_register_1 (
    .Clk(in_10), .Reset(in_11), .ID(4'b0000), .in_3(in_5), .in_4(in_6), .in_5(in_7), .in_6(in_8),
    .in_1(in_9), .in_2({ALU_Out, Addr_out, Data_out, Write}), .out_10(my_register_1_out_10),
    .out_11(my_register_1_out_11), .out_12(my_register_1_out_12), .out_13(my_register_1_out_13),
    .out_14(my_register_1_out_14));
  assign or_3_out = my_register_2_out_11 | or_5_out;  // OR_Gate or_3, 16 bits wide
  assign or_4_out = my_register_2_out_12 | or_6_out;  // OR_Gate or_4, 16 bits wide
  my_register my_register_2 (
    .Clk(in_10), .Reset(in_11), .ID(4'b0001), .in_3(in_5), .in_4(in_6), .in_5(in_7), .in_6(in_8),
    .in_1(in_9), .in_2({ALU_Out, Addr_out, Data_out, Write}), .out_10(my_register_2_out_10),
    .out_11(my_register_2_out_11), .out_12(my_register_2_out_12), .out_13(my_register_2_out_13),
    .out_14(my_register_2_out_14));
  assign or_5_out = my_register_3_out_11 | or_7_out;  // OR_Gate or_5, 16 bits wide
  assign or_6_out = my_register_3_out_12 | or_8_out;  // OR_Gate or_6, 16 bits wide
  my_register my_register_3 (
    .Clk(in_10), .Reset(in_11), .ID(4'b0010), .in_3(in_5), .in_4(in_6), .in_5(in_7), .in_6(in_8),
    .in_1(in_9), .in_2({ALU_Out, Addr_out, Data_out, Write}), .out_10(my_register_3_out_10),
    .out_11(my_register_3_out_11), .out_12(my_register_3_out_12), .out_13(my_register_3_out_13),
    .out_14(my_register_3_out_14));
  assign or_7_out = my_register_4_out_11 | or_9_out;  // OR_Gate or_7, 16 bits wide
  assign or_8_out = my_register_4_out_12 | or_10_out;  // OR_Gate or_8, 16 bits wide
  my_register my_register_4 (
    .Clk(in_10), .Reset(in_11), .ID(4'b0011), .in_3(in_5), .in_4(in_6), .in_5(in_7), .in_6(in_8),
    .in_1(in_9), .in_2({ALU_Out, Addr_out, Data_out, Write}), .out_10(my_register_4_out_10),
    .out_11(my_register_4_out_11), .out_12(my_register_4_out_12), .out_13(my_register_4_out_13),
    .out_14(my_register_4_out_14));
  assign or_9_out = my_register_5_out_11 | or_11_out;  // OR_Gate or_9, 16 bits wide
  assign or_10_out = my_register_5_out_12 | or_12_out;  // OR_Gate or_10, 16 bits wide
  my_register my_register_5 (
    .Clk(in_10), .Reset(in_11), .ID(4'b0100), .in_3(in_5), .in_4(in_6), .in_5(in_7), .in_6(in_8),
    .in_1(in_9), .in_2({ALU_Out, Addr_out, Data_out, Write}), .out_10(my_register_5_out_10),
    .out_11(my_register_5_out_11), .out_12(my_register_5_out_12), .out_13(my_register_5_out_13),
    .out_14(my_register_5_out_14));
  assign or_11_out = my_register_6_out_11 | or_13_out;  // OR_Gate or_11, 16 bits wide
  assign or_12_out = my_register_6_out_12 | or_14_out;  // OR_Gate or_12, 16 bits wide
  my_register my_register_6 (
    .Clk(in_10), .Reset(in_11), .ID(4'b0101), .in_3(in_5), .in_4(in_6), .in_5(in_7), .in_6(in_8),
    .in_1(in_9), .in_2({ALU_Out, Addr_out, Data_out, Write}), .out_10(my_register_6_out_10),
    .out_11(my_register_6_out_11), .out_12(my_register_6_out_12), .out_13(my_register_6_out_13),
    .out_14(my_register_6_out_14));
  assign or_13_out = my_register_7_out_11 | or_15_out;  // OR_Gate or_13, 16 bits wide
  assign or_14_out = my_register_7_out_12 | or_16_out;  // OR_Gate or_14, 16 bits wide
  my_register my_register_7 (
    .Clk(in_10), .Reset(in_11), .ID(4'b0110), .in_3(in_5), .in_4(in_6), .in_5(in_7), .in_6(in_8),
    .in_1(in_9), .in_2({ALU_Out, Addr_out, Data_out, Write}), .out_10(my_register_7_out_10),
    .out_11(my_register_7_out_11), .out_12(my_register_7_out_12), .out_13(my_register_7_out_13),
    .out_14(my_register_7_out_14));
  assign or_15_out = my_register_8_out_11 | or_17_out;  // OR_Gate or_15, 16 bits wide
  assign or_16_out = my_register_8_out_12 | or_18_out;  // OR_Gate or_16, 16 bits wide
  my_register my_register_8 (
    .Clk(in_10), .Reset(in_11), .ID(4'b0111), .in_3(in_5), .in_4(in_6), .in_5(in_7), .in_6(in_8),
    .in_1(in_9), .in_2({ALU_Out, Addr_out, Data_out, Write}), .out_10(my_register_8_out_10),
    .out_11(my_register_8_out_11), .out_12(my_register_8_out_12), .out_13(my_register_8_out_13),
    .out_14(my_register_8_out_14));
  assign or_17_out = my_register_9_out_11 | or_19_out;  // OR_Gate or_17, 16 bits wide
  assign or_18_out = my_register_9_out_12 | or_20_out;  // OR_Gate or_18, 16 bits wide
  my_register my_register_9 (
    .Clk(in_10), .Reset(in_11), .ID(4'b1000), .in_3(in_5), .in_4(in_6), .in_5(in_7), .in_6(in_8),
    .in_1(in_9), .in_2({ALU_Out, Addr_out, Data_out, Write}), .out_10(my_register_9_out_10),
    .out_11(my_register_9_out_11), .out_12(my_register_9_out_12), .out_13(my_register_9_out_13),
    .out_14(my_register_9_out_14));
  assign or_19_out = my_register_10_out_11 | or_21_out;  // OR_Gate or_19, 16 bits wide
  assign or_20_out = my_register_10_out_12 | or_22_out;  // OR_Gate or_20, 16 bits wide
  my_register my_register_10 (
    .Clk(in_10), .Reset(in_11), .ID(4'b1001), .in_3(in_5), .in_4(in_6), .in_5(in_7), .in_6(in_8),
    .in_1(in_9), .in_2({ALU_Out, Addr_out, Data_out, Write}), .out_10(my_register_10_out_10),
    .out_11(my_register_10_out_11), .out_12(my_register_10_out_12), .out_13(my_register_10_out_13),
    .out_14(my_register_10_out_14));
  assign or_21_out = my_register_11_out_11 | or_23_out;  // OR_Gate or_21, 16 bits wide
  assign or_22_out = my_register_11_out_12 | or_24_out;  // OR_Gate or_22, 16 bits wide
  my_register my_register_11 (
    .Clk(in_10), .Reset(in_11), .ID(4'b1010), .in_3(in_5), .in_4(in_6), .in_5(in_7), .in_6(in_8),
    .in_1(in_9), .in_2({ALU_Out, Addr_out, Data_out, Write}), .out_10(my_register_11_out_10),
    .out_11(my_register_11_out_11), .out_12(my_register_11_out_12), .out_13(my_register_11_out_13),
    .out_14(my_register_11_out_14));
  assign or_23_out = my_register_12_out_11 | or_25_out;  // OR_Gate or_23, 16 bits wide
  assign or_24_out = my_register_12_out_12 | or_26_out;  // OR_Gate or_24, 16 bits wide
  my_register my_register_12 (
    .Clk(in_10), .Reset(in_11), .ID(4'b1011), .in_3(in_5), .in_4(in_6), .in_5(in_7), .in_6(in_8),
    .in_1(in_9), .in_2({ALU_Out, Addr_out, Data_out, Write}), .out_10(my_register_12_out_10),
    .out_11(my_register_12_out_11), .out_12(my_register_12_out_12), .out_13(my_register_12_out_13),
    .out_14(my_register_12_out_14));
  assign or_25_out = my_register_13_out_11 | or_27_out;  // OR_Gate or_25, 16 bits wide
  assign or_26_out = my_register_13_out_12 | or_28_out;  // OR_Gate or_26, 16 bits wide
  my_register my_register_13 (
    .Clk(in_10), .Reset(in_11), .ID(4'b1100), .in_3(in_5), .in_4(in_6), .in_5(in_7), .in_6(in_8),
    .in_1(in_9), .in_2({ALU_Out, Addr_out, Data_out, Write}), .out_10(my_register_13_out_10),
    .out_11(my_register_13_out_11), .out_12(my_register_13_out_12), .out_13(my_register_13_out_13),
    .out_14(my_register_13_out_14));
  assign or_27_out = my_register_14_out_11 | or_29_out;  // OR_Gate or_27, 16 bits wide
  assign or_28_out = my_register_14_out_12 | or_30_out;  // OR_Gate or_28, 16 bits wide
  my_register my_register_14 (
    .Clk(in_10), .Reset(in_11), .ID(4'b1101), .in_3(in_5), .in_4(in_6), .in_5(in_7), .in_6(in_8),
    .in_1(in_9), .in_2({ALU_Out, Addr_out, Data_out, Write}), .out_10(my_register_14_out_10),
    .out_11(my_register_14_out_11), .out_12(my_register_14_out_12), .out_13(my_register_14_out_13),
    .out_14(my_register_14_out_14));
  assign or_29_out = my_register_15_out_11 | my_register_16_out_11;  // OR_Gate or_29, 16 bits wide
  assign or_30_out = my_register_15_out_12 | my_register_16_out_12;  // OR_Gate or_30, 16 bits wide
  my_register my_register_15 (
    .Clk(in_10), .Reset(in_11), .ID(4'b1110), .in_3(in_5), .in_4(in_6), .in_5(in_7), .in_6(in_8),
    .in_1(in_9), .in_2({ALU_Out, Addr_out, Data_out, Write}), .out_10(my_register_15_out_10),
    .out_11(my_register_15_out_11), .out_12(my_register_15_out_12), .out_13(my_register_15_out_13),
    .out_14(my_register_15_out_14));
  my_register my_register_16 (
    .Clk(in_10), .Reset(in_11), .ID(4'b1111), .in_3(in_5), .in_4(in_6), .in_5(in_7), .in_6(in_8),
    .in_1(in_9), .in_2({ALU_Out, Addr_out, Data_out, Write}), .out_10(my_register_16_out_10),
    .out_11(my_register_16_out_11), .out_12(my_register_16_out_12), .out_13(my_register_16_out_13),
    .out_14(my_register_16_out_14));
  assign out_14 = my_register_1_out_13 | or_33_out;  // OR_Gate or_31, 16 bits wide
  assign out_15 = my_register_1_out_14 | or_34_out;  // OR_Gate or_32, 16 bits wide
  assign or_33_out = my_register_2_out_13 | or_35_out;  // OR_Gate or_33, 16 bits wide
  assign or_34_out = my_register_2_out_14 | or_36_out;  // OR_Gate or_34, 16 bits wide
  assign or_35_out = my_register_3_out_13 | or_37_out;  // OR_Gate or_35, 16 bits wide
  assign or_36_out = my_register_3_out_14 | or_38_out;  // OR_Gate or_36, 16 bits wide
  assign or_37_out = my_register_4_out_13 | or_39_out;  // OR_Gate or_37, 16 bits wide
  assign or_38_out = my_register_4_out_14 | or_40_out;  // OR_Gate or_38, 16 bits wide
  assign or_39_out = my_register_5_out_13 | or_41_out;  // OR_Gate or_39, 16 bits wide
  assign or_40_out = my_register_5_out_14 | or_42_out;  // OR_Gate or_40, 16 bits wide
  assign or_41_out = my_register_6_out_13 | or_43_out;  // OR_Gate or_41, 16 bits wide
  assign or_42_out = my_register_6_out_14 | or_44_out;  // OR_Gate or_42, 16 bits wide
  assign or_43_out = my_register_7_out_13 | or_45_out;  // OR_Gate or_43, 16 bits wide
  assign or_44_out = my_register_7_out_14 | or_46_out;  // OR_Gate or_44, 16 bits wide
  assign or_45_out = my_register_8_out_13 | or_47_out;  // OR_Gate or_45, 16 bits wide
  assign or_46_out = my_register_8_out_14 | or_48_out;  // OR_Gate or_46, 16 bits wide
  assign or_47_out = my_register_9_out_13 | or_49_out;  // OR_Gate or_47, 16 bits wide
  assign or_48_out = my_register_9_out_14 | or_50_out;  // OR_Gate or_48, 16 bits wide
  assign or_49_out = my_register_10_out_13 | or_51_out;  // OR_Gate or_49, 16 bits wide
  assign or_50_out = my_register_10_out_14 | or_52_out;  // OR_Gate or_50, 16 bits wide
  assign or_51_out = my_register_11_out_13 | or_53_out;  // OR_Gate or_51, 16 bits wide
  assign or_52_out = my_register_11_out_14 | or_54_out;  // OR_Gate or_52, 16 bits wide
  assign or_53_out = my_register_12_out_13 | or_55_out;  // OR_Gate or_53, 16 bits wide
  assign or_54_out = my_register_12_out_14 | or_56_out;  // OR_Gate or_54, 16 bits wide
  assign or_55_out = my_register_13_out_13 | or_57_out;  // OR_Gate or_55, 16 bits wide
  assign or_56_out = my_register_13_out_14 | or_58_out;  // OR_Gate or_56, 16 bits wide
  assign or_57_out = my_register_14_out_13 | or_59_out;  // OR_Gate or_57, 16 bits wide
  assign or_58_out = my_register_14_out_14 | or_60_out;  // OR_Gate or_58, 16 bits wide
  assign or_59_out = my_register_15_out_13 | my_register_16_out_13;  // OR_Gate or_59, 16 bits wide
  assign or_60_out = my_register_15_out_14 | my_register_16_out_14;  // OR_Gate or_60, 16 bits wide

  // Notes on the sheet:
  //   bus output
  //   ALU out 1
  //   ALU out 2
  //   Write target
  //   Data
  //   Data out
  //   Addr out
  //   ALU out 1
  //   ALU out 2
endmodule

module my_register (
  input  [15:0] in_1,
  input  [3:0] in_2,
  input  [3:0] in_3,
  input  [3:0] in_4,
  input  [3:0] in_5,
  input  [3:0] in_6,
  input  Clk,
  input  Reset,
  input  [3:0] ID,
  output [15:0] out_10,
  output [15:0] out_11,
  output [15:0] out_12,
  output [15:0] out_13,
  output [15:0] out_14
);

  wire and_1_out, and_2_out, button_1_out, extra_sticky_gate_1_out_5, nor_1_out, nor_2_out, nor_3_out,
       nor_4_out, or_1_out, or_2_out, sticky_gate_2_propagate_reset, sticky_gate_3_propagate_reset,
       xor_1_out, xor_2_out, xor_3_out, xor_4_out, xor_5_out, xor_6_out, xor_7_out, xor_8_out, xor_9_out,
       xor_10_out, xor_11_out, xor_12_out, xor_13_out, xor_14_out, xor_15_out, xor_16_out, xor_17_out,
       xor_18_out, xor_19_out, xor_20_out;

  or or_1 (or_1_out, in_2[2], in_2[1]);
  xor xor_1 (xor_1_out, in_3[0], ID[0]);
  xor xor_2 (xor_2_out, in_3[1], ID[1]);
  xor xor_3 (xor_3_out, in_3[2], ID[2]);
  xor xor_4 (xor_4_out, in_3[3], ID[3]);
  xor xor_5 (xor_5_out, or_1_out, 1'b1);
  xor xor_6 (xor_6_out, in_4[0], ID[0]);
  xor xor_7 (xor_7_out, in_4[1], ID[1]);
  xor xor_8 (xor_8_out, in_4[2], ID[2]);
  xor xor_9 (xor_9_out, in_4[3], ID[3]);
  xor xor_10 (xor_10_out, in_2[3], 1'b1);
  xor xor_11 (xor_11_out, in_5[0], ID[0]);
  xor xor_12 (xor_12_out, in_5[1], ID[1]);
  xor xor_13 (xor_13_out, in_5[2], ID[2]);
  xor xor_14 (xor_14_out, in_5[3], ID[3]);
  xor xor_15 (xor_15_out, in_2[3], 1'b1);
  xor xor_16 (xor_16_out, in_6[0], ID[0]);
  xor xor_17 (xor_17_out, in_6[1], ID[1]);
  xor xor_18 (xor_18_out, in_6[2], ID[2]);
  xor xor_19 (xor_19_out, in_6[3], ID[3]);
  xor xor_20 (xor_20_out, in_2[0], 1'b1);
  nor nor_1 (nor_1_out, xor_1_out, xor_2_out, xor_3_out, xor_4_out, xor_5_out);
  nor nor_2 (nor_2_out, xor_6_out, xor_7_out, xor_8_out, xor_9_out, xor_10_out);
  nor nor_3 (nor_3_out, xor_11_out, xor_12_out, xor_13_out, xor_14_out, xor_15_out);
  nor nor_4 (nor_4_out, xor_16_out, xor_17_out, xor_18_out, xor_19_out, xor_20_out);
  Register #(.width(16)) register_1 (.D(in_1), .en(nor_4_out), .clk(Clk), .Q(out_10), .clr(Reset));
  and and_1 (and_1_out, in_2[2], nor_1_out);
  Button button_1 (.out(button_1_out));
  and and_2 (and_2_out, in_2[1], nor_1_out);
  or or_2 (or_2_out, Reset, button_1_out);
  sticky_gate sticky_gate_1 (
    .clock(Clk), .reset(extra_sticky_gate_1_out_5), .data_in(out_10), .enable(and_2_out), .out_6(out_11));  // open: propagate_reset
  extra_sticky_gate extra_sticky_gate_1 (
    .Reset(sticky_gate_2_propagate_reset), .in_1(out_10), .Clock(Clk), .Activate(and_1_out),
    .out_5(extra_sticky_gate_1_out_5), .out_6(out_12));
  sticky_gate sticky_gate_2 (
    .clock(Clk), .reset(sticky_gate_3_propagate_reset), .data_in(out_10), .enable(nor_2_out),
    .propagate_reset(sticky_gate_2_propagate_reset), .out_6(out_13));
  sticky_gate sticky_gate_3 (
    .clock(Clk), .reset(or_2_out), .data_in(out_10), .enable(nor_3_out),
    .propagate_reset(sticky_gate_3_propagate_reset), .out_6(out_14));

  // Notes on the sheet:
  //   Data
  //   Write
  //   Data out
  //   Addr out
  //   ALU Out
  //   bus output
  //   ALU out 1
  //   ALU out 2
  //   Write target
  //   Data
  //   Addr
  //   ALU 1
  //   ALU 2
endmodule

module GRU (
  input  in_1,
  output out_2
);

  wire s_r_ff_2_q;

  S_R_Flip_Flop s_r_ff_1 (.S(1'b1), .R(1'b0), .clk(in_1), .Q(out_2), .reset(s_r_ff_2_q));  // open: Qn, preset
  S_R_Flip_Flop s_r_ff_2 (.S(out_2), .R(1'b0), .clk(in_1), .Q(s_r_ff_2_q));  // open: reset, Qn, preset
endmodule

module cave (
  input  [15:0] control_bus_1,
  input  [15:0] control_bus_2,
  input  [15:0] data_bus_in,
  input  [15:0] addr_bus_in,
  input  clocl,
  input  reset,
  output [15:0] data_bus_out,
  output [15:0] addr_bus_out
);

  wire and_1_out, and_2_out, and_3_out, and_4_out, and_5_out, and_6_out, and_7_out, and_8_out, and_9_out,
       and_10_out, and_11_out, and_12_out, and_13_out, and_14_out, and_15_out, and_16_out, buffer_2_out,
       buffer_3_out, buffer_4_out, buffer_5_out, buffer_6_out, buffer_7_out, buffer_8_out, buffer_9_out,
       buffer_10_out, button_1_out, four_bit_eq_cmp_1_out_3, four_bit_eq_cmp_2_out_3, not_1_out, or_1_out,
       or_2_out, or_3_out, or_4_out, or_5_out, or_6_out, or_7_out, or_8_out, or_9_out,
       sixt_bit_eq_cmp_1_out_3, sixt_bit_eq_cmp_2_out_3, sixt_bit_eq_cmp_3_out_3, sixt_bit_eq_cmp_4_out_3,
       sixt_bit_eq_cmp_5_out_3, sixt_bit_eq_cmp_6_out_3, sixt_bit_eq_cmp_7_out_3, sixt_bit_eq_cmp_8_out_3,
       sixt_bit_eq_cmp_9_out_3, sixt_bit_eq_cmp_10_out_3, sixt_bit_eq_cmp_11_out_3, sixt_bit_eq_cmp_12_out_3,
       sixt_bit_eq_cmp_13_out_3, sixt_bit_eq_cmp_14_out_3;
  wire [15:0] extra_sticky_gate_1_out_6, extra_sticky_gate_2_out_6, extra_sticky_gate_3_out_6,
       extra_sticky_gate_4_out_6, register_1_q, register_2_q, sticky_gate_1_out_6, sticky_gate_2_out_6,
       sticky_gate_3_out_6, sticky_gate_4_out_6;

  or or_1 (or_1_out, reset, button_1_out);
  Button button_1 (.out(button_1_out));
  Register #(.trigger("falling"), .width(16)) register_1 (
    .D(data_bus_in), .en(1'b1), .clk(clocl), .Q(register_1_q), .clr(or_1_out));
  // Buffer buffer_1 has open pins: in=buffer_6_out, out=open
  not not_1 (not_1_out, clocl);
  sixt_bit_eq_cmp sixt_bit_eq_cmp_1 (.in_1(control_bus_1), .in_2(16'h90), .out_3(sixt_bit_eq_cmp_1_out_3));
  sixt_bit_eq_cmp sixt_bit_eq_cmp_2 (.in_1(control_bus_2), .in_2(16'h90), .out_3(sixt_bit_eq_cmp_2_out_3));
  sixt_bit_eq_cmp sixt_bit_eq_cmp_3 (.in_1(control_bus_1), .in_2(16'h91), .out_3(sixt_bit_eq_cmp_3_out_3));
  sixt_bit_eq_cmp sixt_bit_eq_cmp_4 (.in_1(control_bus_2), .in_2(16'h91), .out_3(sixt_bit_eq_cmp_4_out_3));
  sixt_bit_eq_cmp sixt_bit_eq_cmp_5 (.in_1(control_bus_1), .in_2(16'h92), .out_3(sixt_bit_eq_cmp_5_out_3));
  sixt_bit_eq_cmp sixt_bit_eq_cmp_6 (.in_1(control_bus_2), .in_2(16'h92), .out_3(sixt_bit_eq_cmp_6_out_3));
  sixt_bit_eq_cmp sixt_bit_eq_cmp_7 (.in_1(control_bus_1), .in_2(16'h93), .out_3(sixt_bit_eq_cmp_7_out_3));
  sixt_bit_eq_cmp sixt_bit_eq_cmp_8 (.in_1(control_bus_2), .in_2(16'h93), .out_3(sixt_bit_eq_cmp_8_out_3));
  sixt_bit_eq_cmp sixt_bit_eq_cmp_9 (.in_1(control_bus_1), .in_2(16'h94), .out_3(sixt_bit_eq_cmp_9_out_3));
  sixt_bit_eq_cmp sixt_bit_eq_cmp_10 (.in_1(control_bus_2), .in_2(16'h94), .out_3(sixt_bit_eq_cmp_10_out_3));
  sixt_bit_eq_cmp sixt_bit_eq_cmp_11 (.in_1(control_bus_1), .in_2(16'h95), .out_3(sixt_bit_eq_cmp_11_out_3));
  sixt_bit_eq_cmp sixt_bit_eq_cmp_12 (.in_1(control_bus_2), .in_2(16'h95), .out_3(sixt_bit_eq_cmp_12_out_3));
  sixt_bit_eq_cmp sixt_bit_eq_cmp_13 (.in_1(control_bus_1), .in_2(16'h96), .out_3(sixt_bit_eq_cmp_13_out_3));
  sixt_bit_eq_cmp sixt_bit_eq_cmp_14 (.in_1(control_bus_2), .in_2(16'h96), .out_3(sixt_bit_eq_cmp_14_out_3));
  four_bit_eq_cmp four_bit_eq_cmp_1 (.in_1(control_bus_1[7:4]), .in_2(4'b0100), .out_3(four_bit_eq_cmp_1_out_3));
  four_bit_eq_cmp four_bit_eq_cmp_2 (.in_1(control_bus_2[7:4]), .in_2(4'b0100), .out_3(four_bit_eq_cmp_2_out_3));
  buf buffer_2 (buffer_2_out, clocl);
  buf buffer_3 (buffer_3_out, buffer_2_out);
  buf buffer_4 (buffer_4_out, buffer_3_out);
  buf buffer_5 (buffer_5_out, buffer_4_out);
  buf buffer_6 (buffer_6_out, buffer_7_out);
  buf buffer_7 (buffer_7_out, buffer_8_out);
  buf buffer_8 (buffer_8_out, buffer_9_out);
  buf buffer_9 (buffer_9_out, buffer_10_out);
  and and_1 (and_1_out, not_1_out, sixt_bit_eq_cmp_1_out_3);
  and and_2 (and_2_out, not_1_out, sixt_bit_eq_cmp_2_out_3);
  and and_3 (and_3_out, not_1_out, sixt_bit_eq_cmp_3_out_3);
  and and_4 (and_4_out, not_1_out, sixt_bit_eq_cmp_4_out_3);
  and and_5 (and_5_out, not_1_out, sixt_bit_eq_cmp_5_out_3);
  and and_6 (and_6_out, not_1_out, sixt_bit_eq_cmp_6_out_3);
  and and_7 (and_7_out, not_1_out, sixt_bit_eq_cmp_7_out_3);
  and and_8 (and_8_out, not_1_out, sixt_bit_eq_cmp_8_out_3);
  and and_9 (and_9_out, not_1_out, sixt_bit_eq_cmp_9_out_3);
  and and_10 (and_10_out, not_1_out, sixt_bit_eq_cmp_10_out_3);
  and and_11 (and_11_out, not_1_out, sixt_bit_eq_cmp_11_out_3);
  and and_12 (and_12_out, not_1_out, sixt_bit_eq_cmp_12_out_3);
  and and_13 (and_13_out, not_1_out, sixt_bit_eq_cmp_13_out_3);
  and and_14 (and_14_out, not_1_out, sixt_bit_eq_cmp_14_out_3);
  and and_15 (and_15_out, not_1_out, four_bit_eq_cmp_1_out_3);
  and and_16 (and_16_out, not_1_out, four_bit_eq_cmp_2_out_3);
  Register #(.trigger("falling"), .width(16)) register_2 (
    .D(addr_bus_in), .en(1'b1), .clk(clocl), .Q(register_2_q), .clr(or_1_out));
  // Probe on register_1_q
  // Probe on register_2_q
  buf buffer_10 (buffer_10_out, buffer_5_out);
  or or_2 (or_2_out, and_1_out, and_2_out);
  or or_3 (or_3_out, and_3_out, and_4_out);
  or or_4 (or_4_out, and_5_out, and_6_out);
  or or_5 (or_5_out, and_7_out, and_8_out);
  or or_6 (or_6_out, and_9_out, and_10_out);
  or or_7 (or_7_out, and_11_out, and_12_out);
  or or_8 (or_8_out, and_13_out, and_14_out);
  or or_9 (or_9_out, and_15_out, and_16_out);
  sticky_gate sticky_gate_1 (
    .clock(clocl), .reset(or_1_out), .data_in(register_1_q), .enable(or_2_out), .out_6(sticky_gate_1_out_6));  // open: propagate_reset
  extra_sticky_gate extra_sticky_gate_1 (
    .Reset(or_1_out), .in_1(register_1_q), .Clock(clocl), .Activate(or_3_out),
    .out_6(extra_sticky_gate_1_out_6));  // open: out_5
  sticky_gate sticky_gate_2 (
    .clock(clocl), .reset(or_1_out), .data_in(register_2_q), .enable(or_4_out), .out_6(sticky_gate_2_out_6));  // open: propagate_reset
  sticky_gate sticky_gate_3 (
    .clock(clocl), .reset(or_1_out), .data_in(register_2_q), .enable(or_5_out), .out_6(sticky_gate_3_out_6));  // open: propagate_reset
  extra_sticky_gate extra_sticky_gate_2 (
    .Reset(or_1_out), .in_1(register_2_q), .Clock(clocl), .Activate(or_6_out),
    .out_6(extra_sticky_gate_2_out_6));  // open: out_5
  extra_sticky_gate extra_sticky_gate_3 (
    .Reset(or_1_out), .in_1(register_1_q), .Clock(clocl), .Activate(or_7_out),
    .out_6(extra_sticky_gate_3_out_6));  // open: out_5
  extra_sticky_gate extra_sticky_gate_4 (
    .Reset(or_1_out), .in_1(register_2_q), .Clock(clocl), .Activate(or_8_out),
    .out_6(extra_sticky_gate_4_out_6));  // open: out_5
  sticky_gate sticky_gate_4 (
    .clock(clocl), .reset(or_1_out), .data_in(register_1_q), .enable(or_9_out), .out_6(sticky_gate_4_out_6));  // open: propagate_reset
  assign data_bus_out = sticky_gate_1_out_6 | sticky_gate_4_out_6 | extra_sticky_gate_4_out_6 | extra_sticky_gate_3_out_6 | sticky_gate_2_out_6;  // OR_Gate or_10, 16 bits wide
  assign addr_bus_out = extra_sticky_gate_1_out_6 | extra_sticky_gate_2_out_6 | sticky_gate_3_out_6;  // OR_Gate or_11, 16 bits wide
endmodule

module falling_edge_PE (
  input  signal_in,
  input  clock,
  input  reset,
  output propagate_reset,
  output propagate_clock,
  output signal_out
);

  wire d_ff_1_q, xor_1_out;

  xor xor_1 (xor_1_out, clock, d_ff_1_q);
  D_Flip_Flop #(.trigger("falling")) d_ff_1 (
    .D(signal_in), .clk(xor_1_out), .Q(d_ff_1_q), .reset(reset));  // open: Qn, preset
  or or_1 (signal_out, signal_in, d_ff_1_q);

  assign propagate_clock = clock;
  assign propagate_reset = reset;
endmodule

module falling_edge_double_PE (
  input  in_1,
  input  in_2,
  input  in_3,
  output out_4,
  output out_5,
  output out_6
);

  wire d_ff_1_q, d_ff_2_q, xor_1_out;

  D_Flip_Flop #(.trigger("falling")) d_ff_1 (
    .D(in_1), .clk(xor_1_out), .Q(d_ff_1_q), .reset(in_3));  // open: Qn, preset
  xor xor_1 (xor_1_out, in_2, d_ff_1_q);
  D_Flip_Flop d_ff_2 (.D(d_ff_1_q), .clk(in_2), .Q(d_ff_2_q), .reset(in_3));  // open: Qn, preset
  or or_1 (out_6, in_1, d_ff_2_q, d_ff_1_q);

  assign out_4 = in_3;
  assign out_5 = in_2;
endmodule

module CPG (
  input  in_1,
  input  in_2,
  input  in_3,
  input  in_4,
  input  in_5,
  output out_6
);

  wire and_1_out, and_2_out, and_3_out, and_4_out, and_5_out, and_6_out, d_ff_1_q, d_ff_2_q, or_1_out,
       or_2_out;

  D_Flip_Flop d_ff_1 (.D(1'b1), .clk(in_5), .Q(d_ff_1_q), .reset(d_ff_1_q));  // open: Qn, preset
  D_Flip_Flop #(.trigger("falling")) d_ff_2 (.D(1'b1), .clk(in_5), .Q(d_ff_2_q), .reset(d_ff_2_q));  // open: Qn, preset
  and and_1 (and_1_out, d_ff_1_q, in_5);
  and and_2 (and_2_out, ~in_5, d_ff_2_q);  // AND_Gate
  and and_3 (and_3_out, in_3, in_5);
  and and_4 (and_4_out, ~in_5, in_4);  // AND_Gate
  and and_5 (and_5_out, in_1, and_1_out);
  and and_6 (and_6_out, in_2, and_2_out);
  or or_1 (or_1_out, and_3_out, and_4_out);
  or or_2 (or_2_out, and_5_out, and_6_out);
  or or_3 (out_6, or_1_out, or_2_out);
endmodule

module CE_DFF (
  input  in_1,
  input  in_2,
  input  in_3,
  input  in_4,
  input  in_5,
  input  in_6,
  output out_7
);

  wire and_1_out, and_2_out, and_3_out, and_4_out, d_ff_1_q, d_ff_2_q, or_1_out;

  D_Flip_Flop d_ff_1 (.D(1'b1), .clk(in_6), .Q(d_ff_1_q), .reset(d_ff_1_q));  // open: Qn, preset
  D_Flip_Flop #(.trigger("falling")) d_ff_2 (.D(1'b1), .clk(in_6), .Q(d_ff_2_q), .reset(d_ff_2_q));  // open: Qn, preset
  and and_1 (and_1_out, in_4, in_6);
  and and_2 (and_2_out, in_5, ~in_6);  // AND_Gate
  and and_3 (and_3_out, d_ff_1_q, in_2, in_6);
  and and_4 (and_4_out, ~in_6, in_3, d_ff_2_q);  // AND_Gate
  D_Flip_Flop #(.trigger("high")) d_ff_3 (.D(in_1), .clk(or_1_out), .Q(out_7));  // open: Qn, preset, reset
  or or_1 (or_1_out, and_1_out, and_2_out, and_3_out, and_4_out);
endmodule

module edger (
  input  in_1,
  output out_2
);

  wire d_ff_1_q, d_ff_2_q;

  D_Flip_Flop d_ff_1 (.D(1'b1), .clk(in_1), .Q(d_ff_1_q), .reset(d_ff_1_q));  // open: Qn, preset
  D_Flip_Flop #(.trigger("falling")) d_ff_2 (.D(1'b1), .clk(in_1), .Q(d_ff_2_q), .reset(d_ff_2_q));  // open: Qn, preset
  or or_1 (out_2, d_ff_1_q, d_ff_2_q);
endmodule

module io_pins_4 (
  input  [15:0] control_bus,
  input  [15:0] data_bus_in,
  input  clock,
  input  reset,
  input  in_5,
  input  in_6,
  input  in_7,
  input  in_8,
  output [15:0] data_bus_out,
  output out_10,
  output out_11,
  output out_12,
  output out_13,
  output out_14,
  output out_15,
  output out_16,
  output out_17
);

  wire and_1_out, and_2_out, and_3_out, and_4_out, and_5_out, and_6_out, and_7_out, and_8_out, and_9_out,
       and_10_out, and_11_out, and_12_out, comparator_1_eq, comparator_2_eq, comparator_3_eq,
       comparator_4_eq, comparator_5_eq, comparator_6_eq, decoder_1_out0, decoder_1_out1, decoder_1_out2,
       decoder_1_out3, multiplexer_1_out, not_1_out, not_2_out, or_1_out, or_2_out, or_3_out, or_4_out,
       or_5_out, or_6_out;
  wire [0:0] or_7_out;

  not not_1 (not_1_out, clock);
  Comparator comparator_1 (.a(control_bus[7:0]), .b(8'h30), .eq(comparator_1_eq));  // open: gt, lt
  Comparator comparator_2 (.a(control_bus[7:0]), .b(8'h31), .eq(comparator_2_eq));  // open: gt, lt
  Comparator comparator_3 (.a(control_bus[7:0]), .b(8'h32), .eq(comparator_3_eq));  // open: gt, lt
  Comparator comparator_4 (.a(control_bus[7:0]), .b(8'h33), .eq(comparator_4_eq));  // open: gt, lt
  Comparator comparator_5 (.a(control_bus[7:0]), .b(8'h34), .eq(comparator_5_eq));  // open: gt, lt
  Comparator comparator_6 (.a(control_bus[7:0]), .b(8'h35), .eq(comparator_6_eq));  // open: gt, lt
  Decoder #(.enable("false"), .select(2)) decoder_1 (
    .out0(decoder_1_out0), .out1(decoder_1_out1), .out2(decoder_1_out2), .out3(decoder_1_out3),
    .sel(control_bus[13:12]));
  or or_1 (or_1_out, comparator_6_eq, comparator_4_eq, comparator_3_eq);
  or or_2 (or_2_out, comparator_2_eq, comparator_1_eq);
  or or_3 (or_3_out, ~comparator_1_eq, comparator_2_eq);  // OR_Gate
  and and_1 (and_1_out, decoder_1_out0, or_1_out, not_1_out);
  and and_2 (and_2_out, decoder_1_out0, or_2_out, not_1_out);
  or or_4 (or_4_out, data_bus_in[0], data_bus_in[1], data_bus_in[2], data_bus_in[3], data_bus_in[4], data_bus_in[5], data_bus_in[6], data_bus_in[7], data_bus_in[8], data_bus_in[9], data_bus_in[10], data_bus_in[11], data_bus_in[12], data_bus_in[13], data_bus_in[14], data_bus_in[15]);
  Multiplexer #(.enable("true")) multiplexer_1 (
    .in0(or_4_out), .in1(1'b1), .out(multiplexer_1_out), .sel(comparator_4_eq), .en(not_2_out));
  not not_2 (not_2_out, comparator_3_eq);
  D_Flip_Flop d_ff_1 (.D(multiplexer_1_out), .clk(and_1_out), .Q(out_10), .reset(reset));  // open: Qn, preset
  D_Flip_Flop d_ff_2 (.D(or_3_out), .clk(and_2_out), .Q(out_11), .reset(reset));  // open: Qn, preset
  and and_3 (and_3_out, decoder_1_out0, in_5);
  D_Flip_Flop d_ff_3 (.D(multiplexer_1_out), .clk(and_4_out), .Q(out_12), .reset(reset));  // open: Qn, preset
  and and_4 (and_4_out, decoder_1_out1, or_1_out, not_1_out);
  D_Flip_Flop d_ff_4 (.D(or_3_out), .clk(and_5_out), .Q(out_13), .reset(reset));  // open: Qn, preset
  and and_5 (and_5_out, decoder_1_out1, or_2_out, not_1_out);
  and and_6 (and_6_out, decoder_1_out1, in_6);
  or or_5 (or_5_out, and_3_out, and_6_out);
  D_Flip_Flop d_ff_5 (.D(multiplexer_1_out), .clk(and_7_out), .Q(out_14), .reset(reset));  // open: Qn, preset
  and and_7 (and_7_out, decoder_1_out2, or_1_out, not_1_out);
  D_Flip_Flop d_ff_6 (.D(or_3_out), .clk(and_8_out), .Q(out_15), .reset(reset));  // open: Qn, preset
  and and_8 (and_8_out, decoder_1_out2, or_2_out, not_1_out);
  or or_6 (or_6_out, or_5_out, and_9_out);
  and and_9 (and_9_out, decoder_1_out2, in_7);
  and and_10 (and_10_out, decoder_1_out3, or_1_out, not_1_out);
  and and_11 (and_11_out, decoder_1_out3, or_2_out, not_1_out);
  D_Flip_Flop d_ff_7 (.D(multiplexer_1_out), .clk(and_10_out), .Q(out_16), .reset(reset));  // open: Qn, preset
  D_Flip_Flop d_ff_8 (.D(or_3_out), .clk(and_11_out), .Q(out_17), .reset(reset));  // open: Qn, preset
  or or_7 (or_7_out[0], or_6_out, and_12_out);
  and and_12 (and_12_out, decoder_1_out3, in_8);
  r_ctl_2 r_ctl_2_1 (
    .n_clock_cycles(control_bus[11:8]), .data_in({{15{1'b0}}, or_7_out[0]}), .clock(clock),
    .read_signal(comparator_5_eq), .reset(reset), .out_6(data_bus_out));
endmodule

module io_pins_8 (
  input  [15:0] control_bus,
  input  [15:0] data_bus_in,
  input  clock,
  input  reset,
  input  in_5,
  input  in_6,
  input  in_7,
  input  in_8,
  input  in_9,
  input  in_10,
  input  in_11,
  input  in_12,
  output [15:0] data_bus_out,
  output out_14,
  output out_15,
  output out_16,
  output out_17,
  output out_18,
  output out_19,
  output out_20,
  output out_21,
  output out_22,
  output out_23,
  output out_24,
  output out_25,
  output out_26,
  output out_27,
  output out_28,
  output out_29
);

  wire and_1_out, and_2_out, and_3_out, and_4_out, and_5_out, and_6_out, and_7_out, and_8_out, and_9_out,
       and_10_out, and_11_out, and_12_out, and_13_out, and_14_out, and_15_out, and_16_out, and_17_out,
       and_18_out, and_19_out, and_20_out, and_21_out, and_22_out, and_23_out, and_24_out, and_25_out,
       buffer_1_out, buffer_2_out, buffer_3_out, buffer_4_out, comparator_1_eq, comparator_2_eq,
       comparator_3_eq, comparator_4_eq, comparator_5_eq, comparator_6_eq, decoder_1_out0, decoder_1_out1,
       decoder_1_out2, decoder_1_out3, decoder_1_out4, decoder_1_out5, decoder_1_out6, decoder_1_out7,
       multiplexer_1_out, not_1_out, not_2_out, not_3_out, or_1_out, or_2_out, or_3_out, or_4_out, or_5_out,
       or_6_out, or_7_out, or_8_out, or_9_out, or_10_out, or_11_out, or_13_out, or_14_out, s_r_ff_1_q,
       s_r_ff_2_q, s_r_ff_3_q, s_r_ff_4_q, s_r_ff_5_q;

  not not_1 (not_1_out, clock);
  Comparator #(.width(12)) comparator_1 (.a(control_bus[11:0]), .b(12'ha0), .eq(comparator_1_eq));  // open: gt, lt
  Comparator #(.width(12)) comparator_2 (.a(control_bus[11:0]), .b(12'ha1), .eq(comparator_2_eq));  // open: gt, lt
  Comparator #(.width(12)) comparator_3 (.a(control_bus[11:0]), .b(12'ha2), .eq(comparator_3_eq));  // open: gt, lt
  Comparator #(.width(12)) comparator_4 (.a(control_bus[11:0]), .b(12'ha3), .eq(comparator_4_eq));  // open: gt, lt
  Comparator comparator_5 (.a(control_bus[7:0]), .b(8'ha4), .eq(comparator_5_eq));  // open: gt, lt
  Comparator comparator_6 (.a(control_bus[7:0]), .b(8'ha5), .eq(comparator_6_eq));  // open: gt, lt
  Decoder #(.enable("false"), .select(3)) decoder_1 (
    .out0(decoder_1_out0), .out1(decoder_1_out1), .out2(decoder_1_out2), .out3(decoder_1_out3),
    .out4(decoder_1_out4), .out5(decoder_1_out5), .out6(decoder_1_out6), .out7(decoder_1_out7),
    .sel(control_bus[14:12]));
  or or_1 (or_1_out, comparator_6_eq, comparator_4_eq, comparator_3_eq);
  or or_2 (or_2_out, comparator_2_eq, comparator_1_eq);
  or or_3 (or_3_out, ~comparator_1_eq, comparator_2_eq);  // OR_Gate
  and and_1 (and_1_out, decoder_1_out0, or_1_out, not_1_out);
  and and_2 (and_2_out, decoder_1_out0, or_2_out, not_1_out);
  or or_4 (or_4_out, data_bus_in[0], data_bus_in[1], data_bus_in[2], data_bus_in[3], data_bus_in[4], data_bus_in[5], data_bus_in[6], data_bus_in[7], data_bus_in[8], data_bus_in[9], data_bus_in[10], data_bus_in[11], data_bus_in[12], data_bus_in[13], data_bus_in[14], data_bus_in[15]);
  Multiplexer #(.enable("true")) multiplexer_1 (
    .in0(or_4_out), .in1(1'b1), .out(multiplexer_1_out), .sel(comparator_4_eq), .en(not_2_out));
  not not_2 (not_2_out, comparator_3_eq);
  D_Flip_Flop d_ff_1 (.D(multiplexer_1_out), .clk(and_1_out), .Q(out_14), .reset(reset));  // open: Qn, preset
  D_Flip_Flop d_ff_2 (.D(or_3_out), .clk(and_2_out), .Q(out_15), .reset(reset));  // open: Qn, preset
  and and_3 (and_3_out, decoder_1_out0, in_5);
  D_Flip_Flop d_ff_3 (.D(multiplexer_1_out), .clk(and_4_out), .Q(out_16), .reset(reset));  // open: Qn, preset
  and and_4 (and_4_out, decoder_1_out1, or_1_out, not_1_out);
  D_Flip_Flop d_ff_4 (.D(or_3_out), .clk(and_5_out), .Q(out_17), .reset(reset));  // open: Qn, preset
  and and_5 (and_5_out, decoder_1_out1, or_2_out, not_1_out);
  and and_6 (and_6_out, decoder_1_out1, in_6);
  or or_5 (or_5_out, and_3_out, and_6_out);
  D_Flip_Flop d_ff_5 (.D(multiplexer_1_out), .clk(and_7_out), .Q(out_18), .reset(reset));  // open: Qn, preset
  and and_7 (and_7_out, decoder_1_out2, or_1_out, not_1_out);
  D_Flip_Flop d_ff_6 (.D(or_3_out), .clk(and_8_out), .Q(out_19), .reset(reset));  // open: Qn, preset
  and and_8 (and_8_out, decoder_1_out2, or_2_out, not_1_out);
  or or_6 (or_6_out, or_5_out, and_9_out);
  and and_9 (and_9_out, decoder_1_out2, in_7);
  and and_10 (and_10_out, decoder_1_out3, or_1_out, not_1_out);
  and and_11 (and_11_out, decoder_1_out3, or_2_out, not_1_out);
  D_Flip_Flop d_ff_7 (.D(multiplexer_1_out), .clk(and_10_out), .Q(out_20), .reset(reset));  // open: Qn, preset
  D_Flip_Flop d_ff_8 (.D(or_3_out), .clk(and_11_out), .Q(out_21), .reset(reset));  // open: Qn, preset
  or or_7 (or_7_out, or_6_out, and_12_out);
  and and_12 (and_12_out, decoder_1_out3, in_8);
  and and_13 (and_13_out, decoder_1_out4, or_1_out, not_1_out);
  and and_14 (and_14_out, decoder_1_out4, or_2_out, not_1_out);
  D_Flip_Flop d_ff_9 (.D(multiplexer_1_out), .clk(and_13_out), .Q(out_22), .reset(reset));  // open: Qn, preset
  D_Flip_Flop d_ff_10 (.D(or_3_out), .clk(and_14_out), .Q(out_23), .reset(reset));  // open: Qn, preset
  and and_15 (and_15_out, decoder_1_out4, in_9);
  or or_8 (or_8_out, or_7_out, and_15_out);
  D_Flip_Flop d_ff_11 (.D(multiplexer_1_out), .clk(and_16_out), .Q(out_24), .reset(reset));  // open: Qn, preset
  and and_16 (and_16_out, decoder_1_out5, or_1_out, not_1_out);
  D_Flip_Flop d_ff_12 (.D(or_3_out), .clk(and_17_out), .Q(out_25), .reset(reset));  // open: Qn, preset
  and and_17 (and_17_out, decoder_1_out5, or_2_out, not_1_out);
  and and_18 (and_18_out, decoder_1_out5, in_10);
  or or_9 (or_9_out, or_8_out, and_18_out);
  D_Flip_Flop d_ff_13 (.D(multiplexer_1_out), .clk(and_19_out), .Q(out_26), .reset(reset));  // open: Qn, preset
  and and_19 (and_19_out, decoder_1_out6, or_1_out, not_1_out);
  D_Flip_Flop d_ff_14 (.D(or_3_out), .clk(and_20_out), .Q(out_27), .reset(reset));  // open: Qn, preset
  and and_20 (and_20_out, decoder_1_out6, or_2_out, not_1_out);
  or or_10 (or_10_out, or_9_out, and_21_out);
  and and_21 (and_21_out, decoder_1_out6, in_11);
  and and_22 (and_22_out, decoder_1_out7, or_1_out, not_1_out);
  and and_23 (and_23_out, decoder_1_out7, or_2_out, not_1_out);
  D_Flip_Flop d_ff_15 (.D(multiplexer_1_out), .clk(and_22_out), .Q(out_28), .reset(reset));  // open: Qn, preset
  D_Flip_Flop d_ff_16 (.D(or_3_out), .clk(and_23_out), .Q(out_29), .reset(reset));  // open: Qn, preset
  or or_11 (or_11_out, or_10_out, and_24_out);
  and and_24 (and_24_out, decoder_1_out7, in_12);
  and and_25 (and_25_out, comparator_5_eq, or_11_out);
  S_R_Flip_Flop s_r_ff_1 (.Q(s_r_ff_1_q), .reset(or_14_out), .preset(and_25_out));  // open: S, R, clk, Qn
  S_R_Flip_Flop s_r_ff_2 (
    .S(s_r_ff_1_q), .R(1'b0), .clk(not_1_out), .Q(s_r_ff_2_q), .reset(or_14_out));  // open: Qn, preset
  S_R_Flip_Flop s_r_ff_3 (
    .S(s_r_ff_2_q), .R(1'b0), .clk(not_1_out), .Q(s_r_ff_3_q), .reset(or_14_out));  // open: Qn, preset
  or or_12 (data_bus_out[0], s_r_ff_1_q, s_r_ff_2_q, s_r_ff_3_q);
  S_R_Flip_Flop #(.trigger("falling")) s_r_ff_4 (
    .S(s_r_ff_3_q), .R(1'b0), .clk(not_1_out), .Q(s_r_ff_4_q), .reset(or_13_out));  // open: Qn, preset
  buf buffer_1 (buffer_1_out, or_14_out);
  buf buffer_2 (buffer_2_out, buffer_1_out);
  or or_13 (or_13_out, reset, s_r_ff_5_q);
  buf buffer_3 (buffer_3_out, buffer_2_out);
  buf buffer_4 (buffer_4_out, buffer_3_out);
  S_R_Flip_Flop s_r_ff_5 (
    .S(buffer_4_out), .R(not_3_out), .clk(not_1_out), .Q(s_r_ff_5_q), .reset(reset));  // open: Qn, preset
  not not_3 (not_3_out, or_14_out);
  or or_14 (or_14_out, s_r_ff_4_q, reset);

  assign data_bus_out[15:1] = {15{1'b0}};
endmodule

module io_pins_16 (
  input  [15:0] control_bus,
  input  [15:0] data_bus_in,
  input  clock,
  input  reset,
  input  in_5,
  input  in_6,
  input  in_7,
  input  in_8,
  input  in_9,
  input  in_10,
  input  in_11,
  input  in_12,
  input  in_13,
  input  in_14,
  input  in_15,
  input  in_16,
  input  in_17,
  input  in_18,
  input  in_19,
  input  in_20,
  output [15:0] data_bus_out,
  output out_22,
  output out_23,
  output out_24,
  output out_25,
  output out_26,
  output out_27,
  output out_28,
  output out_29,
  output out_30,
  output out_31,
  output out_32,
  output out_33,
  output out_34,
  output out_35,
  output out_36,
  output out_37,
  output out_38,
  output out_39,
  output out_40,
  output out_41,
  output out_42,
  output out_43,
  output out_44,
  output out_45,
  output out_46,
  output out_47,
  output out_48,
  output out_49,
  output out_50,
  output out_51,
  output out_52,
  output out_53
);

  wire and_1_out, and_2_out, and_3_out, and_4_out, and_5_out, and_6_out, and_7_out, and_8_out, and_9_out,
       and_10_out, and_11_out, and_12_out, and_13_out, and_14_out, and_15_out, and_16_out, and_17_out,
       and_18_out, and_19_out, and_20_out, and_21_out, and_22_out, and_23_out, and_24_out, and_25_out,
       and_26_out, and_27_out, and_28_out, and_29_out, and_30_out, and_31_out, and_32_out, and_33_out,
       and_34_out, and_35_out, and_36_out, and_37_out, and_38_out, and_39_out, and_40_out, and_41_out,
       and_42_out, and_43_out, and_44_out, and_45_out, and_46_out, and_47_out, and_48_out, and_49_out,
       and_50_out, buffer_1_out, buffer_2_out, buffer_3_out, buffer_4_out, comparator_1_eq, comparator_2_eq,
       comparator_3_eq, comparator_4_eq, comparator_5_eq, comparator_6_eq, decoder_1_out0, decoder_1_out1,
       decoder_1_out2, decoder_1_out3, decoder_1_out4, decoder_1_out5, decoder_1_out6, decoder_1_out7,
       decoder_1_out8, decoder_1_out9, decoder_1_out10, decoder_1_out11, decoder_1_out12, decoder_1_out13,
       decoder_1_out14, decoder_1_out15, multiplexer_1_out, not_1_out, not_2_out, not_3_out, not_4_out,
       or_1_out, or_2_out, or_3_out, or_4_out, or_5_out, or_6_out, or_7_out, or_8_out, or_9_out, or_10_out,
       or_11_out, or_12_out, or_13_out, or_14_out, or_15_out, or_16_out, or_17_out, or_18_out, or_19_out,
       or_21_out, or_22_out, s_r_ff_1_q, s_r_ff_2_q, s_r_ff_3_q, s_r_ff_4_q, s_r_ff_5_q;

  not not_1 (not_1_out, clock);
  Comparator #(.width(12)) comparator_1 (.a(control_bus[11:0]), .b(12'ha0), .eq(comparator_1_eq));  // open: gt, lt
  Comparator #(.width(12)) comparator_2 (.a(control_bus[11:0]), .b(12'ha1), .eq(comparator_2_eq));  // open: gt, lt
  Comparator #(.width(12)) comparator_3 (.a(control_bus[11:0]), .b(12'ha2), .eq(comparator_3_eq));  // open: gt, lt
  Comparator #(.width(12)) comparator_4 (.a(control_bus[11:0]), .b(12'ha3), .eq(comparator_4_eq));  // open: gt, lt
  Comparator comparator_5 (.a(control_bus[7:0]), .b(8'ha4), .eq(comparator_5_eq));  // open: gt, lt
  Comparator comparator_6 (.a(control_bus[7:0]), .b(8'ha5), .eq(comparator_6_eq));  // open: gt, lt
  Decoder #(.enable("false"), .select(4)) decoder_1 (
    .out0(decoder_1_out0), .out1(decoder_1_out1), .out2(decoder_1_out2), .out3(decoder_1_out3),
    .out4(decoder_1_out4), .out5(decoder_1_out5), .out6(decoder_1_out6), .out7(decoder_1_out7),
    .out8(decoder_1_out8), .out9(decoder_1_out9), .out10(decoder_1_out10), .out11(decoder_1_out11),
    .out12(decoder_1_out12), .out13(decoder_1_out13), .out14(decoder_1_out14), .out15(decoder_1_out15),
    .sel(control_bus[15:12]));
  or or_1 (or_1_out, comparator_6_eq, comparator_4_eq, comparator_3_eq);
  or or_2 (or_2_out, comparator_2_eq, comparator_1_eq);
  or or_3 (or_3_out, ~comparator_1_eq, comparator_2_eq);  // OR_Gate
  and and_1 (and_1_out, decoder_1_out0, or_1_out, not_1_out);
  and and_2 (and_2_out, decoder_1_out0, or_2_out, not_1_out);
  or or_4 (or_4_out, data_bus_in[0], data_bus_in[1], data_bus_in[2], data_bus_in[3], data_bus_in[4], data_bus_in[5], data_bus_in[6], data_bus_in[7], data_bus_in[8], data_bus_in[9], data_bus_in[10], data_bus_in[11], data_bus_in[12], data_bus_in[13], data_bus_in[14], data_bus_in[15]);
  Multiplexer #(.enable("true")) multiplexer_1 (
    .in0(or_4_out), .in1(1'b1), .out(multiplexer_1_out), .sel(comparator_4_eq), .en(not_2_out));
  not not_2 (not_2_out, comparator_3_eq);
  D_Flip_Flop d_ff_1 (.D(multiplexer_1_out), .clk(and_1_out), .Q(out_22), .reset(reset));  // open: Qn, preset
  D_Flip_Flop d_ff_2 (.D(or_3_out), .clk(and_2_out), .Q(out_23), .reset(reset));  // open: Qn, preset
  and and_3 (and_3_out, decoder_1_out0, in_5);
  D_Flip_Flop d_ff_3 (.D(multiplexer_1_out), .clk(and_4_out), .Q(out_24), .reset(reset));  // open: Qn, preset
  and and_4 (and_4_out, decoder_1_out1, or_1_out, not_1_out);
  D_Flip_Flop d_ff_4 (.D(or_3_out), .clk(and_5_out), .Q(out_25), .reset(reset));  // open: Qn, preset
  and and_5 (and_5_out, decoder_1_out1, or_2_out, not_1_out);
  and and_6 (and_6_out, decoder_1_out1, in_6);
  or or_5 (or_5_out, and_3_out, and_6_out);
  D_Flip_Flop d_ff_5 (.D(multiplexer_1_out), .clk(and_7_out), .Q(out_26), .reset(reset));  // open: Qn, preset
  and and_7 (and_7_out, decoder_1_out2, or_1_out, not_1_out);
  D_Flip_Flop d_ff_6 (.D(or_3_out), .clk(and_8_out), .Q(out_27), .reset(reset));  // open: Qn, preset
  and and_8 (and_8_out, decoder_1_out2, or_2_out, not_1_out);
  or or_6 (or_6_out, or_5_out, and_9_out);
  and and_9 (and_9_out, decoder_1_out2, in_7);
  and and_10 (and_10_out, decoder_1_out3, or_1_out, not_1_out);
  and and_11 (and_11_out, decoder_1_out3, or_2_out, not_1_out);
  D_Flip_Flop d_ff_7 (.D(multiplexer_1_out), .clk(and_10_out), .Q(out_28), .reset(reset));  // open: Qn, preset
  D_Flip_Flop d_ff_8 (.D(or_3_out), .clk(and_11_out), .Q(out_29), .reset(reset));  // open: Qn, preset
  or or_7 (or_7_out, or_6_out, and_12_out);
  and and_12 (and_12_out, decoder_1_out3, in_8);
  and and_13 (and_13_out, decoder_1_out4, or_1_out, not_1_out);
  and and_14 (and_14_out, decoder_1_out4, or_2_out, not_1_out);
  D_Flip_Flop d_ff_9 (.D(multiplexer_1_out), .clk(and_13_out), .Q(out_30), .reset(reset));  // open: Qn, preset
  D_Flip_Flop d_ff_10 (.D(or_3_out), .clk(and_14_out), .Q(out_31), .reset(reset));  // open: Qn, preset
  and and_15 (and_15_out, decoder_1_out4, in_9);
  or or_8 (or_8_out, or_7_out, and_15_out);
  D_Flip_Flop d_ff_11 (.D(multiplexer_1_out), .clk(and_16_out), .Q(out_32), .reset(reset));  // open: Qn, preset
  and and_16 (and_16_out, decoder_1_out5, or_1_out, not_1_out);
  D_Flip_Flop d_ff_12 (.D(or_3_out), .clk(and_17_out), .Q(out_33), .reset(reset));  // open: Qn, preset
  and and_17 (and_17_out, decoder_1_out5, or_2_out, not_1_out);
  and and_18 (and_18_out, decoder_1_out5, in_10);
  or or_9 (or_9_out, or_8_out, and_18_out);
  D_Flip_Flop d_ff_13 (.D(multiplexer_1_out), .clk(and_19_out), .Q(out_34), .reset(reset));  // open: Qn, preset
  and and_19 (and_19_out, decoder_1_out6, or_1_out, not_1_out);
  D_Flip_Flop d_ff_14 (.D(or_3_out), .clk(and_20_out), .Q(out_35), .reset(reset));  // open: Qn, preset
  and and_20 (and_20_out, decoder_1_out6, or_2_out, not_1_out);
  or or_10 (or_10_out, or_9_out, and_21_out);
  and and_21 (and_21_out, decoder_1_out6, in_11);
  and and_22 (and_22_out, decoder_1_out7, or_1_out, not_1_out);
  and and_23 (and_23_out, decoder_1_out7, or_2_out, not_1_out);
  D_Flip_Flop d_ff_15 (.D(multiplexer_1_out), .clk(and_22_out), .Q(out_36), .reset(reset));  // open: Qn, preset
  D_Flip_Flop d_ff_16 (.D(or_3_out), .clk(and_23_out), .Q(out_37), .reset(reset));  // open: Qn, preset
  or or_11 (or_11_out, or_10_out, and_24_out);
  and and_24 (and_24_out, decoder_1_out7, in_12);
  and and_25 (and_25_out, decoder_1_out8, or_1_out, not_1_out);
  and and_26 (and_26_out, decoder_1_out8, or_2_out, not_1_out);
  D_Flip_Flop d_ff_17 (.D(multiplexer_1_out), .clk(and_25_out), .Q(out_38), .reset(reset));  // open: Qn, preset
  D_Flip_Flop d_ff_18 (.D(or_3_out), .clk(and_26_out), .Q(out_39), .reset(reset));  // open: Qn, preset
  and and_27 (and_27_out, decoder_1_out8, in_13);
  or or_12 (or_12_out, or_11_out, and_27_out);
  D_Flip_Flop d_ff_19 (.D(multiplexer_1_out), .clk(and_28_out), .Q(out_40), .reset(reset));  // open: Qn, preset
  and and_28 (and_28_out, decoder_1_out9, or_1_out, not_1_out);
  D_Flip_Flop d_ff_20 (.D(or_3_out), .clk(and_29_out), .Q(out_41), .reset(reset));  // open: Qn, preset
  and and_29 (and_29_out, decoder_1_out9, or_2_out, not_1_out);
  and and_30 (and_30_out, decoder_1_out9, in_14);
  or or_13 (or_13_out, or_12_out, and_30_out);
  D_Flip_Flop d_ff_21 (.D(multiplexer_1_out), .clk(and_31_out), .Q(out_42), .reset(reset));  // open: Qn, preset
  and and_31 (and_31_out, decoder_1_out10, or_1_out, not_1_out);
  D_Flip_Flop d_ff_22 (.D(or_3_out), .clk(and_32_out), .Q(out_43), .reset(reset));  // open: Qn, preset
  and and_32 (and_32_out, decoder_1_out10, or_2_out, not_1_out);
  or or_14 (or_14_out, or_13_out, and_33_out);
  and and_33 (and_33_out, decoder_1_out10, in_15);
  and and_34 (and_34_out, decoder_1_out11, or_1_out, not_1_out);
  and and_35 (and_35_out, decoder_1_out11, or_2_out, not_1_out);
  D_Flip_Flop d_ff_23 (.D(multiplexer_1_out), .clk(and_34_out), .Q(out_44), .reset(reset));  // open: Qn, preset
  D_Flip_Flop d_ff_24 (.D(or_3_out), .clk(and_35_out), .Q(out_45), .reset(reset));  // open: Qn, preset
  or or_15 (or_15_out, or_14_out, and_36_out);
  and and_36 (and_36_out, decoder_1_out11, in_16);
  and and_37 (and_37_out, decoder_1_out12, or_1_out, not_1_out);
  and and_38 (and_38_out, decoder_1_out12, or_2_out, not_1_out);
  D_Flip_Flop d_ff_25 (.D(multiplexer_1_out), .clk(and_37_out), .Q(out_46), .reset(reset));  // open: Qn, preset
  D_Flip_Flop d_ff_26 (.D(or_3_out), .clk(and_38_out), .Q(out_47), .reset(reset));  // open: Qn, preset
  and and_39 (and_39_out, decoder_1_out12, in_17);
  or or_16 (or_16_out, or_15_out, and_39_out);
  D_Flip_Flop d_ff_27 (.D(multiplexer_1_out), .clk(and_40_out), .Q(out_48), .reset(reset));  // open: Qn, preset
  and and_40 (and_40_out, decoder_1_out13, or_1_out, not_1_out);
  D_Flip_Flop d_ff_28 (.D(or_3_out), .clk(and_41_out), .Q(out_49), .reset(reset));  // open: Qn, preset
  and and_41 (and_41_out, decoder_1_out13, or_2_out, not_1_out);
  and and_42 (and_42_out, decoder_1_out13, in_18);
  or or_17 (or_17_out, or_16_out, and_42_out);
  D_Flip_Flop d_ff_29 (.D(multiplexer_1_out), .clk(and_43_out), .Q(out_50), .reset(reset));  // open: Qn, preset
  and and_43 (and_43_out, decoder_1_out14, or_1_out, not_1_out);
  D_Flip_Flop d_ff_30 (.D(or_3_out), .clk(and_44_out), .Q(out_51), .reset(reset));  // open: Qn, preset
  and and_44 (and_44_out, decoder_1_out14, or_2_out, not_1_out);
  or or_18 (or_18_out, or_17_out, and_45_out);
  and and_45 (and_45_out, decoder_1_out14, in_19);
  and and_46 (and_46_out, decoder_1_out15, or_1_out, not_1_out);
  and and_47 (and_47_out, decoder_1_out15, or_2_out, not_1_out);
  and and_48 (and_48_out, multiplexer_1_out, and_46_out);
  not not_3 (not_3_out, not_1_out);
  D_Flip_Flop d_ff_31 (.D(or_3_out), .clk(and_47_out), .Q(out_53), .reset(reset));  // open: Qn, preset
  or or_19 (or_19_out, or_18_out, and_49_out);
  two_ticker two_ticker_1 (.signal_in(and_48_out), .clock(not_3_out), .reset(reset), .out_4(out_52));
  and and_49 (and_49_out, decoder_1_out15, in_20);
  and and_50 (and_50_out, comparator_5_eq, or_19_out);
  S_R_Flip_Flop s_r_ff_1 (.Q(s_r_ff_1_q), .reset(or_22_out), .preset(and_50_out));  // open: S, R, clk, Qn
  S_R_Flip_Flop s_r_ff_2 (
    .S(s_r_ff_1_q), .R(1'b0), .clk(not_1_out), .Q(s_r_ff_2_q), .reset(or_22_out));  // open: Qn, preset
  S_R_Flip_Flop s_r_ff_3 (
    .S(s_r_ff_2_q), .R(1'b0), .clk(not_1_out), .Q(s_r_ff_3_q), .reset(or_22_out));  // open: Qn, preset
  or or_20 (data_bus_out[0], s_r_ff_1_q, s_r_ff_2_q, s_r_ff_3_q);
  S_R_Flip_Flop #(.trigger("falling")) s_r_ff_4 (
    .S(s_r_ff_3_q), .R(1'b0), .clk(not_1_out), .Q(s_r_ff_4_q), .reset(or_21_out));  // open: Qn, preset
  buf buffer_1 (buffer_1_out, or_22_out);
  buf buffer_2 (buffer_2_out, buffer_1_out);
  or or_21 (or_21_out, reset, s_r_ff_5_q);
  buf buffer_3 (buffer_3_out, buffer_2_out);
  buf buffer_4 (buffer_4_out, buffer_3_out);
  S_R_Flip_Flop s_r_ff_5 (
    .S(buffer_4_out), .R(not_4_out), .clk(not_1_out), .Q(s_r_ff_5_q), .reset(reset));  // open: Qn, preset
  not not_4 (not_4_out, or_22_out);
  or or_22 (or_22_out, s_r_ff_4_q, reset);

  assign data_bus_out[15:1] = {15{1'b0}};
endmodule

module mmio_registers (
  input  [15:0] data_in,
  input  [1:0] reg_select,
  input  write,
  input  clock,
  input  reset,
  output [15:0] out_6,
  output [15:0] out_7,
  output [15:0] out_8,
  output [15:0] out_9
);

  wire and_1_out, and_2_out, and_3_out, and_4_out, decoder_1_out0, decoder_1_out1, decoder_1_out2,
       decoder_1_out3;

  Decoder #(.enable("false"), .select(2)) decoder_1 (
    .out0(decoder_1_out0), .out1(decoder_1_out1), .out2(decoder_1_out2), .out3(decoder_1_out3),
    .sel(reg_select));
  Register #(.width(16)) register_1 (.D(data_in), .en(and_1_out), .clk(clock), .Q(out_6), .clr(reset));
  and and_1 (and_1_out, decoder_1_out0, write);
  Register #(.width(16)) register_2 (.D(data_in), .en(and_2_out), .clk(clock), .Q(out_7), .clr(reset));
  and and_2 (and_2_out, write, decoder_1_out1);
  Register #(.width(16)) register_3 (.D(data_in), .en(and_3_out), .clk(clock), .Q(out_8), .clr(reset));
  and and_3 (and_3_out, write, decoder_1_out2);
  Register #(.width(16)) register_4 (.D(data_in), .en(and_4_out), .clk(clock), .Q(out_9), .clr(reset));
  and and_4 (and_4_out, write, decoder_1_out3);
endmodule

module spi_driver (
  input  write,
  input  read,
  input  [15:0] spi_out_config,
  input  [15:0] data_in,
  input  [15:0] spi_in_config,
  input  clock,
  input  reset,
  input  miso,
  output [15:0] data_out,
  output done,
  output cs,
  output clk,
  output mosi
);

  wire and_1_out, and_2_out, and_3_out, and_4_out, and_5_out, and_6_out, and_7_out, and_8_out, and_9_out,
       and_10_out, and_11_out, and_12_out, and_13_out, and_14_out, and_15_out, clock_division_bell_1_out_6,
       comparator_1_gt, comparator_2_eq, comparator_3_lt, comparator_4_gt, comparator_5_eq,
       falling_edge_delay_1_out_2, falling_edge_delay_2_out_2, nor_1_out, not_2_out, not_or_hasnt_1_out_2,
       not_or_hasnt_2_out_2, or_1_out, or_2_out, or_6_out, or_7_out, or_8_out, or_10_out, or_11_out,
       or_12_out, pulse_extender_1_out_6, rising_edge_delay_1_out_2, rising_edge_delay_2_out_2,
       rising_edge_delay_4_out_2, s_r_ff_1_q, s_r_ff_2_q, s_r_ff_3_q, s_r_ff_4_q, shift_register_1_p3,
       shift_register_1_p4, shift_register_2_p1, shift_register_2_p4, shift_register_2_p15,
       shift_register_2_p16, shift_register_3_p1, shift_register_3_p2, shift_register_3_p3,
       two_ticker_1_out_4, two_ticker_2_out_4, two_ticker_3_out_4, two_ticker_4_out_4;
  wire [1:0] bytes_to_write_q;
  wire [4:0] adder_1_out, adder_2_out, kounter_q, multiplexer_1_out, register_2_q;
  wire [15:0] register_1_q, undriven;

  two_ticker two_ticker_1 (.signal_in(s_r_ff_1_q), .clock(clock), .reset(reset), .out_4(two_ticker_1_out_4));
  Register #(.width(2)) bytes_to_write (
    .D(spi_out_config[1:0]), .clk(two_ticker_1_out_4), .Q(bytes_to_write_q), .clr(reset));  // open: en
  clock_division_bell clock_division_bell_1 (
    .divisor(spi_out_config[15:8]), .load_divisor(two_ticker_1_out_4), .restart(two_ticker_1_out_4),
    .clock(clock), .reset(reset), .out_6(clock_division_bell_1_out_6));
  Comparator #(.mode("unsigned"), .width(2)) comparator_1 (
    .a(bytes_to_write_q), .b(2'b01), .gt(comparator_1_gt));  // open: eq, lt
  Register #(.width(16)) register_1 (.D(data_in), .clk(s_r_ff_1_q), .Q(register_1_q), .clr(reset));  // open: en
  // Shift_Register shift_register_1: pin names not known; wires that end beside it: reset, two_ticker_1_out_4, shift_register_1_p3, shift_register_1_p4, 1'b0, register_1_q[0], register_1_q[1], register_1_q[2], register_1_q[3], register_1_q[4], register_1_q[5], register_1_q[6], register_1_q[7]
  or or_1 (or_1_out, s_r_ff_1_q, shift_register_3_p2);
  not not_1 (cs, or_1_out);
  and and_1 (and_1_out, write, ~shift_register_3_p2);  // AND_Gate
  not_or_hasnt not_or_hasnt_1 (.in_1(and_1_out), .out_2(not_or_hasnt_1_out_2));
  and and_2 (and_2_out, and_1_out, falling_edge_delay_1_out_2);
  S_R_Flip_Flop s_r_ff_1 (.Q(s_r_ff_1_q), .reset(or_2_out), .preset(and_2_out));  // open: S, R, clk, Qn
  or or_2 (or_2_out, reset, two_ticker_3_out_4);
  or or_3 (shift_register_1_p3, and_11_out, and_12_out);
  and and_3 (and_3_out, s_r_ff_1_q, clock_division_bell_1_out_6);
  and and_4 (and_4_out, or_12_out, shift_register_3_p2);
  or or_4 (clk, and_3_out, and_4_out);
  falling_edge_delay falling_edge_delay_1 (.in_1(not_or_hasnt_1_out_2), .out_2(falling_edge_delay_1_out_2));
  and and_5 (and_5_out, s_r_ff_1_q, ~rising_edge_delay_4_out_2);  // AND_Gate
  S_R_Flip_Flop #(.trigger("falling")) s_r_ff_2 (
    .S(1'b0), .R(1'b1), .clk(clock), .Q(s_r_ff_2_q), .reset(reset), .preset(and_5_out));  // open: Qn
  and and_6 (and_6_out, shift_register_2_p1, and_11_out);
  or or_5 (mosi, and_6_out, and_8_out);
  or or_6 (or_6_out, reset, two_ticker_3_out_4);
  and and_7 (and_7_out, ~s_r_ff_2_q, clock_division_bell_1_out_6);  // AND_Gate
  // Shift_Register shift_register_2: pin names not known; wires that end beside it: shift_register_2_p1, reset, two_ticker_1_out_4, shift_register_2_p4, shift_register_1_p4, 1'b0, register_1_q[8], register_1_q[9], register_1_q[10], register_1_q[11], register_1_q[12], register_1_q[13], register_1_q[14], register_1_q[15], shift_register_2_p15, shift_register_2_p16
  S_R_Flip_Flop #(.trigger("falling")) s_r_ff_3 (
    .Q(s_r_ff_3_q), .reset(or_6_out), .preset(s_r_ff_2_q));  // open: S, R, clk, Qn
  rising_edge_delay rising_edge_delay_1 (.in_1(s_r_ff_2_q), .out_2(rising_edge_delay_1_out_2));
  rising_edge_delay rising_edge_delay_2 (.in_1(s_r_ff_1_q), .out_2(rising_edge_delay_2_out_2));
  rising_edge_delay rising_edge_delay_3 (.in_1(and_12_out), .out_2(shift_register_2_p4));
  rising_edge_delay rising_edge_delay_4 (.in_1(s_r_ff_3_q), .out_2(rising_edge_delay_4_out_2));
  or or_7 (or_7_out, rising_edge_delay_1_out_2, and_7_out);
  and and_8 (and_8_out, shift_register_2_p15, and_12_out);
  and and_9 (and_9_out, read, ~s_r_ff_1_q);  // AND_Gate
  rising_edge_delay rising_edge_delay_5 (.in_1(or_7_out), .out_2(shift_register_1_p4));
  Register #(.width(5)) kounter (
    .D(adder_1_out), .en(rising_edge_delay_2_out_2), .clk(and_10_out), .Q(kounter_q), .clr(or_8_out));
  and and_10 (and_10_out, clock, s_r_ff_1_q);
  or or_8 (or_8_out, reset, two_ticker_3_out_4);
  // Shift_Register #(.length(16)) shift_register_3: pin names not known; wires that end beside it: shift_register_3_p1, shift_register_3_p2, shift_register_3_p3, miso
  or or_9 (shift_register_3_p1, two_ticker_4_out_4, reset);
  Adder #(.width(5)) adder_1 (.a(kounter_q), .b(5'b00001), .out(adder_1_out));  // open: cin, cout
  Comparator #(.mode("unsigned"), .width(5)) comparator_2 (
    .a(kounter_q), .b(5'b10000), .eq(comparator_2_eq));  // open: gt, lt
  Comparator #(.mode("unsigned"), .width(5)) comparator_3 (
    .a(kounter_q), .b(5'b00001), .lt(comparator_3_lt));  // open: gt, eq
  Comparator #(.mode("unsigned"), .width(5)) comparator_4 (
    .a(kounter_q), .b(5'b01000), .gt(comparator_4_gt));  // open: eq, lt
  and and_11 (and_11_out, ~comparator_3_lt, ~comparator_4_gt);  // AND_Gate
  and and_12 (and_12_out, comparator_4_gt, comparator_1_gt);
  and and_13 (and_13_out, and_9_out, falling_edge_delay_2_out_2);
  S_R_Flip_Flop s_r_ff_4 (.Q(s_r_ff_4_q), .reset(or_11_out), .preset(and_13_out));  // open: S, R, clk, Qn
  two_ticker two_ticker_2 (.signal_in(shift_register_3_p2), .clock(clock), .reset(reset), .out_4(two_ticker_2_out_4));
  and and_14 (and_14_out, comparator_2_eq, comparator_1_gt);
  or or_10 (or_10_out, and_14_out, and_15_out);
  and and_15 (and_15_out, comparator_4_gt, ~comparator_1_gt);  // AND_Gate
  not_or_hasnt not_or_hasnt_2 (.in_1(and_9_out), .out_2(not_or_hasnt_2_out_2));
  S_R_Flip_Flop s_r_ff_5 (
    .S(s_r_ff_4_q), .R(not_2_out), .clk(clock), .Q(shift_register_3_p2), .reset(or_11_out));  // open: Qn, preset
  not not_2 (not_2_out, s_r_ff_4_q);
  two_ticker two_ticker_3 (.signal_in(or_10_out), .clock(clock), .reset(reset), .out_4(two_ticker_3_out_4));
  falling_edge_delay falling_edge_delay_2 (.in_1(not_or_hasnt_2_out_2), .out_2(falling_edge_delay_2_out_2));
  clock_division_bell clock_division_bell_2 (
    .divisor(spi_out_config[15:8]), .load_divisor(two_ticker_2_out_4), .clock(clock), .reset(reset),
    .out_6(shift_register_3_p3));  // open: restart
  nor nor_1 (nor_1_out, spi_in_config[0], spi_in_config[1], spi_in_config[2], spi_in_config[3], spi_in_config[4]);
  Register #(.width(5)) register_2 (
    .D(adder_2_out), .en(shift_register_3_p2), .clk(shift_register_3_p3), .Q(register_2_q), .clr(or_11_out));
  or or_11 (or_11_out, reset, two_ticker_4_out_4);
  Multiplexer #(.width(5)) multiplexer_1 (
    .in0(spi_in_config[4:0]), .in1(5'b01000), .out(multiplexer_1_out), .sel(nor_1_out));
  Adder #(.width(5)) adder_2 (.a(register_2_q), .b(5'b00001), .out(adder_2_out));  // open: cin, cout
  Comparator #(.mode("unsigned"), .width(5)) comparator_5 (
    .a(register_2_q), .b(multiplexer_1_out), .eq(comparator_5_eq));  // open: gt, lt
  pulse_extender pulse_extender_1 (
    .in_1(comparator_5_eq), .in_2(reset), .in_3(or_12_out), .out_6(pulse_extender_1_out_6));  // open: out_4, out_5
  or or_12 (or_12_out, reset, two_ticker_2_out_4);
  two_ticker two_ticker_4 (
    .signal_in(pulse_extender_1_out_6), .clock(clock), .reset(or_12_out), .out_4(two_ticker_4_out_4));
  Register #(.width(16)) register_3 (.D(undriven), .clk(comparator_5_eq), .Q(data_out), .clr(reset));  // open: en
  or or_13 (done, two_ticker_3_out_4, two_ticker_4_out_4);
endmodule

module clock_division_bell (
  input  [7:0] divisor,
  input  load_divisor,
  input  restart,
  input  clock,
  input  reset,
  output out_6
);

  wire and_1_out, and_2_out, comparator_1_eq, j_k_ff_1_q, nor_1_out, not_1_out, or_1_out, or_2_out,
       rising_edge_delay_1_out_2;
  wire [7:0] adder_1_out, divisor_register_q, kounter_q, multiplexer_1_out, multiplexer_2_out,
       subtractor_1_out, subtractor_2_out;

  Subtractor subtractor_1 (.a(divisor), .b(8'h1), .out(subtractor_1_out));  // open: bin, bout
  Register divisor_register (.D(subtractor_1_out), .en(load_divisor), .clk(clock), .Q(divisor_register_q), .clr(reset));
  not not_1 (not_1_out, nor_1_out);
  Multiplexer #(.width(8)) multiplexer_1 (.in0({8{1'b0}}), .in1(adder_1_out), .out(multiplexer_1_out), .sel(not_1_out));
  Adder adder_1 (.a(kounter_q), .b(8'h1), .out(adder_1_out));  // open: cin, cout
  and and_1 (and_1_out, clock, ~load_divisor);  // AND_Gate
  or or_1 (or_1_out, load_divisor, restart, reset);
  Multiplexer #(.width(8)) multiplexer_2 (
    .in0(multiplexer_1_out), .in1({8{1'b1}}), .out(multiplexer_2_out), .sel(or_1_out));
  and and_2 (and_2_out, and_1_out, ~or_1_out);  // AND_Gate
  rising_edge_delay rising_edge_delay_1 (.in_1(or_1_out), .out_2(rising_edge_delay_1_out_2));
  Register kounter (.D(multiplexer_2_out), .en(1'b1), .clk(or_2_out), .Q(kounter_q));  // open: clr
  or or_2 (or_2_out, and_2_out, rising_edge_delay_1_out_2);
  Subtractor subtractor_2 (.a(kounter_q), .b(divisor_register_q), .out(subtractor_2_out));  // open: bin, bout
  Comparator #(.mode("unsigned")) comparator_1 (.a(divisor), .b({8{1'b0}}), .eq(comparator_1_eq));  // open: gt, lt
  nor nor_1 (nor_1_out, subtractor_2_out[0], subtractor_2_out[1], subtractor_2_out[2], subtractor_2_out[3], subtractor_2_out[4], subtractor_2_out[5], subtractor_2_out[6], subtractor_2_out[7]);
  J_K_Flip_Flop j_k_ff_1 (.J(1'b1), .K(1'b1), .clk(nor_1_out), .Q(j_k_ff_1_q), .reset(or_1_out));  // open: Qn, preset
  Multiplexer multiplexer_3 (.in0(j_k_ff_1_q), .in1(clock), .out(out_6), .sel(comparator_1_eq));
endmodule

module falling_edge_delay (
  input  in_1,
  output out_2
);

  wire buffer_1_out, buffer_2_out, buffer_3_out, buffer_4_out, buffer_5_out, buffer_6_out, buffer_7_out,
       buffer_8_out, buffer_9_out, buffer_10_out, buffer_11_out, buffer_12_out, buffer_13_out, buffer_14_out,
       buffer_15_out, buffer_16_out, buffer_17_out, buffer_18_out, buffer_19_out, buffer_20_out,
       buffer_21_out, buffer_22_out, buffer_23_out, buffer_24_out, buffer_25_out, buffer_26_out,
       buffer_27_out, buffer_28_out, buffer_29_out, buffer_30_out, buffer_31_out, buffer_32_out,
       buffer_33_out, buffer_34_out, buffer_35_out, buffer_36_out, buffer_37_out, buffer_38_out,
       buffer_39_out, buffer_40_out, buffer_41_out, buffer_42_out, buffer_43_out, buffer_44_out,
       buffer_45_out, buffer_46_out, buffer_47_out, buffer_48_out, buffer_49_out, buffer_50_out,
       buffer_51_out, buffer_52_out, buffer_53_out, buffer_54_out, buffer_55_out, buffer_56_out,
       buffer_57_out, buffer_58_out, buffer_59_out, buffer_60_out, buffer_61_out, buffer_62_out,
       buffer_63_out, buffer_64_out;

  buf buffer_1 (buffer_1_out, in_1);
  buf buffer_2 (buffer_2_out, buffer_1_out);
  buf buffer_3 (buffer_3_out, buffer_4_out);
  buf buffer_4 (buffer_4_out, buffer_5_out);
  buf buffer_5 (buffer_5_out, buffer_25_out);
  buf buffer_6 (buffer_6_out, buffer_3_out);
  buf buffer_7 (buffer_7_out, buffer_6_out);
  buf buffer_8 (buffer_8_out, buffer_9_out);
  buf buffer_9 (buffer_9_out, buffer_10_out);
  buf buffer_10 (buffer_10_out, buffer_33_out);
  buf buffer_11 (buffer_11_out, buffer_8_out);
  buf buffer_12 (buffer_12_out, buffer_11_out);
  buf buffer_13 (buffer_13_out, buffer_14_out);
  buf buffer_14 (buffer_14_out, buffer_15_out);
  buf buffer_15 (buffer_15_out, buffer_41_out);
  buf buffer_16 (buffer_16_out, buffer_13_out);
  buf buffer_17 (buffer_17_out, buffer_16_out);
  buf buffer_18 (buffer_18_out, buffer_19_out);
  buf buffer_19 (buffer_19_out, buffer_20_out);
  buf buffer_20 (buffer_20_out, buffer_49_out);
  buf buffer_21 (buffer_21_out, buffer_2_out);
  buf buffer_22 (buffer_22_out, buffer_21_out);
  buf buffer_23 (buffer_23_out, buffer_22_out);
  buf buffer_24 (buffer_24_out, buffer_23_out);
  buf buffer_25 (buffer_25_out, buffer_26_out);
  buf buffer_26 (buffer_26_out, buffer_27_out);
  buf buffer_27 (buffer_27_out, buffer_28_out);
  buf buffer_28 (buffer_28_out, buffer_55_out);
  buf buffer_29 (buffer_29_out, buffer_7_out);
  buf buffer_30 (buffer_30_out, buffer_29_out);
  buf buffer_31 (buffer_31_out, buffer_30_out);
  buf buffer_32 (buffer_32_out, buffer_31_out);
  buf buffer_33 (buffer_33_out, buffer_34_out);
  buf buffer_34 (buffer_34_out, buffer_35_out);
  buf buffer_35 (buffer_35_out, buffer_36_out);
  buf buffer_36 (buffer_36_out, buffer_58_out);
  buf buffer_37 (buffer_37_out, buffer_12_out);
  buf buffer_38 (buffer_38_out, buffer_37_out);
  buf buffer_39 (buffer_39_out, buffer_38_out);
  buf buffer_40 (buffer_40_out, buffer_39_out);
  buf buffer_41 (buffer_41_out, buffer_42_out);
  buf buffer_42 (buffer_42_out, buffer_43_out);
  buf buffer_43 (buffer_43_out, buffer_44_out);
  buf buffer_44 (buffer_44_out, buffer_61_out);
  buf buffer_45 (buffer_45_out, buffer_17_out);
  buf buffer_46 (buffer_46_out, buffer_45_out);
  buf buffer_47 (buffer_47_out, buffer_46_out);
  buf buffer_48 (buffer_48_out, buffer_47_out);
  buf buffer_49 (buffer_49_out, buffer_50_out);
  buf buffer_50 (buffer_50_out, buffer_51_out);
  buf buffer_51 (buffer_51_out, buffer_52_out);
  buf buffer_52 (buffer_52_out, buffer_64_out);
  or or_1 (out_2, buffer_18_out, in_1);
  buf buffer_53 (buffer_53_out, buffer_24_out);
  buf buffer_54 (buffer_54_out, buffer_53_out);
  buf buffer_55 (buffer_55_out, buffer_54_out);
  buf buffer_56 (buffer_56_out, buffer_32_out);
  buf buffer_57 (buffer_57_out, buffer_56_out);
  buf buffer_58 (buffer_58_out, buffer_57_out);
  buf buffer_59 (buffer_59_out, buffer_40_out);
  buf buffer_60 (buffer_60_out, buffer_59_out);
  buf buffer_61 (buffer_61_out, buffer_60_out);
  buf buffer_62 (buffer_62_out, buffer_48_out);
  buf buffer_63 (buffer_63_out, buffer_62_out);
  buf buffer_64 (buffer_64_out, buffer_63_out);
endmodule

module rising_edge_delay (
  input  in_1,
  output out_2
);

  wire buffer_1_out, buffer_2_out, buffer_3_out, buffer_4_out, buffer_5_out, buffer_6_out, buffer_7_out,
       buffer_8_out, buffer_9_out, buffer_10_out, buffer_11_out, buffer_12_out, buffer_13_out, buffer_14_out,
       buffer_15_out, buffer_16_out, buffer_17_out, buffer_18_out, buffer_19_out, buffer_20_out,
       buffer_21_out, buffer_22_out, buffer_23_out, buffer_24_out, buffer_25_out, buffer_26_out,
       buffer_27_out, buffer_28_out, buffer_29_out, buffer_30_out, buffer_31_out, buffer_32_out,
       buffer_33_out, buffer_34_out, buffer_35_out, buffer_36_out, buffer_37_out, buffer_38_out,
       buffer_39_out, buffer_40_out, buffer_41_out, buffer_42_out, buffer_43_out, buffer_44_out,
       buffer_45_out, buffer_46_out, buffer_47_out, buffer_48_out, buffer_49_out, buffer_50_out,
       buffer_51_out, buffer_52_out, buffer_53_out, buffer_54_out, buffer_55_out, buffer_56_out,
       buffer_57_out, buffer_58_out, buffer_59_out, buffer_60_out, buffer_61_out, buffer_62_out,
       buffer_63_out, buffer_64_out;

  buf buffer_1 (buffer_1_out, in_1);
  buf buffer_2 (buffer_2_out, buffer_1_out);
  buf buffer_3 (buffer_3_out, buffer_4_out);
  buf buffer_4 (buffer_4_out, buffer_5_out);
  buf buffer_5 (buffer_5_out, buffer_25_out);
  buf buffer_6 (buffer_6_out, buffer_3_out);
  buf buffer_7 (buffer_7_out, buffer_6_out);
  buf buffer_8 (buffer_8_out, buffer_9_out);
  buf buffer_9 (buffer_9_out, buffer_10_out);
  buf buffer_10 (buffer_10_out, buffer_33_out);
  buf buffer_11 (buffer_11_out, buffer_8_out);
  buf buffer_12 (buffer_12_out, buffer_11_out);
  buf buffer_13 (buffer_13_out, buffer_14_out);
  buf buffer_14 (buffer_14_out, buffer_15_out);
  buf buffer_15 (buffer_15_out, buffer_41_out);
  buf buffer_16 (buffer_16_out, buffer_13_out);
  buf buffer_17 (buffer_17_out, buffer_16_out);
  buf buffer_18 (buffer_18_out, buffer_19_out);
  buf buffer_19 (buffer_19_out, buffer_20_out);
  buf buffer_20 (buffer_20_out, buffer_49_out);
  buf buffer_21 (buffer_21_out, buffer_2_out);
  buf buffer_22 (buffer_22_out, buffer_21_out);
  buf buffer_23 (buffer_23_out, buffer_22_out);
  buf buffer_24 (buffer_24_out, buffer_23_out);
  buf buffer_25 (buffer_25_out, buffer_26_out);
  buf buffer_26 (buffer_26_out, buffer_27_out);
  buf buffer_27 (buffer_27_out, buffer_28_out);
  buf buffer_28 (buffer_28_out, buffer_55_out);
  buf buffer_29 (buffer_29_out, buffer_7_out);
  buf buffer_30 (buffer_30_out, buffer_29_out);
  buf buffer_31 (buffer_31_out, buffer_30_out);
  buf buffer_32 (buffer_32_out, buffer_31_out);
  buf buffer_33 (buffer_33_out, buffer_34_out);
  buf buffer_34 (buffer_34_out, buffer_35_out);
  buf buffer_35 (buffer_35_out, buffer_36_out);
  buf buffer_36 (buffer_36_out, buffer_58_out);
  buf buffer_37 (buffer_37_out, buffer_12_out);
  buf buffer_38 (buffer_38_out, buffer_37_out);
  buf buffer_39 (buffer_39_out, buffer_38_out);
  buf buffer_40 (buffer_40_out, buffer_39_out);
  buf buffer_41 (buffer_41_out, buffer_42_out);
  buf buffer_42 (buffer_42_out, buffer_43_out);
  buf buffer_43 (buffer_43_out, buffer_44_out);
  buf buffer_44 (buffer_44_out, buffer_61_out);
  buf buffer_45 (buffer_45_out, buffer_17_out);
  buf buffer_46 (buffer_46_out, buffer_45_out);
  buf buffer_47 (buffer_47_out, buffer_46_out);
  buf buffer_48 (buffer_48_out, buffer_47_out);
  buf buffer_49 (buffer_49_out, buffer_50_out);
  buf buffer_50 (buffer_50_out, buffer_51_out);
  buf buffer_51 (buffer_51_out, buffer_52_out);
  buf buffer_52 (buffer_52_out, buffer_64_out);
  and and_1 (out_2, buffer_18_out, in_1);
  buf buffer_53 (buffer_53_out, buffer_24_out);
  buf buffer_54 (buffer_54_out, buffer_53_out);
  buf buffer_55 (buffer_55_out, buffer_54_out);
  buf buffer_56 (buffer_56_out, buffer_32_out);
  buf buffer_57 (buffer_57_out, buffer_56_out);
  buf buffer_58 (buffer_58_out, buffer_57_out);
  buf buffer_59 (buffer_59_out, buffer_40_out);
  buf buffer_60 (buffer_60_out, buffer_59_out);
  buf buffer_61 (buffer_61_out, buffer_60_out);
  buf buffer_62 (buffer_62_out, buffer_48_out);
  buf buffer_63 (buffer_63_out, buffer_62_out);
  buf buffer_64 (buffer_64_out, buffer_63_out);

  // Notes on the sheet:
  //   While the falling edge is propagated ASAP
  //   Delays the rising edge from reaching the output for 48 * (buffer propagation delay),
endmodule

module not_or_hasnt (
  input  in_1,
  output out_2
);

  wire and_1_out, s_r_ff_1_q, s_r_ff_2_q;

  S_R_Flip_Flop s_r_ff_1 (.Q(s_r_ff_1_q), .reset(1'b0), .preset(in_1));  // open: S, R, clk, Qn
  and and_1 (and_1_out, s_r_ff_1_q, ~in_1);  // AND_Gate
  S_R_Flip_Flop s_r_ff_2 (.Q(s_r_ff_2_q), .reset(in_1), .preset(and_1_out));  // open: S, R, clk, Qn
  or or_1 (out_2, s_r_ff_2_q, ~s_r_ff_1_q);  // OR_Gate
endmodule

module r_ctl_2 (
  input  read_signal,
  input  [3:0] n_clock_cycles,
  input  [15:0] data_in,
  input  clock,
  input  reset,
  output [15:0] out_6
);

  wire and_1_out, and_2_out, buffer_1_out, buffer_2_out, buffer_3_out, buffer_4_out, buffer_5_out, nor_1_out,
       nor_2_out, or_1_out, or_2_out, rising_edge_delay_1_out_2, rising_edge_delay_2_out_2,
       rising_edge_delay_3_out_2;
  wire [3:0] adder_1_out, multiplexer_1_out, multiplexer_2_out, register_1_q;

  Multiplexer #(.width(4)) multiplexer_1 (
    .in0(n_clock_cycles), .in1(4'b0001), .out(multiplexer_1_out), .sel(nor_1_out));
  nor nor_1 (nor_1_out, n_clock_cycles[0], n_clock_cycles[1], n_clock_cycles[2], n_clock_cycles[3]);
  Adder #(.width(4)) adder_1 (.a(register_1_q), .b(4'b1111), .out(adder_1_out));  // open: cin, cout
  Multiplexer #(.width(4)) multiplexer_2 (
    .in0(adder_1_out), .in1(multiplexer_1_out), .out(multiplexer_2_out), .sel(read_signal));
  Register #(.width(4)) register_1 (.D(multiplexer_2_out), .en(or_1_out), .clk(clock), .Q(register_1_q), .clr(reset));
  or or_1 (or_1_out, ~nor_2_out, read_signal);  // OR_Gate
  and and_1 (and_1_out, ~read_signal, nor_2_out);  // AND_Gate
  or or_2 (or_2_out, and_1_out, reset);
  nor nor_2 (nor_2_out, register_1_q[0], register_1_q[1], register_1_q[2], register_1_q[3]);
  rising_edge_delay rising_edge_delay_1 (.in_1(or_2_out), .out_2(rising_edge_delay_1_out_2));
  rising_edge_delay rising_edge_delay_2 (.in_1(clock), .out_2(rising_edge_delay_2_out_2));
  buf buffer_1 (buffer_1_out, rising_edge_delay_1_out_2);
  buf buffer_2 (buffer_2_out, buffer_1_out);
  buf buffer_3 (buffer_3_out, buffer_2_out);
  buf buffer_4 (buffer_4_out, buffer_3_out);
  Register #(.width(16)) register_2 (
    .D(data_in), .en(read_signal), .clk(rising_edge_delay_3_out_2), .Q(out_6), .clr(and_2_out));
  rising_edge_delay rising_edge_delay_3 (.in_1(rising_edge_delay_2_out_2), .out_2(rising_edge_delay_3_out_2));
  and and_2 (and_2_out, rising_edge_delay_1_out_2, ~buffer_5_out);  // AND_Gate
  buf buffer_5 (buffer_5_out, buffer_4_out);
endmodule

module r_ctl_3 (
  input  read_signal,
  input  [3:0] n_clock_cycles,
  input  [15:0] data_in,
  input  clock,
  input  reset,
  output [15:0] out_6
);

  wire and_1_out, and_2_out, and_3_out, buffer_1_out, buffer_2_out, buffer_3_out, buffer_4_out, buffer_5_out,
       falling_edge_delay_1_out_2, nor_1_out, nor_2_out, or_1_out, or_2_out, rising_edge_delay_1_out_2,
       rising_edge_delay_2_out_2, s_r_ff_1_q;
  wire [3:0] adder_1_out, multiplexer_1_out, multiplexer_2_out, register_1_q;
  wire [15:0] and_4_out, bit_extender_1_out;

  Multiplexer #(.width(4)) multiplexer_1 (
    .in0(n_clock_cycles), .in1(4'b0010), .out(multiplexer_1_out), .sel(nor_1_out));
  nor nor_1 (nor_1_out, n_clock_cycles[0], n_clock_cycles[1], n_clock_cycles[2], n_clock_cycles[3]);
  Adder #(.width(4)) adder_1 (.a(register_1_q), .b(4'b1111), .out(adder_1_out));  // open: cin, cout
  Multiplexer #(.width(4)) multiplexer_2 (
    .in0(adder_1_out), .in1(multiplexer_1_out), .out(multiplexer_2_out), .sel(read_signal));
  Register #(.width(4)) register_1 (.D(multiplexer_2_out), .en(or_1_out), .clk(clock), .Q(register_1_q), .clr(reset));
  or or_1 (or_1_out, ~nor_2_out, read_signal);  // OR_Gate
  and and_1 (and_1_out, ~read_signal, nor_2_out);  // AND_Gate
  or or_2 (or_2_out, and_1_out, reset);
  nor nor_2 (nor_2_out, register_1_q[0], register_1_q[1], register_1_q[2], register_1_q[3]);
  rising_edge_delay rising_edge_delay_1 (.in_1(or_2_out), .out_2(rising_edge_delay_1_out_2));
  buf buffer_1 (buffer_1_out, rising_edge_delay_1_out_2);
  assign bit_extender_1_out = {{15{read_signal}}, read_signal};  // Bit_Extender bit_extender_1
  and and_2 (and_2_out, read_signal, ~clock);  // AND_Gate
  S_R_Flip_Flop s_r_ff_1 (
    .Q(s_r_ff_1_q), .reset(rising_edge_delay_1_out_2), .preset(and_2_out));  // open: S, R, clk, Qn
  buf buffer_2 (buffer_2_out, buffer_1_out);
  buf buffer_3 (buffer_3_out, buffer_2_out);
  buf buffer_4 (buffer_4_out, buffer_3_out);
  buf buffer_5 (buffer_5_out, buffer_4_out);
  rising_edge_delay rising_edge_delay_2 (.in_1(clock), .out_2(rising_edge_delay_2_out_2));
  and and_3 (and_3_out, rising_edge_delay_1_out_2, ~buffer_5_out);  // AND_Gate
  Register #(.width(16)) register_2 (
    .D(data_in), .en(read_signal), .clk(rising_edge_delay_2_out_2), .Q(out_6), .clr(and_3_out));
  falling_edge_delay falling_edge_delay_1 (.in_1(s_r_ff_1_q), .out_2(falling_edge_delay_1_out_2));
  assign and_4_out = data_in & bit_extender_1_out;  // AND_Gate and_4, 16 bits wide
  Multiplexer #(.width(16)) multiplexer_3 (.in0(and_4_out), .sel(falling_edge_delay_1_out_2));  // open: in1, out
endmodule

module double_click (
  input  in_1,
  output out_2
);

  wire and_1_out, and_2_out, buffer_1_out, buffer_2_out, buffer_3_out, buffer_4_out, buffer_5_out,
       buffer_6_out, buffer_7_out, buffer_8_out, buffer_9_out, buffer_10_out, buffer_11_out, buffer_12_out,
       buffer_13_out, buffer_14_out, buffer_15_out, buffer_16_out, buffer_17_out, buffer_18_out,
       buffer_19_out, buffer_20_out, buffer_21_out, buffer_22_out, buffer_23_out, buffer_24_out,
       buffer_25_out, buffer_26_out, buffer_27_out, buffer_28_out, buffer_29_out, buffer_30_out,
       buffer_31_out, buffer_32_out, buffer_33_out, buffer_34_out, buffer_35_out, buffer_36_out;

  buf buffer_1 (buffer_1_out, in_1);
  buf buffer_2 (buffer_2_out, buffer_1_out);
  buf buffer_3 (buffer_3_out, buffer_2_out);
  buf buffer_4 (buffer_4_out, buffer_5_out);
  buf buffer_5 (buffer_5_out, buffer_6_out);
  buf buffer_6 (buffer_6_out, buffer_24_out);
  buf buffer_7 (buffer_7_out, buffer_4_out);
  buf buffer_8 (buffer_8_out, buffer_7_out);
  buf buffer_9 (buffer_9_out, buffer_8_out);
  buf buffer_10 (buffer_10_out, buffer_9_out);
  buf buffer_11 (buffer_11_out, buffer_12_out);
  buf buffer_12 (buffer_12_out, buffer_13_out);
  buf buffer_13 (buffer_13_out, buffer_29_out);
  buf buffer_14 (buffer_14_out, buffer_11_out);
  buf buffer_15 (buffer_15_out, buffer_14_out);
  buf buffer_16 (buffer_16_out, buffer_15_out);
  buf buffer_17 (buffer_17_out, buffer_16_out);
  buf buffer_18 (buffer_18_out, buffer_33_out);
  buf buffer_19 (buffer_19_out, buffer_18_out);
  buf buffer_20 (buffer_20_out, buffer_19_out);
  buf buffer_21 (buffer_21_out, buffer_3_out);
  buf buffer_22 (buffer_22_out, buffer_21_out);
  buf buffer_23 (buffer_23_out, buffer_22_out);
  buf buffer_24 (buffer_24_out, buffer_25_out);
  buf buffer_25 (buffer_25_out, buffer_23_out);
  buf buffer_26 (buffer_26_out, buffer_10_out);
  buf buffer_27 (buffer_27_out, buffer_26_out);
  buf buffer_28 (buffer_28_out, buffer_27_out);
  buf buffer_29 (buffer_29_out, buffer_30_out);
  buf buffer_30 (buffer_30_out, buffer_28_out);
  buf buffer_31 (buffer_31_out, buffer_17_out);
  buf buffer_32 (buffer_32_out, buffer_31_out);
  buf buffer_33 (buffer_33_out, buffer_32_out);
  buf buffer_34 (buffer_34_out, buffer_20_out);
  buf buffer_35 (buffer_35_out, buffer_34_out);
  buf buffer_36 (buffer_36_out, buffer_35_out);
  and and_1 (and_1_out, in_1, ~buffer_23_out);  // AND_Gate
  and and_2 (and_2_out, buffer_33_out, ~buffer_36_out);  // AND_Gate
  or or_1 (out_2, and_1_out, and_2_out);
endmodule

module data_bus_controller (
  input  [15:0] control_bus_1,
  input  [15:0] control_bus_2,
  input  [15:0] addr_bus_in,
  input  [15:0] control_unit_in,
  input  [15:0] registers_in,
  input  [15:0] special_registers_in,
  input  clock,
  input  [15:0] ALU_in,
  input  reset,
  input  [15:0] memory_in,
  input  [15:0] io_in,
  output [15:0] data_bus_out
);

  wire comparator_1_eq, comparator_2_eq, comparator_3_eq, eight_bit_eq_cmp_1_out_3, eight_bit_eq_cmp_2_out_3,
       eight_bit_eq_cmp_3_out_3, eight_bit_eq_cmp_4_out_3, or_1_out, or_3_out, or_4_out;
  wire [7:0] eight_bit_gate_1_data_out, eight_bit_gate_2_data_out, multiplexer_1_out, multiplexer_2_out,
       multiplexer_3_out, or_2_out, register_1_q, subtractor_1_out;
  wire [15:0] multiplexer_4_out, or_5_out;

  eight_bit_eq_cmp eight_bit_eq_cmp_1 (.in_1(control_bus_1[7:0]), .in_2(8'h50), .out_3(eight_bit_eq_cmp_1_out_3));
  Comparator comparator_1 (.a(control_bus_1[15:8]), .b({8{1'b0}}), .eq(comparator_1_eq));  // open: gt, lt
  Multiplexer #(.width(8)) multiplexer_1 (
    .in0(control_bus_1[15:8]), .in1(8'h1), .out(multiplexer_1_out), .sel(comparator_1_eq));
  eight_bit_eq_cmp eight_bit_eq_cmp_2 (.in_1(control_bus_1[7:0]), .in_2(8'h52), .out_3(eight_bit_eq_cmp_2_out_3));
  eight_bit_eq_cmp eight_bit_eq_cmp_3 (.in_1(control_bus_2[7:0]), .in_2(8'h50), .out_3(eight_bit_eq_cmp_3_out_3));
  Comparator comparator_2 (.a(control_bus_2[15:8]), .b({8{1'b0}}), .eq(comparator_2_eq));  // open: gt, lt
  Multiplexer #(.width(8)) multiplexer_2 (
    .in0(control_bus_2[15:8]), .in1(8'h1), .out(multiplexer_2_out), .sel(comparator_2_eq));
  eight_bit_eq_cmp eight_bit_eq_cmp_4 (.in_1(control_bus_2[7:0]), .in_2(8'h52), .out_3(eight_bit_eq_cmp_4_out_3));
  or or_1 (or_1_out, eight_bit_eq_cmp_1_out_3, eight_bit_eq_cmp_3_out_3);
  eight_bit_gate eight_bit_gate_1 (
    .data_in(multiplexer_1_out), .enable(eight_bit_eq_cmp_1_out_3), .data_out(eight_bit_gate_1_data_out));
  assign or_2_out = eight_bit_gate_1_data_out | eight_bit_gate_2_data_out;  // OR_Gate or_2, 8 bits wide
  eight_bit_gate eight_bit_gate_2 (
    .data_in(multiplexer_2_out), .enable(eight_bit_eq_cmp_3_out_3), .data_out(eight_bit_gate_2_data_out));
  Multiplexer #(.width(8)) multiplexer_3 (
    .in0(subtractor_1_out), .in1(or_2_out), .out(multiplexer_3_out), .sel(or_1_out));
  or or_3 (or_3_out, or_1_out, ~comparator_3_eq);  // OR_Gate
  or or_4 (or_4_out, eight_bit_eq_cmp_2_out_3, eight_bit_eq_cmp_4_out_3);
  Register #(.trigger("falling")) register_1 (
    .D(multiplexer_3_out), .en(or_3_out), .clk(clock), .Q(register_1_q), .clr(reset));
  assign or_5_out = control_unit_in | registers_in | special_registers_in | ALU_in | memory_in | io_in;  // OR_Gate or_5, 16 bits wide
  Subtractor subtractor_1 (.a(register_1_q), .b(8'h1), .out(subtractor_1_out));  // open: bin, bout
  Comparator comparator_3 (.a(register_1_q), .b({8{1'b0}}), .eq(comparator_3_eq));  // open: gt, lt
  Register #(.width(16)) register_2 (
    .D(multiplexer_4_out), .en(comparator_3_eq), .clk(clock), .Q(data_bus_out), .clr(reset));
  Multiplexer #(.width(16)) multiplexer_4 (.in0(or_5_out), .in1(addr_bus_in), .out(multiplexer_4_out), .sel(or_4_out));
endmodule

module addr_bus_controller (
  input  [15:0] control_bus_1,
  input  [15:0] control_bus_2,
  input  [15:0] data_bus_in,
  input  [15:0] control_unit_in,
  input  [15:0] registers_in,
  input  [15:0] special_registers_in,
  input  clock,
  input  reset,
  output [15:0] addr_bus_out
);

  wire comparator_1_eq, comparator_2_eq, comparator_3_eq, eight_bit_eq_cmp_1_out_3, eight_bit_eq_cmp_2_out_3,
       eight_bit_eq_cmp_3_out_3, eight_bit_eq_cmp_4_out_3, or_1_out, or_3_out, or_4_out;
  wire [7:0] eight_bit_gate_1_data_out, eight_bit_gate_2_data_out, multiplexer_1_out, multiplexer_2_out,
       multiplexer_3_out, or_2_out, register_1_q, subtractor_1_out;
  wire [15:0] multiplexer_4_out, or_5_out;

  eight_bit_eq_cmp eight_bit_eq_cmp_1 (.in_1(control_bus_1[7:0]), .in_2(8'h51), .out_3(eight_bit_eq_cmp_1_out_3));
  Comparator comparator_1 (.a(control_bus_1[15:8]), .b({8{1'b0}}), .eq(comparator_1_eq));  // open: gt, lt
  Multiplexer #(.width(8)) multiplexer_1 (
    .in0(control_bus_1[15:8]), .in1(8'h1), .out(multiplexer_1_out), .sel(comparator_1_eq));
  eight_bit_eq_cmp eight_bit_eq_cmp_2 (.in_1(control_bus_1[7:0]), .in_2(8'h53), .out_3(eight_bit_eq_cmp_2_out_3));
  eight_bit_eq_cmp eight_bit_eq_cmp_3 (.in_1(control_bus_2[7:0]), .in_2(8'h51), .out_3(eight_bit_eq_cmp_3_out_3));
  Comparator comparator_2 (.a(control_bus_2[15:8]), .b({8{1'b0}}), .eq(comparator_2_eq));  // open: gt, lt
  Multiplexer #(.width(8)) multiplexer_2 (
    .in0(control_bus_2[15:8]), .in1(8'h1), .out(multiplexer_2_out), .sel(comparator_2_eq));
  eight_bit_eq_cmp eight_bit_eq_cmp_4 (.in_1(control_bus_2[7:0]), .in_2(8'h53), .out_3(eight_bit_eq_cmp_4_out_3));
  or or_1 (or_1_out, eight_bit_eq_cmp_1_out_3, eight_bit_eq_cmp_3_out_3);
  eight_bit_gate eight_bit_gate_1 (
    .data_in(multiplexer_1_out), .enable(eight_bit_eq_cmp_1_out_3), .data_out(eight_bit_gate_1_data_out));
  assign or_2_out = eight_bit_gate_1_data_out | eight_bit_gate_2_data_out;  // OR_Gate or_2, 8 bits wide
  eight_bit_gate eight_bit_gate_2 (
    .data_in(multiplexer_2_out), .enable(eight_bit_eq_cmp_3_out_3), .data_out(eight_bit_gate_2_data_out));
  Multiplexer #(.width(8)) multiplexer_3 (
    .in0(subtractor_1_out), .in1(or_2_out), .out(multiplexer_3_out), .sel(or_1_out));
  or or_3 (or_3_out, or_1_out, ~comparator_3_eq);  // OR_Gate
  or or_4 (or_4_out, eight_bit_eq_cmp_2_out_3, eight_bit_eq_cmp_4_out_3);
  Register register_1 (.D(multiplexer_3_out), .en(or_3_out), .clk(clock), .Q(register_1_q), .clr(reset));
  assign or_5_out = control_unit_in | registers_in | special_registers_in;  // OR_Gate or_5, 16 bits wide
  Subtractor subtractor_1 (.a(register_1_q), .b(8'h1), .out(subtractor_1_out));  // open: bin, bout
  Comparator comparator_3 (.a(register_1_q), .b({8{1'b0}}), .eq(comparator_3_eq));  // open: gt, lt
  Register #(.trigger("falling"), .width(16)) register_2 (
    .D(multiplexer_4_out), .en(comparator_3_eq), .clk(clock), .Q(addr_bus_out), .clr(reset));
  Multiplexer #(.width(16)) multiplexer_4 (.in0(or_5_out), .in1(data_bus_in), .out(multiplexer_4_out), .sel(or_4_out));
endmodule

module control_bus_controller (
  input  [15:0] control_1,
  input  [15:0] control_2,
  input  clock,
  input  reset,
  output [15:0] control_bus_1,
  output [15:0] control_bus_2
);

  Register #(.width(16)) register_1 (.D(control_1), .clk(clock), .Q(control_bus_1), .clr(reset));  // open: en
  Register #(.width(16)) register_2 (.D(control_2), .clk(clock), .Q(control_bus_2), .clr(reset));  // open: en
endmodule

module eight_bit_gate (
  input  enable,
  input  [7:0] data_in,
  output [7:0] data_out
);

  assign data_out = {8{enable}} & data_in;  // AND_Gate and_1, 8 bits wide
endmodule
